// Digital circuit GAL2.dig as structural Verilog
module GAL2 (
  input  Ain,
  input  Bin,
  input  Cin,
  input  SETC,
  input  LD,
  input  IR6,
  input  IR5,
  input  IR4,
  input  T8,
  input  VCC,
  input  GND,
  output Cout,
  output CLC,
  output CtoFF,
  output Fout,
  output CLR,
  output nWR,
  output nRD,
  output INC_LD
);

  wire nand_1_out, nand_2_out, nand_4_out, nand_5_out, nand_6_out, nand_7_out, nand_9_out, nand_11_out,
       nand_12_out, nand_13_out, nand_14_out, nand_15_out, nand_16_out, nand_18_out, nand_19_out,
       nand_20_out, nand_21_out, nand_22_out, nand_23_out, nand_24_out, nand_25_out, nand_26_out, not_1_out,
       not_2_out, not_3_out, not_4_out, not_5_out, not_6_out;

  not not_1 (not_1_out, IR4);
  not not_2 (not_2_out, IR5);
  not not_3 (not_3_out, IR6);
  not not_4 (not_4_out, Cin);
  not not_5 (not_5_out, Bin);
  not not_6 (not_6_out, Ain);
  nand nand_1 (nand_1_out, Ain, not_5_out, IR4, not_2_out, IR6);
  nand nand_2 (nand_2_out, Ain, Cin, not_1_out, not_2_out);
  PowerSupply powersupply_1 (.VDD(VCC), .GND(GND));
  nand nand_3 (Cout, nand_1_out, nand_2_out, nand_4_out, nand_5_out, nand_6_out, nand_7_out);
  nand nand_4 (nand_4_out, Ain, Bin, not_1_out, not_2_out);
  nand nand_5 (nand_5_out, Ain, Cin, not_2_out, IR6);
  nand nand_6 (nand_6_out, not_5_out, Cin, IR4, not_2_out, IR6);
  nand nand_7 (nand_7_out, Bin, Cin, not_1_out, not_2_out);
  nand nand_8 (CLC, nand_9_out, LD);
  nand nand_9 (nand_9_out, IR4, not_2_out, IR6);
  nand nand_10 (CtoFF, IR4, not_2_out, IR6, SETC);
  nand nand_11 (nand_11_out, not_6_out, not_5_out, not_4_out, IR4, not_2_out, IR6);
  nand nand_12 (nand_12_out, not_6_out, Bin, Cin, IR4, not_2_out);
  nand nand_13 (nand_13_out, Ain, not_5_out, Cin, IR4, not_2_out);
  nand nand_14 (nand_14_out, Ain, Bin, not_4_out, IR4, not_2_out);
  nand nand_15 (nand_15_out, not_6_out, not_5_out, Cin, not_1_out);
  nand nand_16 (nand_16_out, not_6_out, Bin, not_4_out, not_1_out);
  nand nand_17 (Fout, nand_11_out, nand_12_out, nand_13_out, nand_14_out, nand_15_out, nand_16_out, nand_18_out, nand_19_out, nand_20_out, nand_21_out, nand_22_out, nand_23_out, nand_24_out, nand_25_out, nand_26_out);
  nand nand_18 (nand_18_out, Ain, not_5_out, not_4_out, not_1_out);
  nand nand_19 (nand_19_out, Ain, Bin, Cin, not_1_out);
  nand nand_20 (nand_20_out, not_6_out, not_5_out, Cin, IR5);
  nand nand_21 (nand_21_out, not_6_out, Bin, not_4_out, IR5);
  nand nand_22 (nand_22_out, Ain, not_5_out, not_4_out, IR5);
  nand nand_23 (nand_23_out, Ain, Bin, Cin, IR5);
  nand nand_24 (nand_24_out, Bin, Cin, IR4, not_2_out, not_3_out);
  nand nand_25 (nand_25_out, Bin, not_1_out, IR5, not_3_out);
  nand nand_26 (nand_26_out, Cin, not_1_out, IR5, not_3_out);
  nand nand_27 (CLR, not_1_out, not_2_out, not_3_out, LD);
  nand nand_28 (nWR, not_1_out, IR5, IR6, T8);
  nand nand_29 (nRD, not_1_out, not_2_out, not_3_out);
  nand nand_30 (INC_LD, IR4, IR5, IR6, T8);

  // Notes on the sheet:
  //   Cout: pin 12
  //   CLC: pin 13
  //   CtoFF: pin 14
  //   Fout: pin 15
  //   CLR: pin 16
  //   nWR: pin 17
  //   nRD: pin 18
  //   INC_LD: pin 19
  //   Ain: pin 9
  //   Bin: pin 8
  //   Cin: pin 7
  //   SETC: pin 6
  //   LD: pin 5
  //   IR6: pin 4
  //   IR5: pin 3
  //   IR4: pin 2
  //   T8: pin 1
  //   VCC: pin 20, default 1
  //   GND: pin 10
endmodule
