// Digital circuit MITE-10.dig as structural Verilog
module MITE_10 (
  input  in_1,
  input  in_2,
  input  in_3,
  input  clk,
  output T0,
  output T8,
  output LD,
  output GCLK,
  output SETC,
  output GATE
);

  wire A0, A1, A2, A3, A4, A5, A6, A7, A8, ADD, AND, Aout, Bout, BUS0, BUS1, BUS2, BUS3, BUS4, BUS5, BUS6,
       BUS7, C, Cin, CLA, CLR, Cout, D0, D1, D2, D3, D4, D5, D6, D7, diodebackward_1_out,
       diodebackward_2_out, diodebackward_8_out, diodebackward_9_out, diodeforward_1_out, F, Fout, I0, I1,
       IR0, IR1, IR2, IR3, IR4, IR5, IR6, IR7, LD_t, LOAD, nA, nand_1_out, nand_2_out, nand_3_out,
       nand_5_out, nand_6_out, nand_7_out, nand_8_out, nand_9_out, nand_10_out, nB, nCLRAC, nCTRLD, nJMP,
       nor_1_out, nor_2_out, nor_4_out, not_5_out, not_6_out, not_7_out, not_8_out, not_9_out, not_10_out,
       not_11_out, not_12_out, OR, pullup_2_out, pullup_4_out, pullup_7_out, RCO, ST, SUB, T2, T3, T4, T5,
       T6, T7, T8_t, T9, XOR, xor_1_out, xor_2_out, xor_3_out, xor_4_out, ZERO;
  wire [3:0] U6_pin6;
  wire [3:1] U6_pin12;

  // _62256 U17: pin names not known; wires that end beside it: A8, A8, A7, A6, A5, A4, A3, A2, A1, A0, BUS0, BUS1, BUS2, 1'b0, 1'b1, in_2, A8, A8, A8, A8, in_3, A8, 1'b0, BUS7
  _74161 U8 (
    .pin1(nCLRAC), .pin2(T8), .pin3(BUS0), .pin4(BUS1), .pin5(BUS2), .pin6(BUS3), .pin7(1'b1), .pin8(1'b0),
    .pin9(nCTRLD), .pin10(1'b1), .pin11(A3), .pin12(A2), .pin13(A1), .pin14(A0), .pin15(RCO), .pin16(1'b1));
  _74161 U9 (
    .pin1(nCLRAC), .pin2(T8), .pin3(BUS4), .pin4(BUS5), .pin5(BUS6), .pin6(BUS7), .pin7(1'b1), .pin8(1'b0),
    .pin9(nCTRLD), .pin10(RCO), .pin11(A7), .pin12(A6), .pin13(A5), .pin14(A4), .pin16(1'b1));  // open: pin15
  Reset reset_1 (.out(nCLRAC));
  // _27C1024 U7: pin names not known; wires that end beside it: A8, A8, A8, A8, A8, A8, A8, 1'b1, D3, D4, D5, D6, D7, 1'b0, IR0, IR1, IR2, IR3, IR4, IR5, IR6, IR7, 1'b0, 1'b1
  _74541 U10 (
    .pin1(in_1), .pin2(D0), .pin3(D1), .pin4(D2), .pin5(D3), .pin6(D4), .pin7(D5), .pin8(D6), .pin9(D7),
    .pin10(1'b0), .pin11(BUS7), .pin12(BUS6), .pin13(BUS5), .pin14(BUS4), .pin15(BUS3), .pin16(BUS2),
    .pin17(BUS1), .pin18(BUS0), .pin19(in_1), .pin20(1'b1));
  PullDown pulldown_1 (.out(A8));
  Seven_Seg_Hex seven_seg_hex_1 (.d({4{A8}}), .dp(1'b0));
  Seven_Seg_Hex seven_seg_hex_2 (.d({4{A8}}), .dp(1'b0));
  Seven_Seg_Hex seven_seg_hex_3 (.d({A7, A6, A5, A4}), .dp(1'b0));
  Seven_Seg_Hex seven_seg_hex_4 (.d({A3, A2, A1, A0}), .dp(1'b0));
  Seven_Seg_Hex seven_seg_hex_5 (.d({D7, D6, D5, D4}), .dp(1'b0));
  nor nor_1 (nor_1_out, GATE, clk);
  nor nor_2 (nor_2_out, T8, nJMP);
  Seven_Seg_Hex seven_seg_hex_6 (.d({D3, D2, D1, D0}), .dp(1'b0));
  _744017 U16 (
    .pin1(T5), .pin2(SETC), .pin3(LD_t), .pin4(T2), .pin5(T6), .pin6(T7), .pin7(T3), .pin8(1'b0),
    .pin9(T8_t), .pin10(T4), .pin11(T9), .pin13(1'b0), .pin14(clk), .pin15(1'b0), .pin16(1'b1));  // open: pin12
  not not_1 (nCTRLD, nor_2_out);
  Seven_Seg_Hex seven_seg_hex_7 (.d({IR7, IR6, IR5, IR4}), .dp(1'b0));
  not not_2 (GCLK, nor_1_out);
  Seven_Seg_Hex seven_seg_hex_8 (.d({IR3, IR2, IR1, IR0}), .dp(1'b0));
  not not_3 (LD, LD_t);
  not not_4 (T8, T8_t);
  not not_5 (not_5_out, LOAD);
  not not_6 (not_6_out, AND);
  not not_7 (not_7_out, OR);
  not not_8 (not_8_out, XOR);
  not not_9 (not_9_out, ADD);
  not not_10 (not_10_out, SUB);
  not not_11 (not_11_out, ST);
  not not_12 (not_12_out, nJMP);
  nor nor_3 (GATE, SETC, nor_4_out);
  nor nor_4 (nor_4_out, GATE, T9);
  LED led_1 (.in(not_5_out));
  LED led_2 (.in(not_6_out));
  LED led_3 (.in(not_7_out));
  LED led_4 (.in(not_8_out));
  LED led_5 (.in(not_9_out));
  LED led_6 (.in(not_10_out));
  LED led_7 (.in(not_11_out));
  LED led_8 (.in(not_12_out));
  _74138 U1 (
    .pin1(IR4), .pin2(IR5), .pin3(IR6), .pin4(1'b0), .pin5(1'b0), .pin6(1'b1), .pin7(nJMP), .pin8(1'b0),
    .pin9(ST), .pin10(SUB), .pin11(ADD), .pin12(XOR), .pin13(OR), .pin14(AND), .pin15(LOAD), .pin16(1'b1));
  DiodeBackward diodebackward_1 (.in(LOAD), .out(diodebackward_1_out));
  PullUp pullup_1 (.out(diodebackward_1_out));
  DiodeBackward diodebackward_2 (.in(LOAD), .out(diodebackward_2_out));
  DiodeBackward diodebackward_3 (.in(ADD), .out(diodebackward_2_out));
  DiodeBackward diodebackward_4 (.in(SUB), .out(diodebackward_2_out));
  DiodeBackward diodebackward_5 (.in(nJMP), .out(diodebackward_2_out));
  PullUp pullup_2 (.out(pullup_2_out));
  PullUp pullup_3 (.out(diodebackward_2_out));
  DiodeBackward diodebackward_6 (.in(SUB), .out(pullup_2_out));
  PullUp pullup_4 (.out(pullup_4_out));
  DiodeBackward diodebackward_7 (.in(SUB), .out(pullup_4_out));
  DiodeBackward diodebackward_8 (.in(nJMP), .out(diodebackward_8_out));
  PullUp pullup_5 (.out(diodebackward_8_out));
  DiodeBackward diodebackward_9 (.in(AND), .out(diodebackward_9_out));
  DiodeBackward diodebackward_10 (.in(OR), .out(diodebackward_9_out));
  PullUp pullup_6 (.out(diodebackward_9_out));
  PullUp pullup_7 (.out(pullup_7_out));
  DiodeBackward diodebackward_11 (.in(LOAD), .out(pullup_7_out));
  DiodeBackward diodebackward_12 (.in(OR), .out(pullup_7_out));
  DiodeBackward diodebackward_13 (.in(XOR), .out(pullup_7_out));
  DiodeBackward diodebackward_14 (.in(ADD), .out(pullup_7_out));
  DiodeBackward diodebackward_15 (.in(SUB), .out(pullup_7_out));
  DiodeBackward diodebackward_16 (.in(ST), .out(pullup_7_out));
  DiodeBackward diodebackward_17 (.in(nJMP), .out(pullup_7_out));
  _74540 U2 (
    .pin1(1'b0), .pin2(pullup_7_out), .pin3(diodebackward_9_out), .pin4(diodebackward_8_out),
    .pin5(pullup_4_out), .pin6(pullup_2_out), .pin7(diodebackward_2_out), .pin8(diodebackward_1_out),
    .pin9(1'b0), .pin10(1'b0), .pin12(CLA), .pin13(F), .pin14(C), .pin15(nB), .pin16(nA), .pin17(I1),
    .pin18(I0), .pin19(1'b0), .pin20(1'b1));  // open: pin11
  xor xor_1 (xor_1_out, Aout, nA);
  xor xor_2 (xor_2_out, nB, Bout);
  nand nand_1 (nand_1_out, SETC, C);
  nand nand_2 (nand_2_out, C, C);
  _74595 U4 (
    .pin1(BUS6), .pin2(BUS5), .pin3(BUS4), .pin4(BUS3), .pin5(BUS2), .pin6(BUS1), .pin7(BUS0), .pin8(1'b0),
    .pin10(nCLRAC), .pin11(GCLK), .pin12(T8), .pin13(1'b0), .pin14(Fout), .pin15(BUS7), .pin16(1'b1));  // open: pin9
  nand nand_3 (nand_3_out, nand_2_out, LD_t);
  nand nand_4 (CLR, CLA, LD_t);
  xor xor_3 (xor_3_out, xor_1_out, xor_2_out);
  xor xor_4 (xor_4_out, xor_3_out, Cin);
  nand nand_5 (nand_5_out, xor_3_out, Cin);
  nand nand_6 (nand_6_out, xor_1_out, xor_2_out);
  DiodeForward diodeforward_1 (.in(BUS7), .out(diodeforward_1_out));
  DiodeForward diodeforward_2 (.in(BUS6), .out(diodeforward_1_out));
  DiodeForward diodeforward_3 (.in(BUS5), .out(diodeforward_1_out));
  DiodeForward diodeforward_4 (.in(BUS4), .out(diodeforward_1_out));
  DiodeForward diodeforward_5 (.in(BUS3), .out(diodeforward_1_out));
  DiodeForward diodeforward_6 (.in(BUS2), .out(diodeforward_1_out));
  DiodeForward diodeforward_7 (.in(BUS1), .out(diodeforward_1_out));
  DiodeForward diodeforward_8 (.in(BUS0), .out(diodeforward_1_out));
  nand nand_7 (nand_7_out, nand_5_out, nand_6_out);
  PullDown pulldown_2 (.out(diodeforward_1_out));
  Seven_Seg_Hex seven_seg_hex_9 (.d({BUS7, BUS6, BUS5, BUS4}), .dp(1'b0));
  not not_13 (ZERO, diodeforward_1_out);
  nand nand_8 (nand_8_out, xor_4_out, I0);
  nand nand_9 (nand_9_out, I1, nand_7_out);
  nand nand_10 (nand_10_out, nand_7_out, F);
  Seven_Seg_Hex seven_seg_hex_10 (.d({BUS3, BUS2, BUS1, BUS0}), .dp(1'b0));
  LED led_9 (.in(ZERO));
  nand nand_11 (Fout, nand_8_out, nand_9_out);
  nand nand_12 (Cout, nand_10_out, nand_10_out);
  _7474 U12 (
    .pin1(nand_3_out), .pin2(Cout), .pin3(GCLK), .pin4(nand_1_out), .pin5(Cin), .pin7(1'b0), .pin10(1'b1),
    .pin11(1'b1), .pin12(1'b1), .pin13(1'b1), .pin14(1'b1));  // open: pin6, pin8, pin9
  _74165 U3 (
    .pin1(LD), .pin2(GCLK), .pin3(D3), .pin4(D2), .pin5(D1), .pin6(D0), .pin8(1'b0), .pin9(Bout),
    .pin10(1'b0), .pin11(D7), .pin12(D6), .pin13(D5), .pin14(D4), .pin15(1'b0), .pin16(1'b1));  // open: pin7
  LED led_10 (.in(Cin));
  Seven_Seg_Hex seven_seg_hex_11 (.d(U6_pin6), .dp(1'b0));
  Seven_Seg_Hex seven_seg_hex_12 (.d({U6_pin12, Aout}), .dp(1'b0));
  _74164 U6 (
    .pin1(1'b1), .pin2(Fout), .pin3(U6_pin6[3]), .pin4(U6_pin6[2]), .pin5(U6_pin6[1]), .pin6(U6_pin6[0]),
    .pin7(1'b0), .pin8(GCLK), .pin9(CLR), .pin10(U6_pin12[3]), .pin11(U6_pin12[2]), .pin12(U6_pin12[1]),
    .pin13(Aout), .pin14(1'b1));

  assign T0 = LD;

  // Other names for the same wires on the sheet: A9 = A8; A10 = A8; A11 = A8; A12 = A8; A13 = A8; A14 = A8; A15 = A8;
  //   C_RAM = in_2; nDE = in_1; nLOAD = LD; nRESET = nCLRAC; R0 = D0; R1 = D1; R2 = D2; R3 = D3; R4 = D4; R5 = D5;
  //   R6 = D6; R7 = D7; R8 = IR0; R9 = IR1; R10 = IR2; R11 = IR3; R12 = IR4; R13 = IR5; R14 = IR6; R15 = IR7;
  //   PC_INC = T8; RCLK = T8; RDRAM = in_3; T0_t = LD_t; T1 = SETC

  // Notes on the sheet:
  //   in_1: default 1
  //   in_2: default 1
  //   in_3: default 1
  //   clk: Hz: 8
  //   ROM & PC
  //   Low Address Counter
  //   RAM
  //   ADDRESS
  //   DATA
  //   INSTRUCTION
  //   LOAD
  //   AND
  //   OR
  //   XOR
  //   ADD
  //   SUB
  //   STORE
  //   JMP
  //   MITE-8
  //   Instruction Input
  //   CLA
  //   C
  //   F
  //   ~B
  //   ~A
  //   I0
  //   I1
  //   ALU
  //   Carry is only set before Bit 0 of an operation
  //   Any residual carry is cleared before an operation
  //   ACCUMULATOR
  //   Suppress Carry
  //   ZERO
  //   8-bit Shift Register B
  //   Carry FF
  //   CARRY
  //   MITE 8-bit  Bit serial CPU Testbed
  //   Shift Register A
endmodule
