// Digital circuit MITE_15.dig as structural Verilog
module MITE_15 (
  input  in_1,
  input  clk,
  output T0,
  output T8,
  output LD,
  output GCLK,
  output SETC,
  output GATE
);

  wire A0, A1, A2, A3, A4, A5, A6, A7, A8, Aout, Bout, BUS0, BUS1, BUS2, BUS3, BUS4, BUS5, BUS6, BUS7, Cin,
       CLR, Cout, D0, D1, D2, D3, D4, D5, D6, D7, diodeforward_1_out, Fout, IR0, IR1, IR2, IR3, IR4, IR5,
       IR6, IR7, LD_INC, LD_t, MA0, MA1, MA2, MA3, MA4, MA5, MA6, MA7, MA8, MA9, MA10, MA11, MA12, MA13,
       MA14, MA15, nCLRAC, nor_3_out, not_3_out, not_4_out, nRD, nWR, RCLK, RCO, ResC, SetC_t, T2, T3, T4,
       T5, T6, T7, T8_t, T9, U4_pin9, U5_pin9, U10_p21, ZERO;
  wire [3:0] U1_pin3;
  wire [3:1] U1_pin10;

  // _62256 U10: pin names not known; wires that end beside it: MA14, MA12, MA7, MA6, MA5, MA4, MA3, MA2, MA1, MA0, BUS0, BUS1, BUS2, 1'b0, 1'b1, nWR, MA13, MA8, MA9, MA11, U10_p21, MA10, 1'b0, BUS7
  _74161 U8 (
    .pin1(nCLRAC), .pin2(T8), .pin3(BUS0), .pin4(BUS1), .pin5(BUS2), .pin6(BUS3), .pin7(1'b1), .pin8(1'b0),
    .pin9(LD_INC), .pin10(1'b1), .pin11(A3), .pin12(A2), .pin13(A1), .pin14(A0), .pin15(RCO), .pin16(1'b1));
  _74161 U9 (
    .pin1(nCLRAC), .pin2(T8), .pin3(BUS4), .pin4(BUS5), .pin5(BUS6), .pin6(BUS7), .pin7(1'b1), .pin8(1'b0),
    .pin9(LD_INC), .pin10(RCO), .pin11(A7), .pin12(A6), .pin13(A5), .pin14(A4), .pin16(1'b1));  // open: pin15
  not not_1 (U10_p21, nRD);
  _74595 U4 (
    .pin1(BUS6), .pin2(BUS5), .pin3(BUS4), .pin4(BUS3), .pin5(BUS2), .pin6(BUS1), .pin7(BUS0), .pin8(1'b0),
    .pin9(U4_pin9), .pin10(nCLRAC), .pin11(GCLK), .pin12(RCLK), .pin13(nWR), .pin14(Fout), .pin15(BUS7),
    .pin16(1'b1));
  // _27C1024 U7: pin names not known; wires that end beside it: A8, A8, A8, A8, A8, A8, A8, 1'b1, D3, D4, D5, D6, D7, 1'b0, IR0, IR1, IR2, IR3, IR4, IR5, IR6, IR7, 1'b0, 1'b1
  DiodeForward diodeforward_1 (.in(BUS7), .out(diodeforward_1_out));
  DiodeForward diodeforward_2 (.in(BUS6), .out(diodeforward_1_out));
  DiodeForward diodeforward_3 (.in(BUS5), .out(diodeforward_1_out));
  DiodeForward diodeforward_4 (.in(BUS4), .out(diodeforward_1_out));
  DiodeForward diodeforward_5 (.in(BUS3), .out(diodeforward_1_out));
  DiodeForward diodeforward_6 (.in(BUS2), .out(diodeforward_1_out));
  DiodeForward diodeforward_7 (.in(BUS1), .out(diodeforward_1_out));
  DiodeForward diodeforward_8 (.in(BUS0), .out(diodeforward_1_out));
  PullDown pulldown_1 (.out(A8));
  Seven_Seg_Hex seven_seg_hex_1 (.d({BUS7, BUS6, BUS5, BUS4}), .dp(1'b0));
  not not_2 (ZERO, diodeforward_1_out);
  PullDown pulldown_2 (.out(diodeforward_1_out));
  Seven_Seg_Hex seven_seg_hex_2 (.d({BUS3, BUS2, BUS1, BUS0}), .dp(1'b0));
  LED led_1 (.in(ZERO));
  _74595 U5 (
    .pin1(MA14), .pin2(MA13), .pin3(MA12), .pin4(MA11), .pin5(MA10), .pin6(MA9), .pin7(MA8), .pin8(1'b0),
    .pin9(U5_pin9), .pin10(nCLRAC), .pin11(GCLK), .pin12(RCLK), .pin13(1'b0), .pin14(U4_pin9), .pin15(MA15),
    .pin16(1'b1));
  _74541 U13 (
    .pin1(in_1), .pin2(D0), .pin3(D1), .pin4(D2), .pin5(D3), .pin6(D4), .pin7(D5), .pin8(D6), .pin9(D7),
    .pin10(1'b0), .pin11(BUS7), .pin12(BUS6), .pin13(BUS5), .pin14(BUS4), .pin15(BUS3), .pin16(BUS2),
    .pin17(BUS1), .pin18(BUS0), .pin19(in_1), .pin20(1'b1));
  Seven_Seg_Hex seven_seg_hex_3 (.d({MA15, MA14, MA13, MA12}), .dp(1'b0));
  Seven_Seg_Hex seven_seg_hex_4 (.d({MA11, MA10, MA9, MA8}), .dp(1'b0));
  Seven_Seg_Hex seven_seg_hex_5 (.d(U1_pin3), .dp(1'b0));
  Seven_Seg_Hex seven_seg_hex_6 (.d({U1_pin10, Aout}), .dp(1'b0));
  _74164 U1 (
    .pin1(1'b1), .pin2(Fout), .pin3(U1_pin3[3]), .pin4(U1_pin3[2]), .pin5(U1_pin3[1]), .pin6(U1_pin3[0]),
    .pin7(1'b0), .pin8(GCLK), .pin9(CLR), .pin10(U1_pin10[3]), .pin11(U1_pin10[2]), .pin12(U1_pin10[1]),
    .pin13(Aout), .pin14(1'b1));
  _74595 U6 (
    .pin1(MA6), .pin2(MA5), .pin3(MA4), .pin4(MA3), .pin5(MA2), .pin6(MA1), .pin7(MA0), .pin8(1'b0),
    .pin10(nCLRAC), .pin11(GCLK), .pin12(RCLK), .pin13(1'b0), .pin14(U5_pin9), .pin15(MA7), .pin16(1'b1));  // open: pin9
  Seven_Seg_Hex seven_seg_hex_7 (.d({4{A8}}), .dp(1'b0));
  Seven_Seg_Hex seven_seg_hex_8 (.d({MA15, MA14, MA13, MA12}), .dp(1'b0));
  Seven_Seg_Hex seven_seg_hex_9 (.d({4{A8}}), .dp(1'b0));
  Seven_Seg_Hex seven_seg_hex_10 (.d({MA11, MA10, MA9, MA8}), .dp(1'b0));
  Seven_Seg_Hex seven_seg_hex_11 (.d({MA7, MA6, MA5, MA4}), .dp(1'b0));
  Seven_Seg_Hex seven_seg_hex_12 (.d({A7, A6, A5, A4}), .dp(1'b0));
  Seven_Seg_Hex seven_seg_hex_13 (.d({MA7, MA6, MA5, MA4}), .dp(1'b0));
  Seven_Seg_Hex seven_seg_hex_14 (.d({MA3, MA2, MA1, MA0}), .dp(1'b0));
  Seven_Seg_Hex seven_seg_hex_15 (.d({A3, A2, A1, A0}), .dp(1'b0));
  Seven_Seg_Hex seven_seg_hex_16 (.d({MA3, MA2, MA1, MA0}), .dp(1'b0));
  Seven_Seg_Hex seven_seg_hex_17 (.d({D7, D6, D5, D4}), .dp(1'b0));
  Seven_Seg_Hex seven_seg_hex_18 (.d({BUS7, BUS6, BUS5, BUS4}), .dp(1'b0));
  Seven_Seg_Hex seven_seg_hex_19 (.d({D3, D2, D1, D0}), .dp(1'b0));
  Seven_Seg_Hex seven_seg_hex_20 (.d({BUS3, BUS2, BUS1, BUS0}), .dp(1'b0));
  // _28c16 U12: pin names not known; wires that end beside it: Aout, Bout, Cin, SETC, LD_t, IR6, IR5, IR4, Cout, ResC, SetC_t, 1'b0, 1'b1, T8_t, 1'b0, 1'b1, 1'b0, 1'b0, 1'b0, LD_INC, nRD, nWR
  Seven_Seg_Hex seven_seg_hex_21 (.d({IR7, IR6, IR5, IR4}), .dp(1'b0));
  Seven_Seg_Hex seven_seg_hex_22 (.d({IR3, IR2, IR1, IR0}), .dp(1'b0));
  not not_3 (not_3_out, nWR);
  not not_4 (not_4_out, nRD);
  LED led_2 (.in(Cin));
  LED led_3 (.in(LD_t));
  LED led_4 (.in(SETC));
  LED led_5 (.in(T2));
  LED led_6 (.in(T3));
  LED led_7 (.in(T4));
  LED led_8 (.in(T5));
  LED led_9 (.in(T6));
  LED led_10 (.in(T7));
  LED led_11 (.in(T8_t));
  LED led_12 (.in(T9));
  LED led_13 (.in(not_3_out));
  LED led_14 (.in(not_4_out));
  LED nJMP (.in(LD_INC));
  _7474 U2 (
    .pin1(ResC), .pin2(Cout), .pin3(GCLK), .pin4(SetC_t), .pin5(Cin), .pin7(1'b0), .pin10(1'b1), .pin11(clk),
    .pin12(RCO), .pin13(1'b1), .pin14(1'b1));  // open: pin6, pin8, pin9
  _74165 U3 (
    .pin1(LD), .pin2(GCLK), .pin3(D3), .pin4(D2), .pin5(D1), .pin6(D0), .pin8(1'b0), .pin9(Bout),
    .pin10(1'b0), .pin11(D7), .pin12(D6), .pin13(D5), .pin14(D4), .pin15(1'b0), .pin16(1'b1));  // open: pin7
  _744017 U11 (
    .pin1(T5), .pin2(SETC), .pin3(LD_t), .pin4(T2), .pin5(T6), .pin6(T7), .pin7(T3), .pin8(1'b0),
    .pin9(T8_t), .pin10(T4), .pin11(T9), .pin13(1'b0), .pin14(clk), .pin15(1'b0), .pin16(1'b1));  // open: pin12
  not not_5 (LD, LD_t);
  not not_6 (T8, T8_t);
  nor nor_1 (GCLK, GATE, clk);
  nor nor_2 (GATE, SETC, nor_3_out);
  nor nor_3 (nor_3_out, GATE, T9);
  Reset reset_1 (.out(nCLRAC));
  not not_7 (RCLK, T8_t);

  assign T0 = LD;

  // Other names for the same wires on the sheet: A9 = A8; A10 = A8; A11 = A8; A12 = A8; A13 = A8; A14 = A8; A15 = A8;
  //   nDE = in_1; nLOAD = LD; nRESET = nCLRAC; PC_INC = T8; R0 = D0; R1 = D1; R2 = D2; R3 = D3; R4 = D4; R5 = D5;
  //   R6 = D6; R7 = D7; R8 = IR0; R9 = IR1; R10 = IR2; R11 = IR3; R12 = IR4; R13 = IR5; R14 = IR6; R15 = IR7;
  //   T0_t = LD_t; T1 = SETC

  // Notes on the sheet:
  //   in_1: default 1
  //   clk: Hz: 32
  //   MITE-15
  //   Low Address Counter
  //   RAM
  //   Instruction ROM
  //   OUTPUT
  //   ZERO
  //   ROM -> BUS
  //   MITE 8-bit  Bit serial CPU Testbed
  //   ADDR H
  //   ACCUMULATOR
  //   Shift Register A
  //   Carry is only set before Bit 0 of an operation
  //   Any residual carry is cleared before an operation
  //   RAM ADDRESS
  //   ADDRESS
  //   ADDR L
  //   ALU-PROM
  //   DATA BUS
  //   DATA
  //   ALU PROM
  //   INSTRUCTION
  //   CARRY
  //   ~WR
  //   ~RD
  //   Carry FF
  //   Clock Sequencer
  //   Shift Register B
  //   U14
endmodule
