// Digital circuit MITE_memory_section.dig as structural Verilog
module MITE_memory_section (
  input  in_1,
  input  in_2,
  input  in_3,
  input  in_4,
  input  clk,
  output T0,
  output T8,
  output T9
);

  wire A0, A1, A2, A3, A4, A5, A6, A7, A8, BUS0, BUS1, BUS2, BUS3, BUS4, BUS5, BUS6, BUS7, D0, D1, D2, D3,
       D4, D5, D6, D7, GATE, GCLK, IR0, IR1, IR2, IR3, IR4, IR5, IR6, IR7, LD, nor_1_out, nor_4_out, nRESET,
       RCO, T1, T2, T3, T4, T5, T6, T7, T8_t, T9_t, U7_p9, U7_p10, U7_p11, U7_p12, U7_p13, U7_p15, U7_p16,
       U7_p17, U7_p18, U7_p19, U7_p20, U7_p21, U7_p22, U8_2_pin2, U8_2_pin3, U8_2_pin4;

  // _62256 U17: pin names not known; wires that end beside it: A8, A8, A7, A6, A5, A4, A3, A2, A1, A0, D0, D1, D2, 1'b0, 1'b1, in_3, A8, A8, A8, A8, in_4, A8, 1'b0, D7
  _74161 U8 (
    .pin1(nRESET), .pin2(T9), .pin3(BUS0), .pin4(BUS1), .pin5(BUS2), .pin6(BUS3), .pin7(1'b1), .pin8(1'b0),
    .pin9(in_2), .pin10(1'b1), .pin11(A3), .pin12(A2), .pin13(A1), .pin14(A0), .pin15(RCO), .pin16(1'b1));
  _74161 U9 (
    .pin1(nRESET), .pin2(T9), .pin3(BUS4), .pin4(BUS5), .pin5(BUS6), .pin6(BUS7), .pin7(1'b1), .pin8(1'b0),
    .pin9(in_2), .pin10(RCO), .pin11(A7), .pin12(A6), .pin13(A5), .pin14(A4), .pin16(1'b1));  // open: pin15
  Reset reset_1 (.out(nRESET));
  // _27C1024 U7: pin names not known; wires that end beside it: A8, A8, A8, A8, A8, A8, A8, 1'b1, U7_p9, U7_p10, U7_p11, U7_p12, U7_p13, 1'b0, U7_p15, U7_p16, U7_p17, U7_p18, U7_p19, U7_p20, U7_p21, U7_p22, 1'b0, 1'b1
  _74574 U8_2 (
    .pin1(1'b0), .pin2(U8_2_pin2), .pin3(U8_2_pin3), .pin4(U8_2_pin4), .pin5(U7_p9), .pin6(U7_p10),
    .pin7(U7_p11), .pin8(U7_p12), .pin9(U7_p13), .pin10(1'b0), .pin11(LD), .pin12(IR7), .pin13(IR6),
    .pin14(IR5), .pin15(IR4), .pin16(IR3), .pin17(IR2), .pin18(IR1), .pin19(IR0), .pin20(1'b1));
  _74574 U9_2 (
    .pin1(1'b0), .pin2(U7_p15), .pin3(U7_p16), .pin4(U7_p17), .pin5(U7_p18), .pin6(U7_p19), .pin7(U7_p20),
    .pin8(U7_p21), .pin9(U7_p22), .pin10(1'b0), .pin11(LD), .pin12(D7), .pin13(D6), .pin14(D5), .pin15(D4),
    .pin16(D3), .pin17(D2), .pin18(D1), .pin19(D0), .pin20(1'b1));
  _74541 U10 (
    .pin1(in_1), .pin2(D0), .pin3(D1), .pin4(D2), .pin5(D3), .pin6(D4), .pin7(D5), .pin8(D6), .pin9(D7),
    .pin10(1'b0), .pin11(BUS7), .pin12(BUS6), .pin13(BUS5), .pin14(BUS4), .pin15(BUS3), .pin16(BUS2),
    .pin17(BUS1), .pin18(BUS0), .pin19(in_1), .pin20(1'b1));
  Seven_Seg_Hex seven_seg_hex_1 (.d({4{A8}}), .dp(1'b0));
  Seven_Seg_Hex seven_seg_hex_2 (.d({4{A8}}), .dp(1'b0));
  Seven_Seg_Hex seven_seg_hex_3 (.d({A7, A6, A5, A4}), .dp(1'b0));
  Seven_Seg_Hex seven_seg_hex_4 (.d({A3, A2, A1, A0}), .dp(1'b0));
  PullDown pulldown_1 (.out(A8));
  nor nor_1 (nor_1_out, GATE, clk);
  Seven_Seg_Hex seven_seg_hex_5 (.d({D7, D6, D5, D4}), .dp(1'b0));
  Seven_Seg_Hex seven_seg_hex_6 (.d({D3, D2, D1, D0}), .dp(1'b0));
  _744017 U16 (
    .pin1(T5), .pin2(T1), .pin3(LD), .pin4(T2), .pin5(T6), .pin6(T7), .pin7(T3), .pin8(1'b0), .pin9(T8_t),
    .pin10(T4), .pin11(T9_t), .pin13(1'b0), .pin14(clk), .pin15(1'b0), .pin16(1'b1));  // open: pin12
  nor nor_2 (GCLK, nor_1_out, nor_1_out);
  Seven_Seg_Hex seven_seg_hex_7 (.d({IR7, IR6, IR5, IR4}), .dp(1'b0));
  not not_1 (T0, LD);
  not not_2 (T8, T8_t);
  not not_3 (T9, T9_t);
  Seven_Seg_Hex seven_seg_hex_8 (.d({IR3, IR2, IR1, IR0}), .dp(1'b0));
  nor nor_3 (GATE, T1, nor_4_out);
  nor nor_4 (nor_4_out, GATE, T9_t);

  // Other names for the same wires on the sheet: A9 = A8; A10 = A8; A11 = A8; A12 = A8; A13 = A8; A14 = A8; A15 = A8;
  //   C_RAM = in_3; CLK_D = T9; nCTRLD = in_2; nDE = in_1; nLOAD = T0; RCLK = T8; RDRAM = in_4; T0_t = LD

  // Notes on the sheet:
  //   in_2: default 1
  //   in_3: default 1
  //   in_4: default 1
  //   clk: Hz: 16
  //   ROM & PC
  //   Low Address Counter
  //   RAM
  //   ADDRESS
  //   DATA
endmodule
