// Digital circuit Memory_subsection.dig as structural Verilog
module Memory_subsection (
  input  clk
);

  wire A0, A1, A2, A3, A4, A5, A6, A7, A8, A9, A10, A11, A12, A13, A14, A15, ASEL, C_0, C_1, C_2, C_3, C_4,
       C_5, C_6, C_7, CKCTL, CLK_D, CLK_S, CLKCTL, D0, D1, D2, D3, D4, D5, D6, D7, DTSEL, INSEL, IR0, IR1,
       IR2, IR3, IR4, IR5, IR6, IR7, nCTRLD, nDE, nFETCH, nOEADR, nOECTR, nOEDTR, nor_1_out, not_1_out,
       nPHASE, nRDRAM, nRESET, nWR, nWRRAM, OEADR, OECTR, OEDATAR, PHASE, R0, R1, R2, R3, R4, R5, R6, R7,
       RCO, RDIN1, RDRAM, RDROM, RESET, reset_1_out, uA0, uA1, uA2, uA3, uA4, uA5, uA6, uA7;

  _74573 _74573_1 (
    .pin1(nDE), .pin2(D7), .pin3(D6), .pin4(D5), .pin5(D4), .pin6(D3), .pin7(D2), .pin8(D1), .pin9(D0),
    .pin10(1'b0), .pin11(nRESET), .pin12(IR0), .pin13(IR1), .pin14(IR2), .pin15(IR3), .pin16(IR4),
    .pin17(IR5), .pin18(IR6), .pin19(IR7), .pin20(1'b1));
  _74161 U2 (
    .pin1(nRESET), .pin2(CLK_D), .pin3(A0), .pin4(A1), .pin5(A2), .pin6(A3), .pin7(1'b1), .pin8(1'b0),
    .pin9(nCTRLD), .pin10(1'b1), .pin11(uA3), .pin12(uA2), .pin13(uA1), .pin14(uA0), .pin15(RCO), .pin16(1'b1));
  _74161 U3 (
    .pin1(nRESET), .pin2(CLK_D), .pin3(A4), .pin4(A5), .pin5(A6), .pin6(A7), .pin7(1'b1), .pin8(1'b0),
    .pin9(nCTRLD), .pin10(RCO), .pin11(uA7), .pin12(uA6), .pin13(uA5), .pin14(uA4), .pin16(1'b1));  // open: pin15
  _74574 U5 (
    .pin1(nOECTR), .pin2(D7), .pin3(D6), .pin4(D5), .pin5(D4), .pin6(D3), .pin7(D2), .pin8(D1), .pin9(D0),
    .pin10(1'b0), .pin11(nFETCH), .pin12(A8), .pin13(A9), .pin14(A10), .pin15(A11), .pin16(A12), .pin17(A13),
    .pin18(A14), .pin19(A15), .pin20(1'b1));
  _74541 U4 (
    .pin1(nOECTR), .pin2(uA0), .pin3(uA1), .pin4(uA2), .pin5(uA3), .pin6(uA4), .pin7(uA5), .pin8(uA6),
    .pin9(uA7), .pin10(1'b0), .pin11(A7), .pin12(A6), .pin13(A5), .pin14(A4), .pin15(A3), .pin16(A2),
    .pin17(A1), .pin18(A0), .pin19(nOECTR), .pin20(1'b1));
  PullDown pulldown_1 (.out(D0));
  PullDown pulldown_2 (.out(D1));
  _74574 U6 (
    .pin1(nOEADR), .pin2(D7), .pin3(D6), .pin4(D5), .pin5(D4), .pin6(D3), .pin7(D2), .pin8(D1), .pin9(D0),
    .pin10(1'b0), .pin11(C_4), .pin12(A0), .pin13(A1), .pin14(A2), .pin15(A3), .pin16(A4), .pin17(A5),
    .pin18(A6), .pin19(A7), .pin20(1'b1));
  _74574 U7 (
    .pin1(nOEADR), .pin2(D7), .pin3(D6), .pin4(D5), .pin5(D4), .pin6(D3), .pin7(D2), .pin8(D1), .pin9(D0),
    .pin10(1'b0), .pin11(C_5), .pin12(A8), .pin13(A9), .pin14(A10), .pin15(A11), .pin16(A12), .pin17(A13),
    .pin18(A14), .pin19(A15), .pin20(1'b1));
  PullDown pulldown_3 (.out(D2));
  PullDown pulldown_4 (.out(D3));
  PullDown pulldown_5 (.out(D4));
  PullDown pulldown_6 (.out(D5));
  PullDown pulldown_7 (.out(D6));
  PullDown pulldown_8 (.out(D7));
  // A623308A U16: pin names not known; wires that end beside it: A14, A12, A7, A6, A5, A4, A3, A2, A1, A0, D0, D1, 1'b1, nWRRAM, A13, A8, A9, A11, nRDRAM, A10, 1'b0, D7
  // _28c256 U15: pin names not known; wires that end beside it: D2, 1'b0, A14, A12, A7, A6, A5, A4, A3, A2, A1, A0, D0, D1, D2, 1'b0, 1'b1, nWR, A13, A8, A9, A11, RDROM, A10, RESET, D7
  _74139 U14 (
    .pin1(clk), .pin2(DTSEL), .pin3(PHASE), .pin6(CLKCTL), .pin7(OEDATAR), .pin8(1'b0), .pin9(RDIN1),
    .pin10(RDRAM), .pin13(A15), .pin14(INSEL), .pin15(CLKCTL), .pin16(1'b1));  // open: pin4, pin5, pin11, pin12
  _74138 _74138_1 (
    .pin1(IR0), .pin2(IR1), .pin3(IR2), .pin4(CLK_S), .pin5(1'b0), .pin6(PHASE), .pin7(C_7), .pin8(1'b0),
    .pin9(C_6), .pin10(C_5), .pin11(C_4), .pin12(C_3), .pin13(C_2), .pin14(C_1), .pin15(C_0), .pin16(1'b1));
  not not_1 (not_1_out, clk);
  nor nor_1 (nor_1_out, A15, CKCTL);
  nor nor_2 (CLK_D, 1'b0, not_1_out);
  not not_2 (nPHASE, PHASE);
  not not_3 (CLK_S, not_1_out);
  _74574 U15_2 (
    .pin1(nOEDTR), .pin2(D7), .pin3(D6), .pin4(D5), .pin5(D4), .pin6(D3), .pin7(D2), .pin8(D1), .pin9(D0),
    .pin10(1'b0), .pin11(C_3), .pin12(D0), .pin13(D1), .pin14(D2), .pin15(D3), .pin16(D4), .pin17(D5),
    .pin18(D6), .pin19(D7), .pin20(1'b1));
  nor nor_3 (RDROM, nPHASE, nor_1_out);
  Reset reset_1 (.out(reset_1_out));
  D_FF_AS U1B (.Set(1'b1), .D(reset_1_out), .C(CLK_S), .Clr(1'b1), .Q(RESET), .nQ(nRESET));
  _74541 U12 (
    .pin1(nDE), .pin2(D7), .pin3(D6), .pin4(D5), .pin5(D4), .pin6(D3), .pin7(D2), .pin8(D1), .pin9(D0),
    .pin10(1'b0), .pin11(R0), .pin12(R1), .pin13(R2), .pin14(R3), .pin15(R4), .pin16(R5), .pin17(R6),
    .pin18(R7));  // open: pin19, pin20
  and and_1 (OECTR, nPHASE, ASEL);
  and and_2 (nFETCH, C_0, nRESET);
  // And and_3 is placed but not wired
  // And and_4 is placed but not wired
  not not_4 (OEADR, OECTR);

  // Other names for the same wires on the sheet: C_ACC = C_2; C_ADDRH = C_5; C_ADDRL = C_4; C_DATAR = C_3;
  //   C_EXT = C_7; C_OP = C_0; C_OUT = C_1; C_RAM = C_6

  // Notes on the sheet:
  //   uCODE Counter
  //   Inst Reg.
  //   D->ADDR-H
  //   CTR->ADDR-L
  //   ADDR-L
  //   ADDR-H
  //   RAM
  //   EPROM
  //   Source Select
  //   Data Reg
  //   ROM -> BUS
endmodule
