// Digital circuit Mite_4_with_4017.dig as structural Verilog
module Mite_4_with_4017 (
  input  clk,
  input  in_2,
  input  in_3,
  input  in_4,
  output LD,
  output GCLK,
  output T0,
  output T8,
  output T9,
  output SETC
);

  wire ADD, AND, Aout, Bout, BUS0, BUS1, BUS2, BUS3, BUS4, BUS5, BUS6, BUS7, button_1_out, button_2_out,
       button_3_out, button_4_out, button_5_out, button_6_out, button_7_out, button_8_out, button_9_out, C,
       Cin, CLA, CLR, Cout, D0, D1, D2, D3, D4, D5, D6, D7, d_ff_1_nq, d_ff_2_nq, d_ff_3_nq, d_ff_4_nq,
       d_ff_5_nq, d_ff_6_nq, diodebackward_2_out, diodebackward_6_out, diodebackward_8_out,
       diodebackward_11_out, diodeforward_1_out, F, Fout, GATE, I0, I1, IC16_2_nq, IC16_nq, LD_t, LOAD, nA,
       nand_2_out, nand_3_out, nand_5_out, nand_6_out, nand_7_out, nand_8_out, nand_9_out, nand_10_out,
       nand_11_out, nB, nCLRAC, nJMP, nor_1_out, nor_3_out, OR, pullup_1_out, pullup_4_out, pullup_5_out, ST,
       SUB, T2, T3, T4, T5, T6, T7, T8_t, T9_t, XOR, xor_1_out, xor_2_out, xor_3_out, xor_4_out, ZERO;

  _74138 U1 (
    .pin1(in_2), .pin2(in_3), .pin3(in_4), .pin4(1'b0), .pin5(1'b0), .pin6(1'b1), .pin7(nJMP), .pin8(1'b0),
    .pin9(ST), .pin10(SUB), .pin11(ADD), .pin12(XOR), .pin13(OR), .pin14(AND), .pin15(LOAD), .pin16(1'b1));
  PullUp pullup_1 (.out(pullup_1_out));
  DiodeBackward diodebackward_1 (.in(LOAD), .out(pullup_1_out));
  DiodeBackward diodebackward_2 (.in(LOAD), .out(diodebackward_2_out));
  DiodeBackward diodebackward_3 (.in(ADD), .out(diodebackward_2_out));
  DiodeBackward diodebackward_4 (.in(SUB), .out(diodebackward_2_out));
  DiodeBackward diodebackward_5 (.in(nJMP), .out(diodebackward_2_out));
  Monoflop monoflop_1 (.C(button_1_out), .R(1'b0), .nQ(nCLRAC));  // open: Q
  Button button_1 (.out(button_1_out));
  _74165 U3 (
    .pin1(LD), .pin2(GCLK), .pin3(D3), .pin4(D2), .pin5(D1), .pin6(D0), .pin8(1'b0), .pin9(Bout),
    .pin10(1'b0), .pin11(D7), .pin12(D6), .pin13(D5), .pin14(D4), .pin15(1'b0), .pin16(1'b1));  // open: pin7
  PullUp pullup_2 (.out(diodebackward_2_out));
  DiodeBackward diodebackward_6 (.in(SUB), .out(diodebackward_6_out));
  PullUp pullup_3 (.out(diodebackward_6_out));
  PullUp pullup_4 (.out(pullup_4_out));
  DiodeBackward diodebackward_7 (.in(SUB), .out(pullup_4_out));
  PullUp pullup_5 (.out(pullup_5_out));
  DiodeBackward diodebackward_8 (.in(AND), .out(diodebackward_8_out));
  DiodeBackward diodebackward_9 (.in(OR), .out(diodebackward_8_out));
  DiodeBackward diodebackward_10 (.in(nJMP), .out(pullup_5_out));
  PullUp pullup_6 (.out(diodebackward_8_out));
  DiodeBackward diodebackward_11 (.in(LOAD), .out(diodebackward_11_out));
  DiodeBackward diodebackward_12 (.in(OR), .out(diodebackward_11_out));
  DiodeBackward diodebackward_13 (.in(XOR), .out(diodebackward_11_out));
  DiodeBackward diodebackward_14 (.in(ADD), .out(diodebackward_11_out));
  DiodeBackward diodebackward_15 (.in(SUB), .out(diodebackward_11_out));
  DiodeBackward diodebackward_16 (.in(ST), .out(diodebackward_11_out));
  DiodeBackward diodebackward_17 (.in(nJMP), .out(diodebackward_11_out));
  PullUp pullup_7 (.out(diodebackward_11_out));
  _74540 U2 (
    .pin1(1'b0), .pin2(diodebackward_11_out), .pin3(diodebackward_8_out), .pin4(pullup_5_out),
    .pin5(pullup_4_out), .pin6(diodebackward_6_out), .pin7(diodebackward_2_out), .pin8(pullup_1_out),
    .pin9(1'b0), .pin10(1'b0), .pin12(CLA), .pin13(F), .pin14(C), .pin15(nB), .pin16(nA), .pin17(I1),
    .pin18(I0), .pin19(1'b0), .pin20(1'b1));  // open: pin11
  _74595 U4 (
    .pin1(BUS6), .pin2(BUS5), .pin3(BUS4), .pin4(BUS3), .pin5(BUS2), .pin6(BUS1), .pin7(BUS0), .pin8(1'b0),
    .pin9(Aout), .pin10(1'b1), .pin11(GCLK), .pin12(T9), .pin13(1'b0), .pin14(Fout), .pin15(BUS7),
    .pin16(1'b1));
  LED led_1 (.in(D7));
  D_FF IC16 (.D(IC16_nq), .C(button_2_out), .Q(D7), .nQ(IC16_nq));
  Button button_2 (.out(button_2_out));
  LED led_2 (.in(D6));
  D_FF d_ff_1 (.D(d_ff_1_nq), .C(button_3_out), .Q(D6), .nQ(d_ff_1_nq));
  Button button_3 (.out(button_3_out));
  LED led_3 (.in(D5));
  D_FF d_ff_2 (.D(d_ff_2_nq), .C(button_4_out), .Q(D5), .nQ(d_ff_2_nq));
  Button button_4 (.out(button_4_out));
  LED led_4 (.in(D4));
  D_FF d_ff_3 (.D(d_ff_3_nq), .C(button_5_out), .Q(D4), .nQ(d_ff_3_nq));
  Button button_5 (.out(button_5_out));
  LED led_5 (.in(D3));
  D_FF d_ff_4 (.D(d_ff_4_nq), .C(button_6_out), .Q(D3), .nQ(d_ff_4_nq));
  Button button_6 (.out(button_6_out));
  DiodeForward diodeforward_1 (.in(BUS7), .out(diodeforward_1_out));
  DiodeForward diodeforward_2 (.in(BUS6), .out(diodeforward_1_out));
  DiodeForward diodeforward_3 (.in(BUS5), .out(diodeforward_1_out));
  DiodeForward diodeforward_4 (.in(BUS4), .out(diodeforward_1_out));
  DiodeForward diodeforward_5 (.in(BUS3), .out(diodeforward_1_out));
  DiodeForward diodeforward_6 (.in(BUS2), .out(diodeforward_1_out));
  DiodeForward diodeforward_7 (.in(BUS1), .out(diodeforward_1_out));
  DiodeForward diodeforward_8 (.in(BUS0), .out(diodeforward_1_out));
  LED led_6 (.in(D2));
  D_FF d_ff_5 (.D(d_ff_5_nq), .C(button_7_out), .Q(D2), .nQ(d_ff_5_nq));
  Button button_7 (.out(button_7_out));
  LED led_7 (.in(D1));
  D_FF d_ff_6 (.D(d_ff_6_nq), .C(button_8_out), .Q(D1), .nQ(d_ff_6_nq));
  Button button_8 (.out(button_8_out));
  Seven_Seg_Hex seven_seg_hex_1 (.d({BUS7, BUS6, BUS5, BUS4}), .dp(1'b0));
  nand nand_1 (ZERO, diodeforward_1_out, diodeforward_1_out);
  PullDown pulldown_1 (.out(diodeforward_1_out));
  LED led_8 (.in(D0));
  D_FF IC16_2 (.D(IC16_2_nq), .C(button_9_out), .Q(D0), .nQ(IC16_2_nq));
  Button button_9 (.out(button_9_out));
  Seven_Seg_Hex seven_seg_hex_2 (.d({BUS3, BUS2, BUS1, BUS0}), .dp(1'b0));
  Seven_Seg_Hex seven_seg_hex_3 (.d({D7, D6, D5, D4}), .dp(1'b0));
  LED led_9 (.in(ZERO));
  Seven_Seg_Hex seven_seg_hex_4 (.d({D3, D2, D1, D0}), .dp(1'b0));
  xor xor_1 (xor_1_out, Aout, nA);
  xor xor_2 (xor_2_out, nB, Bout);
  nand nand_2 (nand_2_out, SETC, C);
  nand nand_3 (nand_3_out, C, C);
  nand nand_4 (CLR, CLA, LD_t);
  xor xor_3 (xor_3_out, xor_1_out, xor_2_out);
  nand nand_5 (nand_5_out, nand_3_out, LD_t);
  xor xor_4 (xor_4_out, xor_3_out, Cin);
  nand nand_6 (nand_6_out, xor_3_out, Cin);
  nand nand_7 (nand_7_out, xor_1_out, xor_2_out);
  nand nand_8 (nand_8_out, nand_6_out, nand_7_out);
  nand nand_9 (nand_9_out, xor_4_out, I0);
  nand nand_10 (nand_10_out, I1, nand_8_out);
  nand nand_11 (nand_11_out, nand_8_out, F);
  nand nand_12 (Fout, nand_9_out, nand_10_out);
  nand nand_13 (Cout, nand_11_out, nand_11_out);
  _7474 U12 (
    .pin1(nand_5_out), .pin2(Cout), .pin3(GCLK), .pin4(nand_2_out), .pin5(Cin), .pin7(1'b0), .pin10(1'b1),
    .pin11(1'b1), .pin12(1'b1), .pin13(1'b1), .pin14(1'b1));  // open: pin6, pin8, pin9
  LED led_10 (.in(Cin));
  _744017 U16 (
    .pin1(T5), .pin2(SETC), .pin3(LD_t), .pin4(T2), .pin5(T6), .pin6(T7), .pin7(T3), .pin8(1'b0),
    .pin9(T8_t), .pin10(T4), .pin11(T9_t), .pin13(1'b0), .pin14(clk), .pin15(1'b0), .pin16(1'b1));  // open: pin12
  nor nor_1 (nor_1_out, GATE, clk);
  nor nor_2 (GATE, SETC, nor_3_out);
  nor nor_3 (nor_3_out, GATE, T9_t);
  nor nor_4 (GCLK, nor_1_out, nor_1_out);
  not not_1 (LD, LD_t);
  // Not not_2 has open pins: in=SETC, out=open
  // Not not_3 has open pins: in=T2, out=open
  // Not not_4 has open pins: in=T3, out=open
  // Not not_5 has open pins: in=T4, out=open
  // Not not_6 has open pins: in=T5, out=open
  // Not not_7 has open pins: in=T6, out=open
  // Not not_8 has open pins: in=T7, out=open
  not not_9 (T8, T8_t);
  not not_10 (T9, T9_t);

  assign T0 = LD;

  // Other names for the same wires on the sheet: nLOAD = LD; RCLK = T9; T0_t = LD_t; T1 = SETC

  // Notes on the sheet:
  //   clk: Hz: 4
  //   MITE 4
  //   Instruction Input
  //   STEP/RUN
  //   8-bit Shift Register B
  //   CLR Acc
  //   CLA
  //   F
  //   ~B
  //   C
  //   ~A
  //   I1
  //   I0
  //   LOAD
  //   AND
  //   OR
  //   XOR
  //   ADD
  //   SUB
  //   STORE
  //   JMP
  //   ACCUMULATOR
  //   ENTER L
  //   ZERO
  //   ALU
  //   CLR ACC
  //   MITE 8-bit  Bit serial CPU Testbed
  //   Carry is only set before Bit 0 of an operation
  //   Any residual carry is cleared before an operation
  //   Suppress Carry
  //   Carry FF
  //   CARRY
  //   8 pulse Clock Sequencer (2 ICs)
endmodule
