// Digital circuit Mite_5.dig as structural Verilog
module Mite_5 (
  input  clk,
  input  in_2,
  input  in_3,
  input  in_4,
  output LD,
  output RES,
  output GCLK,
  output T0,
  output nRST,
  output CLR,
  output Fout,
  output CtoFF,
  output ResC,
  output Cout
);

  wire ADD, AND, Aout, Bout, BUS0, BUS1, BUS2, BUS3, BUS4, BUS5, BUS6, BUS7, button_1_out, button_2_out,
       button_3_out, button_4_out, button_5_out, button_6_out, button_7_out, button_8_out, button_9_out,
       button_10_out, C, Cin, CLA, D0, D1, D2, D3, D4, D5, D6, D7, d_ff_1_nq, d_ff_2_nq, d_ff_3_nq,
       d_ff_4_nq, d_ff_5_nq, d_ff_6_nq, diodebackward_1_out, diodebackward_6_out, diodebackward_8_out,
       diodeforward_1_out, F, I0, I1, IC16_2_nq, IC16_nq, IX, LD_t, LOAD, nA, nand_3_out, nand_5_out,
       nand_10_out, nand_11_out, nand_12_out, nand_13_out, nand_14_out, nand_15_out, nB, nCE, nCLRPC, nJMP,
       OR, pullup_1_out, pullup_3_out, pullup_6_out, pullup_7_out, RCO, RST, SETC, ST, SUB, U7_pin15, XOR,
       xor_1_out, xor_2_out, xor_3_out, xor_4_out, ZERO;
  wire [3:0] U6_pin3, U7_pin11;
  wire [3:1] U6_pin10;

  Seven_Seg_Hex seven_seg_hex_1 (.d(U6_pin3), .dp(1'b0));
  Seven_Seg_Hex seven_seg_hex_2 (.d({U6_pin10, Aout}), .dp(1'b0));
  _74164 U6 (
    .pin1(1'b1), .pin2(Fout), .pin3(U6_pin3[3]), .pin4(U6_pin3[2]), .pin5(U6_pin3[1]), .pin6(U6_pin3[0]),
    .pin7(1'b0), .pin8(GCLK), .pin9(CLR), .pin10(U6_pin10[3]), .pin11(U6_pin10[2]), .pin12(U6_pin10[1]),
    .pin13(Aout), .pin14(1'b1));
  _74138 U1 (
    .pin1(in_2), .pin2(in_3), .pin3(in_4), .pin4(1'b0), .pin5(1'b0), .pin6(1'b1), .pin7(nJMP), .pin8(1'b0),
    .pin9(ST), .pin10(SUB), .pin11(ADD), .pin12(XOR), .pin13(OR), .pin14(AND), .pin15(LOAD), .pin16(1'b1));
  Monoflop monoflop_1 (.C(LD), .R(1'b0), .Q(SETC), .nQ(RES));
  Monoflop monoflop_2 (.C(button_1_out), .R(1'b0), .Q(LD_t), .nQ(LD));
  Button button_1 (.out(button_1_out));
  DiodeBackward diodebackward_1 (.in(LOAD), .out(diodebackward_1_out));
  Monoflop monoflop_3 (.C(button_2_out), .R(1'b0), .nQ(nCLRPC));  // open: Q
  Button button_2 (.out(button_2_out));
  PullUp pullup_1 (.out(pullup_1_out));
  PullUp pullup_2 (.out(diodebackward_1_out));
  DiodeBackward diodebackward_2 (.in(LOAD), .out(pullup_1_out));
  DiodeBackward diodebackward_3 (.in(ADD), .out(pullup_1_out));
  DiodeBackward diodebackward_4 (.in(SUB), .out(pullup_1_out));
  DiodeBackward diodebackward_5 (.in(nJMP), .out(pullup_1_out));
  _74165 U3 (
    .pin1(LD), .pin2(GCLK), .pin3(D3), .pin4(D2), .pin5(D1), .pin6(D0), .pin8(1'b0), .pin9(Bout),
    .pin10(1'b0), .pin11(D7), .pin12(D6), .pin13(D5), .pin14(D4), .pin15(1'b0), .pin16(1'b1));  // open: pin7
  PullUp pullup_3 (.out(pullup_3_out));
  DiodeBackward diodebackward_6 (.in(SUB), .out(diodebackward_6_out));
  DiodeBackward diodebackward_7 (.in(SUB), .out(pullup_3_out));
  PullUp pullup_4 (.out(diodebackward_6_out));
  DiodeBackward diodebackward_8 (.in(nJMP), .out(diodebackward_8_out));
  PullUp pullup_5 (.out(diodebackward_8_out));
  PullUp pullup_6 (.out(pullup_6_out));
  DiodeBackward diodebackward_9 (.in(AND), .out(pullup_6_out));
  DiodeBackward diodebackward_10 (.in(OR), .out(pullup_6_out));
  PullUp pullup_7 (.out(pullup_7_out));
  DiodeBackward diodebackward_11 (.in(LOAD), .out(pullup_7_out));
  DiodeBackward diodebackward_12 (.in(OR), .out(pullup_7_out));
  DiodeBackward diodebackward_13 (.in(XOR), .out(pullup_7_out));
  DiodeBackward diodebackward_14 (.in(ADD), .out(pullup_7_out));
  DiodeBackward diodebackward_15 (.in(SUB), .out(pullup_7_out));
  DiodeBackward diodebackward_16 (.in(ST), .out(pullup_7_out));
  DiodeBackward diodebackward_17 (.in(nJMP), .out(pullup_7_out));
  _74540 U2 (
    .pin1(1'b0), .pin2(pullup_7_out), .pin3(pullup_6_out), .pin4(diodebackward_8_out),
    .pin5(diodebackward_6_out), .pin6(pullup_3_out), .pin7(pullup_1_out), .pin8(diodebackward_1_out),
    .pin9(1'b0), .pin10(1'b0), .pin12(CLA), .pin13(F), .pin14(C), .pin15(nB), .pin16(nA), .pin17(I1),
    .pin18(I0), .pin19(1'b0), .pin20(1'b1));  // open: pin11
  LED led_1 (.in(D7));
  D_FF IC16 (.D(IC16_nq), .C(button_3_out), .Q(D7), .nQ(IC16_nq));
  Button button_3 (.out(button_3_out));
  LED led_2 (.in(D6));
  D_FF d_ff_1 (.D(d_ff_1_nq), .C(button_4_out), .Q(D6), .nQ(d_ff_1_nq));
  Button button_4 (.out(button_4_out));
  _74595 U4 (
    .pin1(BUS6), .pin2(BUS5), .pin3(BUS4), .pin4(BUS3), .pin5(BUS2), .pin6(BUS1), .pin7(BUS0), .pin8(1'b0),
    .pin10(RES), .pin11(GCLK), .pin12(T0), .pin13(1'b0), .pin14(Fout), .pin15(BUS7), .pin16(1'b1));  // open: pin9
  LED led_3 (.in(D5));
  D_FF d_ff_2 (.D(d_ff_2_nq), .C(button_5_out), .Q(D5), .nQ(d_ff_2_nq));
  Button button_5 (.out(button_5_out));
  LED led_4 (.in(D4));
  D_FF d_ff_3 (.D(d_ff_3_nq), .C(button_6_out), .Q(D4), .nQ(d_ff_3_nq));
  Button button_6 (.out(button_6_out));
  LED led_5 (.in(D3));
  D_FF d_ff_4 (.D(d_ff_4_nq), .C(button_7_out), .Q(D3), .nQ(d_ff_4_nq));
  Button button_7 (.out(button_7_out));
  LED led_6 (.in(D2));
  D_FF d_ff_5 (.D(d_ff_5_nq), .C(button_8_out), .Q(D2), .nQ(d_ff_5_nq));
  Button button_8 (.out(button_8_out));
  DiodeForward diodeforward_1 (.in(BUS7), .out(diodeforward_1_out));
  DiodeForward diodeforward_2 (.in(BUS6), .out(diodeforward_1_out));
  DiodeForward diodeforward_3 (.in(BUS5), .out(diodeforward_1_out));
  DiodeForward diodeforward_4 (.in(BUS4), .out(diodeforward_1_out));
  DiodeForward diodeforward_5 (.in(BUS3), .out(diodeforward_1_out));
  DiodeForward diodeforward_6 (.in(BUS2), .out(diodeforward_1_out));
  DiodeForward diodeforward_7 (.in(BUS1), .out(diodeforward_1_out));
  DiodeForward diodeforward_8 (.in(BUS0), .out(diodeforward_1_out));
  LED led_7 (.in(D1));
  D_FF d_ff_6 (.D(d_ff_6_nq), .C(button_9_out), .Q(D1), .nQ(d_ff_6_nq));
  Button button_9 (.out(button_9_out));
  LED led_8 (.in(D0));
  D_FF IC16_2 (.D(IC16_2_nq), .C(button_10_out), .Q(D0), .nQ(IC16_2_nq));
  Button button_10 (.out(button_10_out));
  PullDown pulldown_1 (.out(diodeforward_1_out));
  Seven_Seg_Hex seven_seg_hex_3 (.d({D7, D6, D5, D4}), .dp(1'b0));
  Seven_Seg_Hex seven_seg_hex_4 (.d({BUS7, BUS6, BUS5, BUS4}), .dp(1'b0));
  nand nand_1 (ZERO, diodeforward_1_out, diodeforward_1_out);
  Seven_Seg_Hex seven_seg_hex_5 (.d({D3, D2, D1, D0}), .dp(1'b0));
  Seven_Seg_Hex seven_seg_hex_6 (.d({BUS3, BUS2, BUS1, BUS0}), .dp(1'b0));
  LED led_9 (.in(ZERO));
  xor xor_1 (xor_1_out, Aout, nA);
  xor xor_2 (xor_2_out, nB, Bout);
  // NAnd nand_2 has open pins: In_1=SETC, In_2=C, out=open
  nand nand_3 (nand_3_out, C, C);
  nand nand_4 (CLR, CLA, LD_t);
  nand nand_5 (nand_5_out, clk, clk);
  nand nand_6 (RST, RES, nRST);
  nand nand_7 (nRST, RST, T0);
  xor xor_3 (xor_3_out, xor_1_out, xor_2_out);
  // NAnd nand_8 has open pins: In_1=nand_3_out, In_2=LD_t, out=open
  nand nand_9 (GCLK, nand_5_out, RST);
  xor xor_4 (xor_4_out, xor_3_out, Cin);
  nand nand_10 (nand_10_out, xor_3_out, Cin);
  nand nand_11 (nand_11_out, xor_1_out, xor_2_out);
  nand nand_12 (nand_12_out, nand_10_out, nand_11_out);
  _74161 U7 (
    .pin1(RST), .pin2(clk), .pin3(1'b0), .pin4(1'b0), .pin5(1'b0), .pin6(1'b0), .pin7(1'b1), .pin8(1'b0),
    .pin9(1'b1), .pin10(1'b1), .pin11(U7_pin11[3]), .pin12(U7_pin11[2]), .pin13(U7_pin11[1]),
    .pin14(U7_pin11[0]), .pin15(U7_pin15), .pin16(1'b1));
  nand nand_13 (nand_13_out, xor_4_out, I0);
  nand nand_14 (nand_14_out, I1, nand_12_out);
  nand nand_15 (nand_15_out, nand_12_out, F);
  // NAnd nand_16 has open pins: In_1=nand_13_out, In_2=nand_14_out, out=open
  // NAnd nand_17 has open pins: In_1=nand_15_out, In_2=nand_15_out, out=open
  Seven_Seg_Hex seven_seg_hex_7 (.d(U7_pin11), .dp(1'b0));
  and and_1 (RCO, U7_pin11[2], U7_pin11[1], U7_pin11[0]);
  and and_2 (nCE, LD, T0, nRST);
  _7474 U12 (
    .pin1(ResC), .pin2(Cout), .pin3(GCLK), .pin4(CtoFF), .pin5(Cin), .pin7(1'b0), .pin8(T0), .pin9(IX),
    .pin10(1'b1), .pin11(clk), .pin12(RCO), .pin13(1'b1), .pin14(1'b1));  // open: pin6
  LED led_10 (.in(Cin));
  // _28c16 _28c16_1: pin names not known; wires that end beside it: Aout, Bout, Cin, SETC, LD_t, in_4, in_3, in_2, Cout, ResC, CtoFF, 1'b0, 1'b1, 1'b0, 1'b0, 1'b1, 1'b0, 1'b0, 1'b0

  // Other names for the same wires on the sheet: IR4 = in_2; IR5 = in_3; IR6 = in_4; nLOAD = LD; nRES = RES;
  //   SetC_t = CtoFF

  // Notes on the sheet:
  //   clk: Hz: 10
  //   MITE
  //   ACCUMULATOR
  //   Shift Register A
  //   Instruction Input
  //   STEP/RUN
  //   CLR PC
  //   8-bit Shift Register B
  //   Instruction Decode
  //   F
  //   CLA
  //   C
  //   ~B
  //   I1
  //   ~A
  //   I0
  //   LOAD
  //   AND
  //   OR
  //   XOR
  //   ADD
  //   SUB
  //   STORE
  //   JMP
  //   Output Display Register
  //   ENTER L
  //   ZERO
  //   ALU
  //   CLR ACC
  //   U5
  //   MITE 8-bit  Bit serial CPU Testbed
  //   Clock Sequencer
  //   Carry is only set before Bit 0 of an operation
  //   Any residual carry is cleared before an operation
  //   Suppress Carry
  //   # Clock
  //   Carry FF
  //   CARRY
endmodule
