// Digital circuit Mite_with_ROM_ALU_1.dig as structural Verilog
module Mite_with_ROM_ALU_1 (
  input  clk,
  input  I4,
  input  I5,
  input  I6,
  output LD,
  output RES,
  output GCLK,
  output T0,
  output nRST,
  output CLR,
  output Fout,
  output CtoFF,
  output ResC,
  output Cout
);

  wire Ain, Bin, BUS0, BUS1, BUS2, BUS3, BUS4, BUS5, BUS6, BUS7, button_1_out, button_2_out, button_3_out,
       button_4_out, button_5_out, button_6_out, button_7_out, button_8_out, button_9_out, button_10_out,
       Cin, D0, D1, D2, D3, D4, D5, D6, D7, d_ff_1_nq, d_ff_2_nq, d_ff_3_nq, d_ff_4_nq, d_ff_5_nq, d_ff_6_nq,
       diodeforward_1_out, IC16_2_nq, IC16_nq, IX, LD_t, nand_2_out, nCE, nCLRPC, RCO, RST, SETC, U7_pin15,
       ZERO;
  wire [3:0] U4_pin3, U7_pin11;
  wire [3:1] U4_pin10;

  _74165 U3 (
    .pin1(LD), .pin2(GCLK), .pin3(D3), .pin4(D2), .pin5(D1), .pin6(D0), .pin8(1'b0), .pin9(Bin),
    .pin10(1'b0), .pin11(D7), .pin12(D6), .pin13(D5), .pin14(D4), .pin15(1'b0), .pin16(1'b1));  // open: pin7
  Monoflop monoflop_1 (.C(LD), .R(1'b0), .Q(SETC), .nQ(RES));
  Monoflop monoflop_2 (.C(button_1_out), .R(1'b0), .Q(LD_t), .nQ(LD));
  Button button_1 (.out(button_1_out));
  Seven_Seg_Hex seven_seg_hex_1 (.d(U4_pin3), .dp(1'b0));
  Monoflop monoflop_3 (.C(button_2_out), .R(1'b0), .nQ(nCLRPC));  // open: Q
  Button button_2 (.out(button_2_out));
  Seven_Seg_Hex seven_seg_hex_2 (.d({U4_pin10, Ain}), .dp(1'b0));
  _74164 U4 (
    .pin1(1'b1), .pin2(Fout), .pin3(U4_pin3[3]), .pin4(U4_pin3[2]), .pin5(U4_pin3[1]), .pin6(U4_pin3[0]),
    .pin7(1'b0), .pin8(GCLK), .pin9(CLR), .pin10(U4_pin10[3]), .pin11(U4_pin10[2]), .pin12(U4_pin10[1]),
    .pin13(Ain), .pin14(1'b1));
  LED led_1 (.in(D7));
  D_FF IC16 (.D(IC16_nq), .C(button_3_out), .Q(D7), .nQ(IC16_nq));
  Button button_3 (.out(button_3_out));
  LED led_2 (.in(D6));
  D_FF d_ff_1 (.D(d_ff_1_nq), .C(button_4_out), .Q(D6), .nQ(d_ff_1_nq));
  Button button_4 (.out(button_4_out));
  _74595 U5 (
    .pin1(BUS6), .pin2(BUS5), .pin3(BUS4), .pin4(BUS3), .pin5(BUS2), .pin6(BUS1), .pin7(BUS0), .pin8(1'b0),
    .pin10(RES), .pin11(GCLK), .pin12(T0), .pin13(1'b0), .pin14(Fout), .pin15(BUS7), .pin16(1'b1));  // open: pin9
  LED led_3 (.in(D5));
  D_FF d_ff_2 (.D(d_ff_2_nq), .C(button_5_out), .Q(D5), .nQ(d_ff_2_nq));
  Button button_5 (.out(button_5_out));
  LED led_4 (.in(D4));
  D_FF d_ff_3 (.D(d_ff_3_nq), .C(button_6_out), .Q(D4), .nQ(d_ff_3_nq));
  Button button_6 (.out(button_6_out));
  LED led_5 (.in(D3));
  D_FF d_ff_4 (.D(d_ff_4_nq), .C(button_7_out), .Q(D3), .nQ(d_ff_4_nq));
  Button button_7 (.out(button_7_out));
  LED led_6 (.in(D2));
  D_FF d_ff_5 (.D(d_ff_5_nq), .C(button_8_out), .Q(D2), .nQ(d_ff_5_nq));
  Button button_8 (.out(button_8_out));
  Seven_Seg_Hex seven_seg_hex_3 (.d({BUS7, BUS6, BUS5, BUS4}), .dp(1'b0));
  DiodeForward diodeforward_1 (.in(BUS7), .out(diodeforward_1_out));
  DiodeForward diodeforward_2 (.in(BUS6), .out(diodeforward_1_out));
  DiodeForward diodeforward_3 (.in(BUS5), .out(diodeforward_1_out));
  DiodeForward diodeforward_4 (.in(BUS4), .out(diodeforward_1_out));
  DiodeForward diodeforward_5 (.in(BUS3), .out(diodeforward_1_out));
  DiodeForward diodeforward_6 (.in(BUS2), .out(diodeforward_1_out));
  DiodeForward diodeforward_7 (.in(BUS1), .out(diodeforward_1_out));
  DiodeForward diodeforward_8 (.in(BUS0), .out(diodeforward_1_out));
  LED led_7 (.in(D1));
  D_FF d_ff_6 (.D(d_ff_6_nq), .C(button_9_out), .Q(D1), .nQ(d_ff_6_nq));
  Button button_9 (.out(button_9_out));
  Seven_Seg_Hex seven_seg_hex_4 (.d({BUS3, BUS2, BUS1, BUS0}), .dp(1'b0));
  PullDown pulldown_1 (.out(diodeforward_1_out));
  LED led_8 (.in(D0));
  D_FF IC16_2 (.D(IC16_2_nq), .C(button_10_out), .Q(D0), .nQ(IC16_2_nq));
  Button button_10 (.out(button_10_out));
  nand nand_1 (ZERO, diodeforward_1_out, diodeforward_1_out);
  Seven_Seg_Hex seven_seg_hex_5 (.d({D7, D6, D5, D4}), .dp(1'b0));
  LED led_9 (.in(ZERO));
  Seven_Seg_Hex seven_seg_hex_6 (.d({D3, D2, D1, D0}), .dp(1'b0));
  nand nand_2 (nand_2_out, clk, clk);
  nand nand_3 (RST, RES, nRST);
  nand nand_4 (nRST, RST, T0);
  // _28c16 U1: pin names not known; wires that end beside it: Ain, Bin, Cin, SETC, LD_t, I6, I5, I4, Cout, ResC, CtoFF, 1'b0, 1'b1, 1'b0, 1'b0, 1'b1, 1'b0, 1'b0, 1'b0
  nand nand_5 (GCLK, nand_2_out, RST);
  _74161 U7 (
    .pin1(RST), .pin2(clk), .pin3(1'b0), .pin4(1'b0), .pin5(1'b0), .pin6(1'b0), .pin7(1'b1), .pin8(1'b0),
    .pin9(1'b1), .pin10(1'b1), .pin11(U7_pin11[3]), .pin12(U7_pin11[2]), .pin13(U7_pin11[1]),
    .pin14(U7_pin11[0]), .pin15(U7_pin15), .pin16(1'b1));
  LED led_10 (.in(Cin));
  _7474 U2 (
    .pin1(ResC), .pin2(Cout), .pin3(GCLK), .pin4(CtoFF), .pin5(Cin), .pin7(1'b0), .pin8(T0), .pin9(IX),
    .pin10(1'b1), .pin11(clk), .pin12(RCO), .pin13(1'b1), .pin14(1'b1));  // open: pin6
  Seven_Seg_Hex seven_seg_hex_7 (.d(U7_pin11), .dp(1'b0));
  and and_1 (RCO, U7_pin11[2], U7_pin11[1], U7_pin11[0]);
  and and_2 (nCE, LD, T0, nRST);

  // Other names for the same wires on the sheet: IR4 = I4; IR5 = I5; IR6 = I6; nLOAD = LD; nRES = RES; SetC_t = CtoFF

  // Notes on the sheet:
  //   clk: Hz: 2147483647
  //   8-bit Shift Register B
  //   Instruction Input
  //   STEP/RUN
  //   ACCUMULATOR
  //   CLR PC
  //   Shift Register A
  //   Output Display Register
  //   ENTER L
  //   OUTPUT REGISTER
  //   ZERO
  //   ALU
  //   U6
  //   ALU PROM
  //   Clock Sequencer
  //   Carry is only set before Bit 0 of an operation
  //   Any residual carry is cleared before an operation
  //   MITE 8-bit  Bit serial CPU Testbed
  //   CARRY
  //   Carry FF
  //   # Clock
endmodule
