// Digital circuit mite_1.dig as structural Verilog
module mite_1 (
  input  clk,
  input  in_2,
  input  in_3,
  input  in_4,
  input  nRES_COUNT,
  input  JMP,
  output LD,
  output RES,
  output GCLK,
  output T0,
  output nRST,
  output nCE
);

  wire A0, A1, A2, A3, A4, A5, A6, A7, A8, A9, A10, A11, A12, A13, A14, A15, AC0, AC1, AC2, AC3, AC4, AC5,
       AC6, AC7, ADD, AND, Aout, Bout, BUS0, BUS1, BUS2, BUS3, BUS4, BUS5, BUS6, BUS7, BUS8, BUS9, BUS10,
       BUS11, BUS12, BUS13, BUS14, BUS15, button_1_out, button_2_out, button_3_out, button_4_out,
       button_5_out, button_6_out, button_7_out, button_8_out, button_9_out, button_10_out, button_11_out,
       button_12_out, button_13_out, button_14_out, button_15_out, button_16_out, button_17_out,
       button_18_out, C, Cin, CLA, CLR, Cout, D0, D1, D2, D3, D4, D5, D6, D7, D8, D9, D10, D11, D12, D13,
       D14, D15, d_ff_1_nq, d_ff_2_nq, d_ff_3_nq, d_ff_4_nq, d_ff_5_nq, d_ff_6_nq, d_ff_7_nq, d_ff_8_nq,
       d_ff_9_nq, d_ff_10_nq, d_ff_11_nq, d_ff_12_nq, diodebackward_1_out, diodebackward_2_out,
       diodebackward_8_out, diodebackward_9_out, diodeforward_1_out, F, Fout, I0, I1, IC16_2_nq, IC16_nq,
       IC17_2_nq, IC17_nq, IX, LD_t, LOAD, nA, nand_1_out, nand_2_out, nand_3_out, nand_6_out, nand_7_out,
       nand_9_out, nand_12_out, nand_14_out, nand_15_out, nand_16_out, nand_17_out, nand_18_out, nand_19_out,
       nB, nCLRPC, nJMP, OR, PC_Cin, PCin, PCout, pullup_2_out, pullup_4_out, pullup_7_out, RCO, RST, SETC,
       ST, SUB, U7_pin15, XOR, xor_1_out, xor_2_out, xor_3_out, xor_4_out, xor_5_out, xor_6_out, xor_7_out,
       xor_8_out, ZERO;
  wire [3:0] U6_pin6, U7_pin11;
  wire [3:1] U6_pin10;

  // _27C1024 U24: pin names not known; wires that end beside it: 1'b1, 1'b0, BUS15, BUS14, BUS13, BUS12, BUS11, BUS10, BUS9, BUS8, 1'b0, BUS7, BUS6, BUS5, BUS4, BUS3, 1'b1, A15, A14, A13, A12, A11, A10, A9
  nand nand_1 (nand_1_out, PCout, PC_Cin);
  xor xor_1 (xor_1_out, PCout, PC_Cin);
  xor xor_2 (xor_2_out, JMP, 1'b1);
  xor xor_3 (xor_3_out, nand_1_out, 1'b1);
  xor xor_4 (xor_4_out, nRES_COUNT, xor_2_out);
  nand nand_2 (nand_2_out, xor_1_out, xor_4_out);
  nand nand_3 (nand_3_out, xor_2_out, Bout);
  nand nand_4 (PCin, nand_2_out, nand_3_out);
  Seven_Seg_Hex seven_seg_hex_1 (.d({A15, A14, A13, A12}), .dp(1'b0));
  Seven_Seg_Hex seven_seg_hex_2 (.d({A11, A10, A8, A9}), .dp(1'b0));
  _74595 U23 (
    .pin1(A14), .pin2(A13), .pin3(A12), .pin4(A11), .pin5(A10), .pin6(A9), .pin7(A8), .pin8(1'b0),
    .pin10(1'b0), .pin11(GCLK), .pin12(T0), .pin13(1'b0), .pin14(PCin), .pin15(A15), .pin16(1'b1));  // open: pin9
  _74595 U22 (
    .pin1(A6), .pin2(A5), .pin3(A4), .pin4(A3), .pin5(A2), .pin6(A1), .pin7(A0), .pin8(1'b0), .pin9(PCout),
    .pin10(nCLRPC), .pin11(GCLK), .pin12(T0), .pin13(1'b0), .pin14(PCin), .pin15(A7), .pin16(1'b1));
  _7474 U29 (
    .pin1(1'b1), .pin2(xor_3_out), .pin3(GCLK), .pin4(LD), .pin5(PC_Cin), .pin7(1'b0), .pin10(1'b1),
    .pin11(1'b1), .pin12(1'b1), .pin13(1'b1), .pin14(1'b1));  // open: pin6, pin8, pin9
  Seven_Seg_Hex seven_seg_hex_3 (.d({A7, A6, A5, A4}), .dp(1'b0));
  Seven_Seg_Hex seven_seg_hex_4 (.d({A3, A2, A1, A0}), .dp(1'b0));
  Seven_Seg_Hex seven_seg_hex_5 (.d({BUS15, BUS14, BUS13, BUS12}), .dp(1'b0));
  Seven_Seg_Hex seven_seg_hex_6 (.d({BUS11, BUS10, BUS9, BUS8}), .dp(1'b0));
  _74138 U1 (
    .pin1(in_2), .pin2(in_3), .pin3(in_4), .pin4(1'b0), .pin5(1'b0), .pin6(1'b1), .pin7(nJMP), .pin8(1'b0),
    .pin9(ST), .pin10(SUB), .pin11(ADD), .pin12(XOR), .pin13(OR), .pin14(AND), .pin15(LOAD), .pin16(1'b1));
  Monoflop monoflop_1 (.C(LD), .R(1'b0), .Q(SETC), .nQ(RES));
  Monoflop monoflop_2 (.C(button_1_out), .R(1'b0), .Q(LD_t), .nQ(LD));
  Button button_1 (.out(button_1_out));
  Seven_Seg_Hex seven_seg_hex_7 (.d({BUS7, BUS6, BUS5, BUS4}), .dp(1'b0));
  DiodeBackward diodebackward_1 (.in(LOAD), .out(diodebackward_1_out));
  Monoflop monoflop_3 (.C(button_2_out), .R(1'b0), .nQ(nCLRPC));  // open: Q
  Button button_2 (.out(button_2_out));
  Seven_Seg_Hex seven_seg_hex_8 (.d({BUS3, BUS2, BUS1, BUS0}), .dp(1'b0));
  PullUp pullup_1 (.out(diodebackward_1_out));
  DiodeBackward diodebackward_2 (.in(LOAD), .out(diodebackward_2_out));
  DiodeBackward diodebackward_3 (.in(ADD), .out(diodebackward_2_out));
  DiodeBackward diodebackward_4 (.in(SUB), .out(diodebackward_2_out));
  DiodeBackward diodebackward_5 (.in(nJMP), .out(diodebackward_2_out));
  PullUp pullup_2 (.out(pullup_2_out));
  PullUp pullup_3 (.out(diodebackward_2_out));
  DiodeBackward diodebackward_6 (.in(SUB), .out(pullup_2_out));
  PullUp pullup_4 (.out(pullup_4_out));
  DiodeBackward diodebackward_7 (.in(SUB), .out(pullup_4_out));
  DiodeBackward diodebackward_8 (.in(nJMP), .out(diodebackward_8_out));
  PullUp pullup_5 (.out(diodebackward_8_out));
  DiodeBackward diodebackward_9 (.in(AND), .out(diodebackward_9_out));
  DiodeBackward diodebackward_10 (.in(OR), .out(diodebackward_9_out));
  _74165 U3 (
    .pin1(LD), .pin2(GCLK), .pin3(D3), .pin4(D2), .pin5(D1), .pin6(D0), .pin8(1'b0), .pin9(Bout),
    .pin10(1'b0), .pin11(D7), .pin12(D6), .pin13(D5), .pin14(D4), .pin15(1'b0), .pin16(1'b1));  // open: pin7
  PullUp pullup_6 (.out(diodebackward_9_out));
  PullUp pullup_7 (.out(pullup_7_out));
  DiodeBackward diodebackward_11 (.in(LOAD), .out(pullup_7_out));
  DiodeBackward diodebackward_12 (.in(OR), .out(pullup_7_out));
  DiodeBackward diodebackward_13 (.in(XOR), .out(pullup_7_out));
  DiodeBackward diodebackward_14 (.in(ADD), .out(pullup_7_out));
  DiodeBackward diodebackward_15 (.in(SUB), .out(pullup_7_out));
  DiodeBackward diodebackward_16 (.in(ST), .out(pullup_7_out));
  DiodeBackward diodebackward_17 (.in(nJMP), .out(pullup_7_out));
  _74540 U2 (
    .pin1(1'b0), .pin2(pullup_7_out), .pin3(diodebackward_9_out), .pin4(diodebackward_8_out),
    .pin5(pullup_4_out), .pin6(pullup_2_out), .pin7(diodebackward_2_out), .pin8(diodebackward_1_out),
    .pin9(1'b0), .pin10(1'b0), .pin12(CLA), .pin13(F), .pin14(C), .pin15(nB), .pin16(nA), .pin17(I1),
    .pin18(I0), .pin19(1'b0), .pin20(1'b1));  // open: pin11
  LED led_1 (.in(D15));
  D_FF IC17 (.D(IC17_nq), .C(button_3_out), .Q(D15), .nQ(IC17_nq));
  LED led_2 (.in(D14));
  D_FF d_ff_1 (.D(d_ff_1_nq), .C(button_4_out), .Q(D14), .nQ(d_ff_1_nq));
  Button button_3 (.out(button_3_out));
  LED led_3 (.in(D13));
  D_FF d_ff_2 (.D(d_ff_2_nq), .C(button_5_out), .Q(D13), .nQ(d_ff_2_nq));
  Button button_4 (.out(button_4_out));
  LED led_4 (.in(D12));
  D_FF d_ff_3 (.D(d_ff_3_nq), .C(button_6_out), .Q(D12), .nQ(d_ff_3_nq));
  Button button_5 (.out(button_5_out));
  _74595 U4 (
    .pin1(AC6), .pin2(AC5), .pin3(AC4), .pin4(AC3), .pin5(AC2), .pin6(AC1), .pin7(AC0), .pin8(1'b0),
    .pin10(RES), .pin11(GCLK), .pin12(T0), .pin13(1'b0), .pin14(Fout), .pin15(AC7), .pin16(1'b1));  // open: pin9
  LED led_5 (.in(D11));
  D_FF d_ff_4 (.D(d_ff_4_nq), .C(button_7_out), .Q(D11), .nQ(d_ff_4_nq));
  Button button_6 (.out(button_6_out));
  LED led_6 (.in(D10));
  D_FF d_ff_5 (.D(d_ff_5_nq), .C(button_8_out), .Q(D10), .nQ(d_ff_5_nq));
  Button button_7 (.out(button_7_out));
  LED led_7 (.in(D9));
  D_FF d_ff_6 (.D(d_ff_6_nq), .C(button_9_out), .Q(D9), .nQ(d_ff_6_nq));
  Button button_8 (.out(button_8_out));
  LED led_8 (.in(D8));
  D_FF IC17_2 (.D(IC17_2_nq), .C(button_10_out), .Q(D8), .nQ(IC17_2_nq));
  Button button_9 (.out(button_9_out));
  Seven_Seg_Hex seven_seg_hex_9 (.d({D15, D14, D13, D12}), .dp(1'b0));
  Button button_10 (.out(button_10_out));
  DiodeForward diodeforward_1 (.in(AC7), .out(diodeforward_1_out));
  DiodeForward diodeforward_2 (.in(AC6), .out(diodeforward_1_out));
  DiodeForward diodeforward_3 (.in(AC5), .out(diodeforward_1_out));
  DiodeForward diodeforward_4 (.in(AC4), .out(diodeforward_1_out));
  DiodeForward diodeforward_5 (.in(AC3), .out(diodeforward_1_out));
  DiodeForward diodeforward_6 (.in(AC2), .out(diodeforward_1_out));
  DiodeForward diodeforward_7 (.in(AC1), .out(diodeforward_1_out));
  DiodeForward diodeforward_8 (.in(AC0), .out(diodeforward_1_out));
  Seven_Seg_Hex seven_seg_hex_10 (.d({D11, D10, D9, D8}), .dp(1'b0));
  Seven_Seg_Hex seven_seg_hex_11 (.d({AC7, AC6, AC5, AC4}), .dp(1'b0));
  nand nand_5 (ZERO, diodeforward_1_out, diodeforward_1_out);
  PullDown pulldown_1 (.out(diodeforward_1_out));
  LED led_9 (.in(D7));
  D_FF IC16 (.D(IC16_nq), .C(button_11_out), .Q(D7), .nQ(IC16_nq));
  Button button_11 (.out(button_11_out));
  Seven_Seg_Hex seven_seg_hex_12 (.d({AC3, AC2, AC1, AC0}), .dp(1'b0));
  LED led_10 (.in(D6));
  D_FF d_ff_7 (.D(d_ff_7_nq), .C(button_12_out), .Q(D6), .nQ(d_ff_7_nq));
  Button button_12 (.out(button_12_out));
  LED led_11 (.in(ZERO));
  LED led_12 (.in(D5));
  D_FF d_ff_8 (.D(d_ff_8_nq), .C(button_13_out), .Q(D5), .nQ(d_ff_8_nq));
  Button button_13 (.out(button_13_out));
  LED led_13 (.in(D4));
  D_FF d_ff_9 (.D(d_ff_9_nq), .C(button_14_out), .Q(D4), .nQ(d_ff_9_nq));
  Button button_14 (.out(button_14_out));
  LED led_14 (.in(D3));
  D_FF d_ff_10 (.D(d_ff_10_nq), .C(button_15_out), .Q(D3), .nQ(d_ff_10_nq));
  Button button_15 (.out(button_15_out));
  Seven_Seg_Hex seven_seg_hex_13 (.d(U6_pin6), .dp(1'b0));
  LED led_15 (.in(D2));
  D_FF d_ff_11 (.D(d_ff_11_nq), .C(button_16_out), .Q(D2), .nQ(d_ff_11_nq));
  Button button_16 (.out(button_16_out));
  Seven_Seg_Hex seven_seg_hex_14 (.d({U6_pin10, Aout}), .dp(1'b0));
  _74164 U6 (
    .pin1(1'b1), .pin2(Fout), .pin3(U6_pin6[3]), .pin4(U6_pin6[2]), .pin5(U6_pin6[1]), .pin6(U6_pin6[0]),
    .pin7(1'b0), .pin8(GCLK), .pin9(CLR), .pin10(U6_pin10[3]), .pin11(U6_pin10[2]), .pin12(U6_pin10[1]),
    .pin13(Aout), .pin14(1'b1));
  LED led_16 (.in(D1));
  D_FF d_ff_12 (.D(d_ff_12_nq), .C(button_17_out), .Q(D1), .nQ(d_ff_12_nq));
  Button button_17 (.out(button_17_out));
  LED led_17 (.in(D0));
  D_FF IC16_2 (.D(IC16_2_nq), .C(button_18_out), .Q(D0), .nQ(IC16_2_nq));
  Button button_18 (.out(button_18_out));
  Seven_Seg_Hex seven_seg_hex_15 (.d({D7, D6, D5, D4}), .dp(1'b0));
  Seven_Seg_Hex seven_seg_hex_16 (.d({D3, D2, D1, D0}), .dp(1'b0));
  xor xor_5 (xor_5_out, Aout, nA);
  xor xor_6 (xor_6_out, nB, Bout);
  nand nand_6 (nand_6_out, SETC, C);
  nand nand_7 (nand_7_out, C, C);
  nand nand_8 (CLR, CLA, LD_t);
  nand nand_9 (nand_9_out, clk, clk);
  nand nand_10 (RST, RES, nRST);
  nand nand_11 (nRST, RST, T0);
  xor xor_7 (xor_7_out, xor_5_out, xor_6_out);
  nand nand_12 (nand_12_out, nand_7_out, LD_t);
  nand nand_13 (GCLK, nand_9_out, RST);
  xor xor_8 (xor_8_out, xor_7_out, Cin);
  nand nand_14 (nand_14_out, xor_7_out, Cin);
  nand nand_15 (nand_15_out, xor_5_out, xor_6_out);
  _74161 U7 (
    .pin1(RST), .pin2(clk), .pin3(1'b0), .pin4(1'b0), .pin5(1'b0), .pin6(1'b0), .pin7(1'b1), .pin8(1'b0),
    .pin9(1'b1), .pin10(1'b1), .pin11(U7_pin11[3]), .pin12(U7_pin11[2]), .pin13(U7_pin11[1]),
    .pin14(U7_pin11[0]), .pin15(U7_pin15), .pin16(1'b1));
  nand nand_16 (nand_16_out, nand_14_out, nand_15_out);
  nand nand_17 (nand_17_out, xor_8_out, I0);
  nand nand_18 (nand_18_out, I1, nand_16_out);
  nand nand_19 (nand_19_out, nand_16_out, F);
  and and_1 (nCE, LD, T0, nRST);
  Seven_Seg_Hex seven_seg_hex_17 (.d(U7_pin11), .dp(1'b0));
  and and_2 (RCO, U7_pin11[2], U7_pin11[1], U7_pin11[0]);
  nand nand_20 (Fout, nand_17_out, nand_18_out);
  nand nand_21 (Cout, nand_19_out, nand_19_out);
  _7474 U12 (
    .pin1(nand_12_out), .pin2(Cout), .pin3(GCLK), .pin4(nand_6_out), .pin5(Cin), .pin7(1'b0), .pin8(T0),
    .pin9(IX), .pin10(1'b1), .pin11(clk), .pin12(RCO), .pin13(1'b1), .pin14(1'b1));  // open: pin6
  LED led_18 (.in(Cin));

  // Other names for the same wires on the sheet: nLD = LD; nLOAD = LD; nR = T0; nRES = RES; nRRES = nCLRPC

  // Notes on the sheet:
  //   clk: Hz: 4
  //   nRES_COUNT: default 1
  //   JMP: default 1
  //   ROM and Serial PC
  //   Carry is only set before Bit 0 of an operation
  //   U28A
  //   U27A
  //   U27D
  //   16-bit ROM
  //   U27C
  //   U27B
  //   U28C
  //   U28B
  //   U28D
  //   PROGRAM COUNTER
  //   PC Carry FF
  //   Program Counter
  //   MITE
  //   Instruction Input
  //   INSTR
  //   STEP/RUN
  //   BUS
  //   CLR PC
  //   Instruction Decode
  //   CLA
  //   C
  //   F
  //   8-bit Shift Register B
  //   ~B
  //   ~A
  //   I0
  //   I1
  //   LOAD
  //   AND
  //   OR
  //   XOR
  //   ADD
  //   SUB
  //   STORE
  //   JMP
  //   Output Display Register
  //   ENTER H
  //   Data Input
  //   OUTPUT REGISTER
  //   ZERO
  //   ENTER L
  //   ACCUMULATOR
  //   Shift Register A
  //   U5
  //   ALU
  //   CLR ACC
  //   MITE 8-bit  Bit serial CPU Testbed
  //   Clock Sequencer
  //   Any residual carry is cleared before an operation
  //   Suppress Carry
  //   # Clock
  //   Carry FF
  //   CARRY
endmodule
