// Digital circuit mite_14.dig as structural Verilog
module mite_14 (
  input  in_1,
  input  in_2,
  input  clk,
  output T0,
  output T8,
  output LD,
  output GCLK,
  output SETC,
  output GATE,
  output CLR,
  output Fout,
  output CtoFF,
  output ResC,
  output Cout
);

  wire A0, A1, A2, A3, A4, A5, A6, A7, A8, ADD, AND, Aout, Bout, BUS0, BUS1, BUS2, BUS3, BUS4, BUS5, BUS6,
       BUS7, Cin, D0, D1, D2, D3, D4, D5, D6, D7, diodebackward_1_out, diodeforward_1_out, IR0, IR1, IR2,
       IR3, IR4, IR5, IR6, IR7, LD_t, LOAD, MA0, MA1, MA2, MA3, MA4, MA5, MA6, MA7, MA8, MA9, MA10, MA11,
       MA12, MA13, MA14, MA15, nCLRAC, nCTRLD, nJMP, nor_2_out, not_1_out, not_2_out, not_5_out, not_6_out,
       not_7_out, not_8_out, not_9_out, not_10_out, not_11_out, not_12_out, OR, RCO, ST, SUB, T2, T3, T4, T5,
       T6, T7, T8_t, T9, U4_pin9, U5_pin9, WRRAM, XOR, ZERO;
  wire [3:0] U14_pin3;
  wire [3:1] U14_pin12;

  Seven_Seg_Hex seven_seg_hex_1 (.d({4{A8}}), .dp(1'b0));
  Seven_Seg_Hex seven_seg_hex_2 (.d({MA15, MA14, MA13, MA12}), .dp(1'b0));
  Seven_Seg_Hex seven_seg_hex_3 (.d({4{A8}}), .dp(1'b0));
  Seven_Seg_Hex seven_seg_hex_4 (.d({MA11, MA10, MA9, MA8}), .dp(1'b0));
  Seven_Seg_Hex seven_seg_hex_5 (.d({A7, A6, A5, A4}), .dp(1'b0));
  Seven_Seg_Hex seven_seg_hex_6 (.d({MA7, MA6, MA5, MA4}), .dp(1'b0));
  Seven_Seg_Hex seven_seg_hex_7 (.d({A3, A2, A1, A0}), .dp(1'b0));
  Seven_Seg_Hex seven_seg_hex_8 (.d({MA3, MA2, MA1, MA0}), .dp(1'b0));
  Seven_Seg_Hex seven_seg_hex_9 (.d({D7, D6, D5, D4}), .dp(1'b0));
  Seven_Seg_Hex seven_seg_hex_10 (.d({BUS7, BUS6, BUS5, BUS4}), .dp(1'b0));
  Seven_Seg_Hex seven_seg_hex_11 (.d({D3, D2, D1, D0}), .dp(1'b0));
  Seven_Seg_Hex seven_seg_hex_12 (.d({BUS3, BUS2, BUS1, BUS0}), .dp(1'b0));
  Seven_Seg_Hex seven_seg_hex_13 (.d({IR7, IR6, IR5, IR4}), .dp(1'b0));
  not not_1 (not_1_out, WRRAM);
  not not_2 (not_2_out, in_2);
  Seven_Seg_Hex seven_seg_hex_14 (.d({IR3, IR2, IR1, IR0}), .dp(1'b0));
  LED led_1 (.in(LD_t));
  LED led_2 (.in(SETC));
  LED led_3 (.in(T2));
  LED led_4 (.in(T3));
  LED led_5 (.in(T4));
  LED led_6 (.in(T5));
  LED led_7 (.in(T6));
  LED led_8 (.in(T7));
  LED led_9 (.in(T8_t));
  LED led_10 (.in(T9));
  LED led_11 (.in(not_1_out));
  LED led_12 (.in(not_2_out));
  _74161 U8 (
    .pin1(nCLRAC), .pin2(T8), .pin3(BUS0), .pin4(BUS1), .pin5(BUS2), .pin6(BUS3), .pin7(1'b1), .pin8(1'b0),
    .pin9(nCTRLD), .pin10(1'b1), .pin11(A3), .pin12(A2), .pin13(A1), .pin14(A0), .pin15(RCO), .pin16(1'b1));
  _74161 U9 (
    .pin1(nCLRAC), .pin2(T8), .pin3(BUS4), .pin4(BUS5), .pin5(BUS6), .pin6(BUS7), .pin7(1'b1), .pin8(1'b0),
    .pin9(nCTRLD), .pin10(RCO), .pin11(A7), .pin12(A6), .pin13(A5), .pin14(A4), .pin16(1'b1));  // open: pin15
  // _62256 U10: pin names not known; wires that end beside it: MA14, MA12, MA7, MA6, MA5, MA4, MA3, MA2, MA1, MA0, BUS0, BUS1, BUS2, 1'b0, 1'b1, WRRAM, MA13, MA8, MA9, MA11, in_2, MA10, 1'b0, BUS7
  _74595 U4 (
    .pin1(BUS6), .pin2(BUS5), .pin3(BUS4), .pin4(BUS3), .pin5(BUS2), .pin6(BUS1), .pin7(BUS0), .pin8(1'b0),
    .pin9(U4_pin9), .pin10(nCLRAC), .pin11(GCLK), .pin12(T8), .pin13(1'b0), .pin14(Fout), .pin15(BUS7),
    .pin16(1'b1));
  Reset reset_1 (.out(nCLRAC));
  Seven_Seg_Hex seven_seg_hex_15 (.d({BUS7, BUS6, BUS5, BUS4}), .dp(1'b0));
  Seven_Seg_Hex seven_seg_hex_16 (.d({BUS3, BUS2, BUS1, BUS0}), .dp(1'b0));
  // _27C1024 U7: pin names not known; wires that end beside it: A8, A8, A8, A8, A8, A8, A8, 1'b1, D3, D4, D5, D6, D7, 1'b0, IR0, IR1, IR2, IR3, IR4, IR5, IR6, IR7, 1'b0, 1'b1
  _74165 U3 (
    .pin1(LD), .pin2(GCLK), .pin3(D3), .pin4(D2), .pin5(D1), .pin6(D0), .pin8(1'b0), .pin9(Bout),
    .pin10(1'b0), .pin11(D7), .pin12(D6), .pin13(D5), .pin14(D4), .pin15(1'b0), .pin16(1'b1));  // open: pin7
  _74595 U5 (
    .pin1(MA14), .pin2(MA13), .pin3(MA12), .pin4(MA11), .pin5(MA10), .pin6(MA9), .pin7(MA8), .pin8(1'b0),
    .pin9(U5_pin9), .pin10(nCLRAC), .pin11(GCLK), .pin12(T8), .pin13(1'b0), .pin14(U4_pin9), .pin15(MA15),
    .pin16(1'b1));
  _74541 U12 (
    .pin1(in_1), .pin2(D0), .pin3(D1), .pin4(D2), .pin5(D3), .pin6(D4), .pin7(D5), .pin8(D6), .pin9(D7),
    .pin10(1'b0), .pin11(BUS7), .pin12(BUS6), .pin13(BUS5), .pin14(BUS4), .pin15(BUS3), .pin16(BUS2),
    .pin17(BUS1), .pin18(BUS0), .pin19(in_1), .pin20(1'b1));
  DiodeBackward diodebackward_1 (.in(IR4), .out(diodebackward_1_out));
  DiodeBackward diodebackward_2 (.in(IR5), .out(diodebackward_1_out));
  DiodeBackward diodebackward_3 (.in(IR6), .out(diodebackward_1_out));
  PullDown pulldown_1 (.out(A8));
  PullUp pullup_1 (.out(diodebackward_1_out));
  LED led_13 (.in(diodebackward_1_out));
  Seven_Seg_Hex seven_seg_hex_17 (.d({MA15, MA14, MA13, MA12}), .dp(1'b0));
  not not_3 (LD, LD_t);
  not not_4 (T8, T8_t);
  Seven_Seg_Hex seven_seg_hex_18 (.d({MA11, MA10, MA9, MA8}), .dp(1'b0));
  nor nor_1 (GATE, SETC, nor_2_out);
  nor nor_2 (nor_2_out, GATE, T9);
  _74595 U6 (
    .pin1(MA6), .pin2(MA5), .pin3(MA4), .pin4(MA3), .pin5(MA2), .pin6(MA1), .pin7(MA0), .pin8(1'b0),
    .pin10(nCLRAC), .pin11(GCLK), .pin12(T8), .pin13(1'b0), .pin14(U5_pin9), .pin15(MA7), .pin16(1'b1));  // open: pin9
  // _28c16 U11: pin names not known; wires that end beside it: Aout, Bout, Cin, SETC, LD_t, IR6, IR5, IR4, Cout, ResC, CtoFF, 1'b0, 1'b1, 1'b0, 1'b0, 1'b1, 1'b0, 1'b0, 1'b0
  or or_1 (GCLK, GATE, clk);
  or or_2 (nCTRLD, T8, nJMP);
  or or_3 (WRRAM, T8, ST);
  Seven_Seg_Hex seven_seg_hex_19 (.d({MA7, MA6, MA5, MA4}), .dp(1'b0));
  Seven_Seg_Hex seven_seg_hex_20 (.d({MA3, MA2, MA1, MA0}), .dp(1'b0));
  _74138 U1 (
    .pin1(IR4), .pin2(IR5), .pin3(IR6), .pin4(1'b0), .pin5(1'b0), .pin6(1'b1), .pin7(nJMP), .pin8(1'b0),
    .pin9(ST), .pin10(SUB), .pin11(ADD), .pin12(XOR), .pin13(OR), .pin14(AND), .pin15(LOAD), .pin16(1'b1));
  Seven_Seg_Hex seven_seg_hex_21 (.d(U14_pin3), .dp(1'b0));
  Seven_Seg_Hex seven_seg_hex_22 (.d({U14_pin12, Aout}), .dp(1'b0));
  _74164 U14 (
    .pin1(1'b1), .pin2(Fout), .pin3(U14_pin3[3]), .pin4(U14_pin3[2]), .pin5(U14_pin3[1]), .pin6(U14_pin3[0]),
    .pin7(1'b0), .pin8(GCLK), .pin9(CLR), .pin10(U14_pin12[3]), .pin11(U14_pin12[2]), .pin12(U14_pin12[1]),
    .pin13(Aout), .pin14(1'b1));
  _744017 U16 (
    .pin1(T5), .pin2(SETC), .pin3(LD_t), .pin4(T2), .pin5(T6), .pin6(T7), .pin7(T3), .pin8(1'b0),
    .pin9(T8_t), .pin10(T4), .pin11(T9), .pin13(1'b0), .pin14(clk), .pin15(1'b0), .pin16(1'b1));  // open: pin12
  _7474 U13 (
    .pin1(ResC), .pin2(Cout), .pin3(GCLK), .pin4(CtoFF), .pin5(Cin), .pin7(1'b0), .pin10(1'b1), .pin11(clk),
    .pin12(RCO), .pin13(1'b1), .pin14(1'b1));  // open: pin6, pin8, pin9
  LED led_14 (.in(Cin));
  DiodeForward diodeforward_1 (.in(BUS7), .out(diodeforward_1_out));
  DiodeForward diodeforward_2 (.in(BUS6), .out(diodeforward_1_out));
  DiodeForward diodeforward_3 (.in(BUS5), .out(diodeforward_1_out));
  DiodeForward diodeforward_4 (.in(BUS4), .out(diodeforward_1_out));
  DiodeForward diodeforward_5 (.in(BUS3), .out(diodeforward_1_out));
  DiodeForward diodeforward_6 (.in(BUS2), .out(diodeforward_1_out));
  DiodeForward diodeforward_7 (.in(BUS1), .out(diodeforward_1_out));
  DiodeForward diodeforward_8 (.in(BUS0), .out(diodeforward_1_out));
  PullDown pulldown_2 (.out(diodeforward_1_out));
  not not_5 (not_5_out, LOAD);
  not not_6 (not_6_out, AND);
  not not_7 (not_7_out, OR);
  not not_8 (not_8_out, XOR);
  not not_9 (not_9_out, ADD);
  not not_10 (not_10_out, SUB);
  not not_11 (not_11_out, ST);
  not not_12 (not_12_out, nJMP);
  LED led_15 (.in(ZERO));
  not not_13 (ZERO, diodeforward_1_out);
  LED led_16 (.in(not_5_out));
  LED led_17 (.in(not_6_out));
  LED led_18 (.in(not_7_out));
  LED led_19 (.in(not_8_out));
  LED led_20 (.in(not_9_out));
  LED led_21 (.in(not_10_out));
  LED led_22 (.in(not_11_out));
  LED led_23 (.in(not_12_out));

  assign T0 = LD;

  // Other names for the same wires on the sheet: A9 = A8; A10 = A8; A11 = A8; A12 = A8; A13 = A8; A14 = A8; A15 = A8;
  //   nDE = in_1; nLOAD = LD; nRESET = nCLRAC; R0 = D0; R1 = D1; R2 = D2; R3 = D3; R4 = D4; R5 = D5; R6 = D6; R7 = D7;
  //   R8 = IR0; R9 = IR1; R10 = IR2; R11 = IR3; R12 = IR4; R13 = IR5; R14 = IR6; R15 = IR7; PC_INC = T8; RCLK = T8;
  //   RDRAM = in_2; SetC_t = CtoFF; T0_t = LD_t; T1 = SETC

  // Notes on the sheet:
  //   in_1: default 1
  //   in_2: default 1
  //   clk: Hz: 2
  //   ADDRESS
  //   RAM ADDRESS
  //   U15
  //   DATA BUS
  //   DATA
  //   INSTRUCTION
  //   ~WR
  //   ~RD
  //   ROM & PC
  //   MITE-8
  //   Low Address Counter
  //   RAM
  //   OUTPUT
  //   8-bit Shift Register B
  //   ADDR H
  //   JMP
  //   ALU
  //   U2
  //   Carry is only set before Bit 0 of an operation
  //   Any residual carry is cleared before an operation
  //   ALU PROM
  //   ADDR L
  //   ACCUMULATOR
  //   LOAD
  //   AND
  //   OR
  //   XOR
  //   ADD
  //   SUB
  //   STORE
  //   MITE 8-bit  Bit serial CPU Testbed
  //   Shift Register A
  //   Carry FF
  //   CARRY
  //   ZERO
endmodule
