// Digital circuit mite_2_ROM.dig as structural Verilog
module mite_2_ROM (
  input  clk,
  input  in_2,
  input  in_3,
  input  in_4,
  output LD,
  output RES,
  output GCLK,
  output T0,
  output nRST,
  output nCE
);

  wire ADD, AND, Aout, Bout, BUS0, BUS1, BUS2, BUS3, BUS4, BUS5, BUS6, BUS7, button_1_out, button_2_out,
       button_3_out, button_4_out, button_5_out, button_6_out, button_7_out, button_8_out, button_9_out,
       button_10_out, button_11_out, button_12_out, button_13_out, button_14_out, button_15_out,
       button_16_out, button_17_out, button_18_out, C, Cin, CLA, CLR, Cout, D0, D1, D2, D3, D4, D5, D6, D7,
       D8, D9, D10, D11, D12, D13, D14, D15, d_ff_1_nq, d_ff_2_nq, d_ff_3_nq, d_ff_4_nq, d_ff_5_nq,
       d_ff_6_nq, d_ff_7_nq, d_ff_8_nq, d_ff_9_nq, d_ff_10_nq, d_ff_11_nq, d_ff_12_nq, diodebackward_1_out,
       diodebackward_2_out, diodebackward_8_out, diodebackward_9_out, diodeforward_1_out, F, Fout, I0, I1,
       IC16_2_nq, IC16_nq, IC17_2_nq, IC17_nq, IR0, IR1, IR2, IR3, IR4, IR5, IR6, IR7, IX, L, LD_t, LOAD, nA,
       nand_2_out, nand_3_out, nand_5_out, nand_8_out, nand_10_out, nand_11_out, nand_12_out, nand_13_out,
       nand_14_out, nand_15_out, nB, nCLRPC, nDE, nJMP, nPH, nPL, OR, PC0, PC1, PC2, PC3, PC4, PC5, PC6, PC7,
       PC8, PC9, PC10, PC11, PC12, PC13, PC14, PC15, pullup_1_out, pullup_3_out, pullup_5_out, pullup_8_out,
       RCO, reset_1_out, RST, SETC, ST, SUB, U3_pin2, U3_pin15, U4_pin15, U5_pin15, U7_2_pin15, U7_p9,
       U7_p10, U7_p11, U7_p12, U7_p13, U7_p15, U7_p16, U7_p17, U7_p18, U7_p19, U7_p20, U7_p21, U7_p22,
       U8_pin2, U8_pin3, U8_pin4, XOR, xor_1_out, xor_2_out, xor_3_out, xor_4_out, Y0, Y1, Y2, Y3, Y4, Y5,
       Y6, Y7, ZERO;
  wire [3:0] U6_2_pin6, U7_2_pin11;
  wire [3:1] U6_2_pin10;

  Reset reset_1 (.out(reset_1_out));
  _74163 U3 (
    .pin1(reset_1_out), .pin2(U3_pin2), .pin3(BUS0), .pin4(BUS1), .pin5(BUS2), .pin6(BUS3), .pin7(1'b1),
    .pin8(1'b0), .pin9(nPL), .pin10(1'b1), .pin11(PC3), .pin12(PC2), .pin13(PC1), .pin14(PC0),
    .pin15(U3_pin15), .pin16(1'b1));
  _74163 U4 (
    .pin1(reset_1_out), .pin2(U3_pin2), .pin3(BUS4), .pin4(BUS5), .pin5(BUS6), .pin6(BUS7), .pin7(1'b1),
    .pin8(1'b0), .pin9(nPL), .pin10(U3_pin15), .pin11(PC7), .pin12(PC6), .pin13(PC5), .pin14(PC4),
    .pin15(U4_pin15), .pin16(1'b1));
  _74163 U5 (
    .pin1(reset_1_out), .pin2(U3_pin2), .pin3(Y0), .pin4(Y1), .pin5(Y2), .pin6(Y3), .pin7(1'b1), .pin8(1'b0),
    .pin9(nPH), .pin10(U4_pin15), .pin11(PC11), .pin12(PC10), .pin13(PC9), .pin14(PC8), .pin15(U5_pin15),
    .pin16(1'b1));
  _74163 U6 (
    .pin1(reset_1_out), .pin2(U3_pin2), .pin3(Y4), .pin4(Y5), .pin5(Y6), .pin6(Y7), .pin7(1'b1), .pin8(1'b0),
    .pin9(nPH), .pin10(U5_pin15), .pin11(PC15), .pin12(PC14), .pin13(PC13), .pin14(PC12), .pin16(1'b1));  // open: pin15
  // _27C1024 U7: pin names not known; wires that end beside it: PC9, PC10, PC11, PC12, PC13, PC14, PC15, 1'b1, U7_p9, U7_p10, U7_p11, U7_p12, U7_p13, 1'b0, U7_p15, U7_p16, U7_p17, U7_p18, U7_p19, U7_p20, U7_p21, U7_p22, 1'b0, 1'b1
  PullUp pullup_1 (.out(pullup_1_out));
  _74574 U8 (
    .pin1(pullup_1_out), .pin2(U8_pin2), .pin3(U8_pin3), .pin4(U8_pin4), .pin5(U7_p9), .pin6(U7_p10),
    .pin7(U7_p11), .pin8(U7_p12), .pin9(U7_p13), .pin10(1'b0), .pin11(L), .pin12(IR7), .pin13(IR6),
    .pin14(IR5), .pin15(IR4), .pin16(IR3), .pin17(IR2), .pin18(IR1), .pin19(IR0), .pin20(1'b1));
  _74574 U9 (
    .pin1(1'b0), .pin2(U7_p15), .pin3(U7_p16), .pin4(U7_p17), .pin5(U7_p18), .pin6(U7_p19), .pin7(U7_p20),
    .pin8(U7_p21), .pin9(U7_p22), .pin10(1'b0), .pin11(L), .pin12(D7), .pin13(D6), .pin14(D5), .pin15(D4),
    .pin16(D3), .pin17(D2), .pin18(D1), .pin19(D0), .pin20(1'b1));
  _74541 U10 (
    .pin1(nDE), .pin2(D0), .pin3(D1), .pin4(D2), .pin5(D3), .pin6(D4), .pin7(D5), .pin8(D6), .pin9(D7),
    .pin10(1'b0), .pin11(BUS7), .pin12(BUS6), .pin13(BUS5), .pin14(BUS4), .pin15(BUS3), .pin16(BUS2),
    .pin17(BUS1), .pin18(BUS0), .pin19(nDE), .pin20(1'b1));
  _74138 U1 (
    .pin1(in_2), .pin2(in_3), .pin3(in_4), .pin4(1'b0), .pin5(1'b0), .pin6(1'b1), .pin7(nJMP), .pin8(1'b0),
    .pin9(ST), .pin10(SUB), .pin11(ADD), .pin12(XOR), .pin13(OR), .pin14(AND), .pin15(LOAD), .pin16(1'b1));
  Monoflop monoflop_1 (.C(LD), .R(1'b0), .Q(SETC), .nQ(RES));
  Monoflop monoflop_2 (.C(button_1_out), .R(1'b0), .Q(LD_t), .nQ(LD));
  Button button_1 (.out(button_1_out));
  DiodeBackward diodebackward_1 (.in(LOAD), .out(diodebackward_1_out));
  Monoflop monoflop_3 (.C(button_2_out), .R(1'b0), .nQ(nCLRPC));  // open: Q
  Button button_2 (.out(button_2_out));
  PullUp pullup_2 (.out(diodebackward_1_out));
  DiodeBackward diodebackward_2 (.in(LOAD), .out(diodebackward_2_out));
  DiodeBackward diodebackward_3 (.in(ADD), .out(diodebackward_2_out));
  DiodeBackward diodebackward_4 (.in(SUB), .out(diodebackward_2_out));
  DiodeBackward diodebackward_5 (.in(nJMP), .out(diodebackward_2_out));
  PullUp pullup_3 (.out(pullup_3_out));
  PullUp pullup_4 (.out(diodebackward_2_out));
  DiodeBackward diodebackward_6 (.in(SUB), .out(pullup_3_out));
  _74165 U3_2 (
    .pin1(LD), .pin2(GCLK), .pin3(D3), .pin4(D2), .pin5(D1), .pin6(D0), .pin8(1'b0), .pin9(Bout),
    .pin10(1'b0), .pin11(D7), .pin12(D6), .pin13(D5), .pin14(D4), .pin15(1'b0), .pin16(1'b1));  // open: pin7
  PullUp pullup_5 (.out(pullup_5_out));
  DiodeBackward diodebackward_7 (.in(SUB), .out(pullup_5_out));
  DiodeBackward diodebackward_8 (.in(nJMP), .out(diodebackward_8_out));
  PullUp pullup_6 (.out(diodebackward_8_out));
  DiodeBackward diodebackward_9 (.in(AND), .out(diodebackward_9_out));
  DiodeBackward diodebackward_10 (.in(OR), .out(diodebackward_9_out));
  PullUp pullup_7 (.out(diodebackward_9_out));
  PullUp pullup_8 (.out(pullup_8_out));
  DiodeBackward diodebackward_11 (.in(LOAD), .out(pullup_8_out));
  DiodeBackward diodebackward_12 (.in(OR), .out(pullup_8_out));
  DiodeBackward diodebackward_13 (.in(XOR), .out(pullup_8_out));
  DiodeBackward diodebackward_14 (.in(ADD), .out(pullup_8_out));
  DiodeBackward diodebackward_15 (.in(SUB), .out(pullup_8_out));
  DiodeBackward diodebackward_16 (.in(ST), .out(pullup_8_out));
  DiodeBackward diodebackward_17 (.in(nJMP), .out(pullup_8_out));
  _74540 U2 (
    .pin1(1'b0), .pin2(pullup_8_out), .pin3(diodebackward_9_out), .pin4(diodebackward_8_out),
    .pin5(pullup_5_out), .pin6(pullup_3_out), .pin7(diodebackward_2_out), .pin8(diodebackward_1_out),
    .pin9(1'b0), .pin10(1'b0), .pin12(CLA), .pin13(F), .pin14(C), .pin15(nB), .pin16(nA), .pin17(I1),
    .pin18(I0), .pin19(1'b0), .pin20(1'b1));  // open: pin11
  LED led_1 (.in(D15));
  D_FF IC17 (.D(IC17_nq), .C(button_3_out), .Q(D15), .nQ(IC17_nq));
  LED led_2 (.in(D14));
  D_FF d_ff_1 (.D(d_ff_1_nq), .C(button_4_out), .Q(D14), .nQ(d_ff_1_nq));
  Button button_3 (.out(button_3_out));
  LED led_3 (.in(D13));
  D_FF d_ff_2 (.D(d_ff_2_nq), .C(button_5_out), .Q(D13), .nQ(d_ff_2_nq));
  Button button_4 (.out(button_4_out));
  LED led_4 (.in(D12));
  D_FF d_ff_3 (.D(d_ff_3_nq), .C(button_6_out), .Q(D12), .nQ(d_ff_3_nq));
  Button button_5 (.out(button_5_out));
  _74595 U4_2 (
    .pin1(BUS6), .pin2(BUS5), .pin3(BUS4), .pin4(BUS3), .pin5(BUS2), .pin6(BUS1), .pin7(BUS0), .pin8(1'b0),
    .pin10(RES), .pin11(GCLK), .pin12(T0), .pin13(1'b0), .pin14(Fout), .pin15(BUS7), .pin16(1'b1));  // open: pin9
  LED led_5 (.in(D11));
  D_FF d_ff_4 (.D(d_ff_4_nq), .C(button_7_out), .Q(D11), .nQ(d_ff_4_nq));
  Button button_6 (.out(button_6_out));
  LED led_6 (.in(D10));
  D_FF d_ff_5 (.D(d_ff_5_nq), .C(button_8_out), .Q(D10), .nQ(d_ff_5_nq));
  Button button_7 (.out(button_7_out));
  LED led_7 (.in(D9));
  D_FF d_ff_6 (.D(d_ff_6_nq), .C(button_9_out), .Q(D9), .nQ(d_ff_6_nq));
  Button button_8 (.out(button_8_out));
  LED led_8 (.in(D8));
  D_FF IC17_2 (.D(IC17_2_nq), .C(button_10_out), .Q(D8), .nQ(IC17_2_nq));
  Button button_9 (.out(button_9_out));
  Seven_Seg_Hex seven_seg_hex_1 (.d({D15, D14, D13, D12}), .dp(1'b0));
  Button button_10 (.out(button_10_out));
  DiodeForward diodeforward_1 (.in(BUS7), .out(diodeforward_1_out));
  DiodeForward diodeforward_2 (.in(BUS6), .out(diodeforward_1_out));
  DiodeForward diodeforward_3 (.in(BUS5), .out(diodeforward_1_out));
  DiodeForward diodeforward_4 (.in(BUS4), .out(diodeforward_1_out));
  DiodeForward diodeforward_5 (.in(BUS3), .out(diodeforward_1_out));
  DiodeForward diodeforward_6 (.in(BUS2), .out(diodeforward_1_out));
  DiodeForward diodeforward_7 (.in(BUS1), .out(diodeforward_1_out));
  DiodeForward diodeforward_8 (.in(BUS0), .out(diodeforward_1_out));
  Seven_Seg_Hex seven_seg_hex_2 (.d({D11, D10, D9, D8}), .dp(1'b0));
  Seven_Seg_Hex seven_seg_hex_3 (.d({BUS7, BUS6, BUS5, BUS4}), .dp(1'b0));
  nand nand_1 (ZERO, diodeforward_1_out, diodeforward_1_out);
  PullDown pulldown_1 (.out(diodeforward_1_out));
  LED led_9 (.in(D7));
  D_FF IC16 (.D(IC16_nq), .C(button_11_out), .Q(D7), .nQ(IC16_nq));
  Button button_11 (.out(button_11_out));
  Seven_Seg_Hex seven_seg_hex_4 (.d({BUS3, BUS2, BUS1, BUS0}), .dp(1'b0));
  LED led_10 (.in(D6));
  D_FF d_ff_7 (.D(d_ff_7_nq), .C(button_12_out), .Q(D6), .nQ(d_ff_7_nq));
  Button button_12 (.out(button_12_out));
  LED led_11 (.in(ZERO));
  LED led_12 (.in(D5));
  D_FF d_ff_8 (.D(d_ff_8_nq), .C(button_13_out), .Q(D5), .nQ(d_ff_8_nq));
  Button button_13 (.out(button_13_out));
  LED led_13 (.in(D4));
  D_FF d_ff_9 (.D(d_ff_9_nq), .C(button_14_out), .Q(D4), .nQ(d_ff_9_nq));
  Button button_14 (.out(button_14_out));
  LED led_14 (.in(D3));
  D_FF d_ff_10 (.D(d_ff_10_nq), .C(button_15_out), .Q(D3), .nQ(d_ff_10_nq));
  Button button_15 (.out(button_15_out));
  Seven_Seg_Hex seven_seg_hex_5 (.d(U6_2_pin6), .dp(1'b0));
  LED led_15 (.in(D2));
  D_FF d_ff_11 (.D(d_ff_11_nq), .C(button_16_out), .Q(D2), .nQ(d_ff_11_nq));
  Button button_16 (.out(button_16_out));
  Seven_Seg_Hex seven_seg_hex_6 (.d({U6_2_pin10, Aout}), .dp(1'b0));
  _74164 U6_2 (
    .pin1(1'b1), .pin2(Fout), .pin3(U6_2_pin6[3]), .pin4(U6_2_pin6[2]), .pin5(U6_2_pin6[1]),
    .pin6(U6_2_pin6[0]), .pin7(1'b0), .pin8(GCLK), .pin9(CLR), .pin10(U6_2_pin10[3]), .pin11(U6_2_pin10[2]),
    .pin12(U6_2_pin10[1]), .pin13(Aout), .pin14(1'b1));
  LED led_16 (.in(D1));
  D_FF d_ff_12 (.D(d_ff_12_nq), .C(button_17_out), .Q(D1), .nQ(d_ff_12_nq));
  Button button_17 (.out(button_17_out));
  LED led_17 (.in(D0));
  D_FF IC16_2 (.D(IC16_2_nq), .C(button_18_out), .Q(D0), .nQ(IC16_2_nq));
  Button button_18 (.out(button_18_out));
  Seven_Seg_Hex seven_seg_hex_7 (.d({D7, D6, D5, D4}), .dp(1'b0));
  Seven_Seg_Hex seven_seg_hex_8 (.d({D3, D2, D1, D0}), .dp(1'b0));
  xor xor_1 (xor_1_out, Aout, nA);
  xor xor_2 (xor_2_out, nB, Bout);
  nand nand_2 (nand_2_out, SETC, C);
  nand nand_3 (nand_3_out, C, C);
  nand nand_4 (CLR, CLA, LD_t);
  nand nand_5 (nand_5_out, clk, clk);
  nand nand_6 (RST, RES, nRST);
  nand nand_7 (nRST, RST, T0);
  xor xor_3 (xor_3_out, xor_1_out, xor_2_out);
  nand nand_8 (nand_8_out, nand_3_out, LD_t);
  nand nand_9 (GCLK, nand_5_out, RST);
  xor xor_4 (xor_4_out, xor_3_out, Cin);
  nand nand_10 (nand_10_out, xor_3_out, Cin);
  nand nand_11 (nand_11_out, xor_1_out, xor_2_out);
  nand nand_12 (nand_12_out, nand_10_out, nand_11_out);
  _74161 U7_2 (
    .pin1(RST), .pin2(clk), .pin3(1'b0), .pin4(1'b0), .pin5(1'b0), .pin6(1'b0), .pin7(1'b1), .pin8(1'b0),
    .pin9(1'b1), .pin10(1'b1), .pin11(U7_2_pin11[3]), .pin12(U7_2_pin11[2]), .pin13(U7_2_pin11[1]),
    .pin14(U7_2_pin11[0]), .pin15(U7_2_pin15), .pin16(1'b1));
  nand nand_13 (nand_13_out, xor_4_out, I0);
  nand nand_14 (nand_14_out, I1, nand_12_out);
  nand nand_15 (nand_15_out, nand_12_out, F);
  nand nand_16 (Fout, nand_13_out, nand_14_out);
  nand nand_17 (Cout, nand_15_out, nand_15_out);
  Seven_Seg_Hex seven_seg_hex_9 (.d(U7_2_pin11), .dp(1'b0));
  and and_1 (RCO, U7_2_pin11[2], U7_2_pin11[1], U7_2_pin11[0]);
  and and_2 (nCE, LD, T0, nRST);
  _7474 U12 (
    .pin1(nand_8_out), .pin2(Cout), .pin3(GCLK), .pin4(nand_2_out), .pin5(Cin), .pin7(1'b0), .pin8(T0),
    .pin9(IX), .pin10(1'b1), .pin11(clk), .pin12(RCO), .pin13(1'b1), .pin14(1'b1));  // open: pin6
  LED led_18 (.in(Cin));

  // Other names for the same wires on the sheet: nLOAD = LD; nRES = RES

  // Notes on the sheet:
  //   clk: Hz: 4
  //   ROM & PC
  //   MITE
  //   Instruction Input
  //   STEP/RUN
  //   8-bit Shift Register B
  //   CLR PC
  //   Instruction Decode
  //   CLA
  //   C
  //   F
  //   ~B
  //   ~A
  //   I0
  //   I1
  //   LOAD
  //   AND
  //   OR
  //   XOR
  //   ADD
  //   SUB
  //   STORE
  //   JMP
  //   Output Display Register
  //   ENTER H
  //   Data Input
  //   OUTPUT REGISTER
  //   ZERO
  //   ENTER L
  //   ACCUMULATOR
  //   Shift Register A
  //   ALU
  //   CLR ACC
  //   U5
  //   MITE 8-bit  Bit serial CPU Testbed
  //   Clock Sequencer
  //   Carry is only set before Bit 0 of an operation
  //   Any residual carry is cleared before an operation
  //   Suppress Carry
  //   # Clock
  //   Carry FF
  //   CARRY
endmodule
