// Digital circuit mite_proto_000.dig as structural Verilog
module mite_proto_000 (
  input  clk,
  input  in_3,
  input  in_4,
  input  in_5,
  input  in_15,
  input  clk_3,
  output Fout,
  output nLDB,
  output out_7,
  output SETC,
  output RES,
  output RUN,
  output T0,
  output GCLK,
  output RST,
  output CLK_2
);

  wire _0_out, _1_out, _2_out, _3_out, _4_out, _5_out, _6_out, _7_out, _8_out, _9_out, _74173_4_pin11,
       _74173_4_pin12, _74173_4_pin13, _74173_4_pin14, _74193_1_pin12, _74193_1_pin13, _74193_2_pin12,
       _74193_2_pin13, _74193_3_pin12, _74193_3_pin13, _74540_1_pin11, _74540_1_pin12, _74540_1_pin13,
       _74540_1_pin14, _74540_1_pin15, _74540_1_pin16, _74540_1_pin17, _74573_1_pin12, _74573_1_pin13,
       _74573_1_pin14, _74573_1_pin15, _74573_1_pin16, _74573_1_pin17, _74573_1_pin18, _74573_1_pin19,
       _74573_2_pin12, _74573_2_pin13, _74573_2_pin14, _74573_2_pin15, _74573_2_pin16, _74573_2_pin17,
       _74573_2_pin18, _74573_2_pin19, A0, A1, A2, A3, A4, A5, A6, A7, A8, A9, A10, A11, A12, A13, A14, A15,
       A_out, AC0, AC1, AC2, AC3, AC4, AC5, AC6, AC7, AC8, AC9, AC10, AC11, AC12, AC13, AC14, AC15, ADD,
       Address_out, ALU, ALU_to_RAM_out, AND, B_out, Bout, BUS0, BUS1, BUS2, BUS3, BUS4, BUS5, BUS6, BUS7,
       BUS8, BUS9, BUS10, BUS11, BUS12, BUS13, BUS14, BUS15, button_2_out, C, C_out, Cin, CL0, CL1, CL2, CL3,
       CLA, Clear_out, CLR, Cout, D8, D9, D10, D11, D_out, Dec_out, Deposit_nWR_out, diodebackward_3_out,
       diodebackward_4_out, diodebackward_11_out, diodebackward_13_out, diodebackward_15_out,
       diodebackward_30_out, diodeforward_1_out, DN, E_out, Examine_nRD_out, F, F0, F1, F2, F3, F4, F5, F6,
       F_out, I0, I1, Inc_out, IX, LOAD, nA, nALB, nand_5_out, nand_6_out, nand_8_out, nand_10_out,
       nand_11_out, nand_13_out, nand_14_out, nand_15_out, nand_16_out, nand_17_out, nand_18_out, nB, nCLRPC,
       nDE, nJMP, nLATCH, nLD, nOE, not_4_out, not_9_out, nWE, nZERO, OR, pullup_1_out, pullup_2_out,
       pullup_5_out, pullup_6_out, pullup_9_out, pullup_12_out, pullup_13_out, Q0, Q1, Q2, Q3, Q4, Q5, Q6,
       Q7, Q8, Q9, Q10, Q11, Q12, Q13, Q14, Q15, ST, SUB, U3_pin9, U7_pin15, UP, XOR, xor_1_out, xor_2_out,
       xor_3_out, xor_4_out;

  PullUp pullup_1 (.out(pullup_1_out));
  DiodeBackward diodebackward_1 (.in(Address_out), .out(pullup_1_out));
  PullUp pullup_2 (.out(pullup_2_out));
  DiodeBackward diodebackward_2 (.in(Dec_out), .out(pullup_2_out));
  DiodeBackward diodebackward_3 (.in(Inc_out), .out(diodebackward_3_out));
  not not_1 (nLD, _74540_1_pin11);
  _74139 _74139_1 (
    .pin1(1'b1), .pin2(1'b1), .pin3(1'b1), .pin8(1'b0), .pin11(nALB), .pin12(nDE), .pin13(1'b0), .pin14(ALU),
    .pin15(nWE), .pin16(1'b1));  // open: pin4, pin5, pin6, pin7, pin9, pin10
  PullUp pullup_3 (.out(diodebackward_3_out));
  DiodeBackward diodebackward_4 (.in(ALU_to_RAM_out), .out(diodebackward_4_out));
  DiodeBackward diodebackward_5 (.in(Examine_nRD_out), .out(diodebackward_4_out));
  DiodeBackward diodebackward_6 (.in(Dec_out), .out(diodebackward_4_out));
  DiodeBackward diodebackward_7 (.in(Inc_out), .out(diodebackward_4_out));
  PullUp pullup_4 (.out(diodebackward_4_out));
  PullUp pullup_5 (.out(pullup_5_out));
  DiodeBackward diodebackward_8 (.in(Examine_nRD_out), .out(pullup_5_out));
  DiodeBackward diodebackward_9 (.in(Deposit_nWR_out), .out(pullup_5_out));
  not not_2 (ALU, _74540_1_pin15);
  not not_3 (nWE, _74540_1_pin16);
  nand nand_1 (UP, _74540_1_pin13, _74540_1_pin14);
  nand nand_2 (DN, _74540_1_pin12, _74540_1_pin14);
  PullUp pullup_6 (.out(pullup_6_out));
  DiodeBackward diodebackward_10 (.in(ALU_to_RAM_out), .out(pullup_6_out));
  DiodeBackward diodebackward_11 (.in(Examine_nRD_out), .out(diodebackward_11_out));
  DiodeBackward diodebackward_12 (.in(Deposit_nWR_out), .out(pullup_6_out));
  not not_4 (not_4_out, _74540_1_pin17);
  PullUp pullup_7 (.out(diodebackward_11_out));
  DiodeBackward diodebackward_13 (.in(Clear_out), .out(diodebackward_13_out));
  _74540 _74540_1 (
    .pin1(1'b0), .pin2(diodebackward_13_out), .pin3(diodebackward_11_out), .pin4(pullup_6_out),
    .pin5(pullup_5_out), .pin6(diodebackward_4_out), .pin7(diodebackward_3_out), .pin8(pullup_2_out),
    .pin9(pullup_1_out), .pin10(1'b0), .pin11(_74540_1_pin11), .pin12(_74540_1_pin12),
    .pin13(_74540_1_pin13), .pin14(_74540_1_pin14), .pin15(_74540_1_pin15), .pin16(_74540_1_pin16),
    .pin17(_74540_1_pin17), .pin18(RES), .pin19(1'b0), .pin20(1'b1));
  PullUp pullup_8 (.out(diodebackward_13_out));
  Button #(.activeLow("true")) ALU_to_RAM (.out(ALU_to_RAM_out));
  Button #(.activeLow("true")) Clear (.out(Clear_out));
  Button #(.activeLow("true")) Examine_nRD (.out(Examine_nRD_out));
  Button #(.activeLow("true")) Deposit_nWR (.out(Deposit_nWR_out));
  Button #(.activeLow("true")) Dec (.out(Dec_out));
  Button #(.activeLow("true")) Inc (.out(Inc_out));
  Button #(.activeLow("true")) Address (.out(Address_out));
  nand nand_3 (nOE, not_4_out, in_15);
  _74173 _74173_1 (
    .pin1(1'b0), .pin2(1'b0), .pin3(A12), .pin4(A13), .pin5(A14), .pin6(A15), .pin7(nLATCH), .pin8(1'b0),
    .pin9(1'b0), .pin10(1'b0), .pin11(A11), .pin12(A10), .pin13(A9), .pin14(A8), .pin15(1'b0), .pin16(1'b1));
  _74165 U3 (
    .pin1(out_7), .pin2(GCLK), .pin3(D11), .pin4(D10), .pin5(D9), .pin6(D8), .pin8(1'b0), .pin9(U3_pin9),
    .pin10(1'b0), .pin11(BUS15), .pin12(BUS14), .pin13(BUS13), .pin14(BUS12), .pin15(1'b0), .pin16(1'b1));  // open: pin7
  _74165 U4 (
    .pin1(out_7), .pin2(GCLK), .pin3(BUS3), .pin4(BUS2), .pin5(BUS1), .pin6(BUS0), .pin8(1'b0), .pin9(Bout),
    .pin10(U3_pin9), .pin11(BUS7), .pin12(BUS6), .pin13(BUS5), .pin14(BUS4), .pin15(1'b0), .pin16(1'b1));  // open: pin7
  Seven_Seg_Hex seven_seg_hex_1 (.d({A15, A14, A13, A12}), .dp(1'b0));
  Seven_Seg_Hex seven_seg_hex_2 (.d({A11, A10, A9, A8}), .dp(1'b0));
  Seven_Seg_Hex seven_seg_hex_3 (.d({A7, A6, A5, A4}), .dp(1'b0));
  Seven_Seg_Hex seven_seg_hex_4 (.d({A3, A2, A1, A0}), .dp(1'b0));
  Button #(.activeLow("true")) u_C (.out(C_out));
  Button #(.activeLow("true")) _8 (.out(_8_out));
  Button #(.activeLow("true")) _4 (.out(_4_out));
  Button #(.activeLow("true")) _0 (.out(_0_out));
  _74173 _74173_2 (
    .pin1(1'b0), .pin2(1'b0), .pin3(A8), .pin4(A9), .pin5(A10), .pin6(A11), .pin7(nLATCH), .pin8(1'b0),
    .pin9(1'b0), .pin10(1'b0), .pin11(A7), .pin12(A6), .pin13(A5), .pin14(A4), .pin15(1'b0), .pin16(1'b1));
  Button #(.activeLow("true")) D (.out(D_out));
  Button #(.activeLow("true")) _9 (.out(_9_out));
  Button #(.activeLow("true")) _5 (.out(_5_out));
  Button #(.activeLow("true")) _1 (.out(_1_out));
  Seven_Seg_Hex seven_seg_hex_5 (.d({Q15, Q14, Q13, Q12}), .dp(1'b0));
  _74173 _74173_3 (
    .pin1(1'b0), .pin2(1'b0), .pin3(A4), .pin4(A5), .pin5(A6), .pin6(A7), .pin7(nLATCH), .pin8(1'b0),
    .pin9(1'b0), .pin10(1'b0), .pin11(A3), .pin12(A2), .pin13(A1), .pin14(A0), .pin15(1'b0), .pin16(1'b1));
  Seven_Seg_Hex seven_seg_hex_6 (.d({Q11, Q10, Q9, Q8}), .dp(1'b0));
  Button #(.activeLow("true")) E (.out(E_out));
  Button #(.activeLow("true")) A (.out(A_out));
  Button #(.activeLow("true")) _6 (.out(_6_out));
  Button #(.activeLow("true")) _2 (.out(_2_out));
  _74164 U5 (
    .pin1(1'b1), .pin2(Fout), .pin3(AC15), .pin4(AC14), .pin5(AC13), .pin6(AC12), .pin7(1'b0), .pin8(GCLK),
    .pin9(CLR), .pin10(AC11), .pin11(AC10), .pin12(AC9), .pin13(AC8), .pin14(1'b1));
  Seven_Seg_Hex seven_seg_hex_7 (.d({Q7, Q6, Q5, Q4}), .dp(1'b0));
  Button #(.activeLow("true")) u_F (.out(F_out));
  Button #(.activeLow("true")) B (.out(B_out));
  Button #(.activeLow("true")) _7 (.out(_7_out));
  Button #(.activeLow("true")) _3 (.out(_3_out));
  Seven_Seg_Hex seven_seg_hex_8 (.d({Q3, Q2, Q1, Q0}), .dp(1'b0));
  _74173 _74173_4 (
    .pin1(1'b0), .pin2(1'b0), .pin3(A0), .pin4(A1), .pin5(A2), .pin6(A3), .pin7(nLATCH), .pin8(1'b0),
    .pin9(1'b0), .pin10(1'b0), .pin11(_74173_4_pin11), .pin12(_74173_4_pin12), .pin13(_74173_4_pin13),
    .pin14(_74173_4_pin14), .pin15(1'b0), .pin16(1'b1));
  Seven_Seg_Hex seven_seg_hex_9 (.d({BUS15, BUS14, BUS13, BUS12}), .dp(1'b0));
  Seven_Seg_Hex seven_seg_hex_10 (.d({AC15, AC14, AC13, AC12}), .dp(1'b0));
  Seven_Seg_Hex seven_seg_hex_11 (.d({BUS11, BUS10, BUS9, BUS8}), .dp(1'b0));
  PullUp pullup_9 (.out(pullup_9_out));
  DiodeBackward diodebackward_14 (.in(F_out), .out(pullup_9_out));
  DiodeBackward diodebackward_15 (.in(F_out), .out(diodebackward_15_out));
  DiodeBackward diodebackward_16 (.in(E_out), .out(pullup_9_out));
  DiodeBackward diodebackward_17 (.in(E_out), .out(diodebackward_15_out));
  DiodeBackward diodebackward_18 (.in(D_out), .out(diodebackward_15_out));
  DiodeBackward diodebackward_19 (.in(D_out), .out(pullup_9_out));
  DiodeBackward diodebackward_20 (.in(C_out), .out(diodebackward_15_out));
  DiodeBackward diodebackward_21 (.in(C_out), .out(pullup_9_out));
  DiodeBackward diodebackward_22 (.in(B_out), .out(pullup_9_out));
  DiodeBackward diodebackward_23 (.in(A_out), .out(pullup_9_out));
  DiodeBackward diodebackward_24 (.in(_9_out), .out(pullup_9_out));
  DiodeBackward diodebackward_25 (.in(_8_out), .out(pullup_9_out));
  DiodeBackward diodebackward_26 (.in(_7_out), .out(diodebackward_15_out));
  DiodeBackward diodebackward_27 (.in(_6_out), .out(diodebackward_15_out));
  DiodeBackward diodebackward_28 (.in(_5_out), .out(diodebackward_15_out));
  DiodeBackward diodebackward_29 (.in(_4_out), .out(diodebackward_15_out));
  not not_5 (_74173_4_pin11, pullup_9_out);
  Seven_Seg_Hex seven_seg_hex_12 (.d({AC11, AC10, AC9, AC8}), .dp(1'b0));
  Seven_Seg_Hex seven_seg_hex_13 (.d({BUS7, BUS6, BUS5, BUS4}), .dp(1'b0));
  PullUp pullup_10 (.out(diodebackward_15_out));
  DiodeBackward diodebackward_30 (.in(F_out), .out(diodebackward_30_out));
  DiodeBackward diodebackward_31 (.in(E_out), .out(diodebackward_30_out));
  DiodeBackward diodebackward_32 (.in(B_out), .out(diodebackward_30_out));
  DiodeBackward diodebackward_33 (.in(A_out), .out(diodebackward_30_out));
  DiodeBackward diodebackward_34 (.in(_7_out), .out(diodebackward_30_out));
  DiodeBackward diodebackward_35 (.in(_6_out), .out(diodebackward_30_out));
  DiodeBackward diodebackward_36 (.in(_3_out), .out(diodebackward_30_out));
  DiodeBackward diodebackward_37 (.in(_2_out), .out(diodebackward_30_out));
  not not_6 (_74173_4_pin12, diodebackward_15_out);
  Seven_Seg_Hex seven_seg_hex_14 (.d({AC7, AC6, AC5, AC4}), .dp(1'b0));
  Seven_Seg_Hex seven_seg_hex_15 (.d({BUS3, BUS2, BUS1, BUS0}), .dp(1'b0));
  PullUp pullup_11 (.out(diodebackward_30_out));
  PullUp pullup_12 (.out(pullup_12_out));
  DiodeBackward diodebackward_38 (.in(F_out), .out(pullup_12_out));
  DiodeBackward diodebackward_39 (.in(D_out), .out(pullup_12_out));
  DiodeBackward diodebackward_40 (.in(B_out), .out(pullup_12_out));
  DiodeBackward diodebackward_41 (.in(_9_out), .out(pullup_12_out));
  DiodeBackward diodebackward_42 (.in(_7_out), .out(pullup_12_out));
  DiodeBackward diodebackward_43 (.in(_5_out), .out(pullup_12_out));
  DiodeBackward diodebackward_44 (.in(_3_out), .out(pullup_12_out));
  DiodeBackward diodebackward_45 (.in(_1_out), .out(pullup_12_out));
  not not_7 (_74173_4_pin14, pullup_12_out);
  not not_8 (_74173_4_pin13, diodebackward_30_out);
  Seven_Seg_Hex seven_seg_hex_16 (.d({AC3, AC2, AC1, AC0}), .dp(1'b0));
  _74164 U6 (
    .pin1(1'b1), .pin2(AC8), .pin3(AC7), .pin4(AC6), .pin5(AC5), .pin6(AC4), .pin7(1'b0), .pin8(GCLK),
    .pin9(CLR), .pin10(AC3), .pin11(AC2), .pin12(AC1), .pin13(AC0), .pin14(1'b1));
  PullUp pullup_13 (.out(pullup_13_out));
  DiodeBackward diodebackward_46 (.in(F_out), .out(pullup_13_out));
  DiodeBackward diodebackward_47 (.in(E_out), .out(pullup_13_out));
  DiodeBackward diodebackward_48 (.in(D_out), .out(pullup_13_out));
  DiodeBackward diodebackward_49 (.in(C_out), .out(pullup_13_out));
  DiodeBackward diodebackward_50 (.in(B_out), .out(pullup_13_out));
  DiodeBackward diodebackward_51 (.in(A_out), .out(pullup_13_out));
  DiodeBackward diodebackward_52 (.in(_9_out), .out(pullup_13_out));
  DiodeBackward diodebackward_53 (.in(_8_out), .out(pullup_13_out));
  DiodeBackward diodebackward_54 (.in(_7_out), .out(pullup_13_out));
  DiodeBackward diodebackward_55 (.in(_6_out), .out(pullup_13_out));
  DiodeBackward diodebackward_56 (.in(_5_out), .out(pullup_13_out));
  DiodeBackward diodebackward_57 (.in(_4_out), .out(pullup_13_out));
  DiodeBackward diodebackward_58 (.in(_3_out), .out(pullup_13_out));
  DiodeBackward diodebackward_59 (.in(_2_out), .out(pullup_13_out));
  DiodeBackward diodebackward_60 (.in(_1_out), .out(pullup_13_out));
  DiodeBackward diodebackward_61 (.in(_0_out), .out(pullup_13_out));
  not not_9 (not_9_out, pullup_13_out);
  Monoflop monoflop_1 (.C(not_9_out), .R(1'b0), .nQ(nLATCH));  // open: Q
  LED led_1 (.in(nLATCH));
  Monoflop monoflop_2 (.C(RUN), .R(1'b0), .Q(nLDB), .nQ(out_7));
  Button button_1 (.out(RUN));
  DiodeForward diodeforward_1 (.in(AC15), .out(diodeforward_1_out));
  DiodeForward diodeforward_2 (.in(AC14), .out(diodeforward_1_out));
  DiodeForward diodeforward_3 (.in(AC13), .out(diodeforward_1_out));
  DiodeForward diodeforward_4 (.in(AC12), .out(diodeforward_1_out));
  DiodeForward diodeforward_5 (.in(AC11), .out(diodeforward_1_out));
  DiodeForward diodeforward_6 (.in(AC10), .out(diodeforward_1_out));
  DiodeForward diodeforward_7 (.in(AC9), .out(diodeforward_1_out));
  DiodeForward diodeforward_8 (.in(AC8), .out(diodeforward_1_out));
  DiodeForward diodeforward_9 (.in(AC7), .out(diodeforward_1_out));
  DiodeForward diodeforward_10 (.in(AC6), .out(diodeforward_1_out));
  DiodeForward diodeforward_11 (.in(AC5), .out(diodeforward_1_out));
  DiodeForward diodeforward_12 (.in(AC4), .out(diodeforward_1_out));
  DiodeForward diodeforward_13 (.in(AC3), .out(diodeforward_1_out));
  DiodeForward diodeforward_14 (.in(AC2), .out(diodeforward_1_out));
  DiodeForward diodeforward_15 (.in(AC1), .out(diodeforward_1_out));
  DiodeForward diodeforward_16 (.in(AC0), .out(diodeforward_1_out));
  Monoflop monoflop_3 (.C(out_7), .R(1'b0), .Q(SETC), .nQ(RES));
  LED led_2 (.in(diodeforward_1_out));
  PullDown pulldown_1 (.out(diodeforward_1_out));
  nand nand_4 (nZERO, diodeforward_1_out, diodeforward_1_out);
  Monoflop monoflop_4 (.C(button_2_out), .R(1'b0), .nQ(nCLRPC));  // open: Q
  Button button_2 (.out(button_2_out));
  _74193 _74193_1 (
    .pin1(A1), .pin2(Q1), .pin3(Q0), .pin4(DN), .pin5(UP), .pin6(Q2), .pin7(Q3), .pin8(1'b0), .pin9(A3),
    .pin10(A2), .pin11(nLD), .pin12(_74193_1_pin12), .pin13(_74193_1_pin13), .pin14(RES), .pin15(A0),
    .pin16(1'b1));
  _74193 _74193_2 (
    .pin1(A5), .pin2(Q5), .pin3(Q4), .pin4(_74193_1_pin13), .pin5(_74193_1_pin12), .pin6(Q6), .pin7(Q7),
    .pin8(1'b0), .pin9(A7), .pin10(A6), .pin11(nLD), .pin12(_74193_2_pin12), .pin13(_74193_2_pin13),
    .pin14(RES), .pin15(A4), .pin16(1'b1));
  _74193 _74193_3 (
    .pin1(A9), .pin2(Q9), .pin3(Q8), .pin4(_74193_2_pin13), .pin5(_74193_2_pin12), .pin6(Q10), .pin7(Q11),
    .pin8(1'b0), .pin9(A11), .pin10(A10), .pin11(nLD), .pin12(_74193_3_pin12), .pin13(_74193_3_pin13),
    .pin14(RES), .pin15(A8), .pin16(1'b1));
  _74193 _74193_4 (
    .pin1(A13), .pin2(Q13), .pin3(Q12), .pin4(_74193_3_pin13), .pin5(_74193_3_pin12), .pin6(Q14), .pin7(Q15),
    .pin8(1'b0), .pin9(A15), .pin10(A14), .pin11(nLD), .pin14(RES), .pin15(A12), .pin16(1'b1));  // open: pin12, pin13
  nand nand_5 (nand_5_out, SETC, C);
  nand nand_6 (nand_6_out, C, C);
  nand nand_7 (CLR, CLA, nLDB);
  _74138 U1 (
    .pin1(in_3), .pin2(in_4), .pin3(in_5), .pin4(1'b0), .pin5(1'b0), .pin6(1'b1), .pin7(nJMP), .pin8(1'b0),
    .pin9(ST), .pin10(SUB), .pin11(ADD), .pin12(XOR), .pin13(OR), .pin14(AND), .pin15(LOAD), .pin16(1'b1));
  nand nand_8 (nand_8_out, clk, clk);
  nand nand_9 (RST, RES, nand_10_out);
  nand nand_10 (nand_10_out, RST, T0);
  xor xor_1 (xor_1_out, AC0, nA);
  xor xor_2 (xor_2_out, nB, Bout);
  nand nand_11 (nand_11_out, nand_6_out, nLDB);
  DiodeBackward diodebackward_62 (.in(LOAD), .out(F6));
  PullUp pullup_14 (.out(F6));
  DiodeBackward diodebackward_63 (.in(LOAD), .out(F5));
  DiodeBackward diodebackward_64 (.in(ADD), .out(F5));
  DiodeBackward diodebackward_65 (.in(SUB), .out(F5));
  DiodeBackward diodebackward_66 (.in(nJMP), .out(F5));
  nand nand_12 (GCLK, nand_8_out, RST);
  xor xor_3 (xor_3_out, xor_1_out, xor_2_out);
  PullUp pullup_15 (.out(F4));
  PullUp pullup_16 (.out(F5));
  DiodeBackward diodebackward_67 (.in(SUB), .out(F4));
  Seven_Seg_Hex seven_seg_hex_17 (.d({CL3, CL2, CL1, CL0}), .dp(1'b0));
  PullUp pullup_17 (.out(F3));
  DiodeBackward diodebackward_68 (.in(SUB), .out(F3));
  xor xor_4 (xor_4_out, xor_3_out, Cin);
  nand nand_13 (nand_13_out, xor_3_out, Cin);
  nand nand_14 (nand_14_out, xor_1_out, xor_2_out);
  // _62256 _62256_1: pin names not known; wires that end beside it: Q14, Q12, Q7, Q6, Q5, Q4, Q3, Q2, Q1, Q0, BUS8, BUS9, BUS10, 1'b0, 1'b1, nWE, Q13, Q8, Q9, Q11, nOE, Q10, 1'b0, BUS15
  _74541 _74541_1 (
    .pin1(nDE), .pin2(A15), .pin3(A14), .pin4(A13), .pin5(A12), .pin6(A11), .pin7(A10), .pin8(A9), .pin9(A8),
    .pin10(1'b0), .pin11(BUS8), .pin12(BUS9), .pin13(BUS10), .pin14(BUS11), .pin15(BUS12), .pin16(BUS13),
    .pin17(BUS14), .pin18(BUS15), .pin19(nDE), .pin20(1'b1));
  _74541 _74541_2 (
    .pin1(nDE), .pin2(AC15), .pin3(AC14), .pin4(AC13), .pin5(AC12), .pin6(AC11), .pin7(AC10), .pin8(AC9),
    .pin9(AC8), .pin10(1'b0), .pin11(BUS8), .pin12(BUS9), .pin13(BUS10), .pin14(BUS11), .pin15(BUS12),
    .pin16(BUS13), .pin17(BUS14), .pin18(BUS15), .pin19(nDE), .pin20(1'b1));
  PullUp pullup_18 (.out(F2));
  DiodeBackward diodebackward_69 (.in(AND), .out(F1));
  DiodeBackward diodebackward_70 (.in(OR), .out(F1));
  _74161 U7 (
    .pin1(RST), .pin2(clk), .pin3(1'b0), .pin4(1'b0), .pin5(1'b0), .pin6(1'b0), .pin7(1'b1), .pin8(1'b0),
    .pin9(1'b1), .pin10(1'b1), .pin11(CL3), .pin12(CL2), .pin13(CL1), .pin14(CL0), .pin15(U7_pin15),
    .pin16(1'b1));
  PullUp pullup_19 (.out(F1));
  PullUp pullup_20 (.out(F0));
  DiodeBackward diodebackward_71 (.in(LOAD), .out(F0));
  DiodeBackward diodebackward_72 (.in(OR), .out(F0));
  DiodeBackward diodebackward_73 (.in(XOR), .out(F0));
  DiodeBackward diodebackward_74 (.in(ADD), .out(F0));
  DiodeBackward diodebackward_75 (.in(SUB), .out(F0));
  DiodeBackward diodebackward_76 (.in(ST), .out(F0));
  nand nand_15 (nand_15_out, nand_13_out, nand_14_out);
  nand nand_16 (nand_16_out, xor_4_out, I0);
  nand nand_17 (nand_17_out, I1, nand_15_out);
  nand nand_18 (nand_18_out, nand_15_out, F);
  _74540 U2 (
    .pin1(1'b0), .pin2(F0), .pin3(F1), .pin4(F2), .pin5(F3), .pin6(F4), .pin7(F5), .pin8(F6), .pin9(1'b0),
    .pin10(1'b0), .pin12(CLA), .pin13(F), .pin14(C), .pin15(nB), .pin16(nA), .pin17(I1), .pin18(I0),
    .pin19(1'b0), .pin20(1'b1));  // open: pin11
  _7474 U8 (
    .pin1(1'b1), .pin2(U7_pin15), .pin3(clk), .pin4(1'b1), .pin5(IX), .pin6(T0), .pin7(1'b0), .pin9(Cin),
    .pin10(nand_5_out), .pin11(GCLK), .pin12(Cout), .pin13(nand_11_out), .pin14(1'b1));  // open: pin8
  nand nand_19 (Fout, nand_16_out, nand_17_out);
  nand nand_20 (Cout, nand_18_out, nand_18_out);
  // _62256 _62256_2: pin names not known; wires that end beside it: Q14, Q12, Q7, Q6, Q5, Q4, Q3, Q2, Q1, Q0, BUS0, BUS1, BUS2, 1'b0, 1'b1, nWE, Q13, Q8, Q9, Q11, nOE, Q10, 1'b0, BUS7
  _74541 _74541_3 (
    .pin1(nDE), .pin2(A7), .pin3(A6), .pin4(A5), .pin5(A4), .pin6(A3), .pin7(A2), .pin8(A1), .pin9(A0),
    .pin10(1'b0), .pin11(BUS0), .pin12(BUS1), .pin13(BUS2), .pin14(BUS3), .pin15(BUS4), .pin16(BUS5),
    .pin17(BUS6), .pin18(BUS7), .pin19(nDE), .pin20(1'b1));
  _74541 _74541_4 (
    .pin1(nDE), .pin2(AC7), .pin3(AC6), .pin4(AC5), .pin5(AC4), .pin6(AC3), .pin7(AC2), .pin8(AC1),
    .pin9(AC0), .pin10(1'b0), .pin11(BUS0), .pin12(BUS1), .pin13(BUS2), .pin14(BUS3), .pin15(BUS4),
    .pin16(BUS5), .pin17(BUS6), .pin18(BUS7), .pin19(nDE), .pin20(1'b1));
  _74573 _74573_1 (
    .pin2(BUS15), .pin3(BUS14), .pin4(BUS13), .pin5(BUS12), .pin6(BUS11), .pin7(BUS10), .pin8(BUS9),
    .pin9(BUS8), .pin10(1'b0), .pin12(_74573_1_pin12), .pin13(_74573_1_pin13), .pin14(_74573_1_pin14),
    .pin15(_74573_1_pin15), .pin16(_74573_1_pin16), .pin17(_74573_1_pin17), .pin18(_74573_1_pin18),
    .pin19(_74573_1_pin19), .pin20(1'b1));  // open: pin1, pin11
  _74573 _74573_2 (
    .pin2(BUS7), .pin3(BUS6), .pin4(BUS5), .pin5(BUS4), .pin6(BUS3), .pin7(BUS2), .pin8(BUS1), .pin9(BUS0),
    .pin10(1'b0), .pin12(_74573_2_pin12), .pin13(_74573_2_pin13), .pin14(_74573_2_pin14),
    .pin15(_74573_2_pin15), .pin16(_74573_2_pin16), .pin17(_74573_2_pin17), .pin18(_74573_2_pin18),
    .pin19(_74573_2_pin19), .pin20(1'b1));  // open: pin1, pin11

  assign CLK_2 = clk;
  assign clk_3 = clk;

  // Other names for the same wires on the sheet: Aout = AC0; LDA = nLDB; nLDB_t = out_7

  // Notes on the sheet:
  //   clk: Hz: 2147483647
  //   in_15: default 1
  //   clk_3: Hz: 10
  //   Front Panel
  //   LOAD
  //   UP
  //   DOWN
  //   COUNT
  //   spider000
  //   Spider 000 Bit serial CPU Testbed
  //   ~DE
  //   WRITE
  //   RESET
  //   READ
  //   16 bit Shift Register B
  //   KEY DATA
  //   Hex Keypad
  //   KEYSWITCH REGISTER
  //   RAM ADDRESS
  //   16 bit Shift Register A
  //   ACCUMULATOR
  //   RAM DATA
  //   STEP/RUN
  //   PC and RAM
  //   PROGRAM COUNTER
  //   Instruction Input
  //   CLR PC
  //   000 LOAD
  //   001 AND
  //   010 OR
  //   011 XOR
  //   100 ADD
  //   101 SUB
  //   110 STORE
  //   111 JUMP
  //   CLR ACC
  //   CLA
  //   # Clock
  //   Carry is only set before Bit 0 of an operation
  //   Any residual carry is cleared before an operation
  //   C
  //   F
  //   DATA BUFFER HI
  //   ~B
  //   RAM HI
  //   AC to BUS HI
  //   ~A
  //   I0
  //   I1
  //   Clock Sequencer
  //   AND
  //   OR
  //   XOR
  //   ADD
  //   SUB
  //   STORE
  //   JMP
  //   Instruction Decode
  //   Suppress Carry
  //   DATA BUFFER LO
  //   AC to BUS LO
  //   RAM LO
  //   Carry FF
  //   Instruction Register
  //   Address/Data Register
endmodule
