// Digital circuit MITE22_ROM_ALU.dig as structural Verilog
module MITE22_ROM_ALU (
  input  in_1,
  input  clk,
  input  in_9,
  input  in_10,
  input  in_11,
  input  in_12,
  input  in_13,
  output T0,
  output T8,
  output LD,
  output GCLK,
  output SETC,
  output GATE
);

  wire A0, A1, A2, A3, A4, A5, A6, A7, A8, Aout, Bout, BUS0, BUS1, BUS2, BUS3, BUS4, BUS5, BUS6, BUS7,
       button_1_out, button_2_out, button_3_out, button_4_out, button_5_out, button_6_out, button_7_out,
       button_8_out, Cin, CLR, Cout, d_ff_1_nq, d_ff_2_nq, d_ff_3_nq, d_ff_4_nq, d_ff_5_nq, d_ff_6_nq,
       d_ff_7_nq, diodeforward_1_out, Fout, IC20_nq, IR0, IR1, IR2, IR3, IR7, LD_INC, LD_t, MA0, MA1, MA2,
       MA3, MA4, MA5, MA6, MA7, MA8, MA9, MA10, MA11, MA12, MA13, MA14, MA15, nCLRAC, nor_3_out, not_4_out,
       not_5_out, not_6_out, nRD, nWR, OUT0, OUT1, OUT2, OUT3, OUT4, OUT5, OUT6, OUT7, R0, R1, R2, R3, R4,
       R5, R6, R7, R12, R13, R14, RAM_INC, RCO, ResC, SetC_t, T2, T3, T4, T5, T6, T7, T8_t, U2_pin8, U2_pin9,
       U4_pin9, U5_pin9, U16_pin15, ZERO;
  wire [3:0] U1_pin3, U19_pin5, U19_pin9;
  wire [3:1] U1_pin12;

  // A623308A U15: pin names not known; wires that end beside it: MA14, MA12, MA7, MA6, MA5, MA4, MA3, MA2, MA1, MA0, BUS0, BUS1, BUS2, 1'b0, 1'b1, nWR, MA13, MA8, MA9, MA11, 1'b1, MA10, 1'b0, BUS7
  _74161 U16 (
    .pin1(nCLRAC), .pin2(RAM_INC), .pin3(R0), .pin4(R1), .pin5(R2), .pin6(R3), .pin7(1'b1), .pin8(1'b0),
    .pin9(LD_INC), .pin10(1'b1), .pin11(MA3), .pin12(MA2), .pin13(MA1), .pin14(MA0), .pin15(U16_pin15),
    .pin16(1'b1));
  _74161 U17 (
    .pin1(nCLRAC), .pin2(RAM_INC), .pin3(R4), .pin4(R5), .pin5(R6), .pin6(R7), .pin7(1'b1), .pin8(1'b0),
    .pin9(LD_INC), .pin10(U16_pin15), .pin11(MA7), .pin12(MA6), .pin13(MA5), .pin14(MA4), .pin16(1'b1));  // open: pin15
  _74299 U18 (
    .pin1(in_9), .pin2(nWR), .pin3(nWR), .pin4(BUS6), .pin5(BUS4), .pin6(BUS2), .pin7(BUS0), .pin9(nCLRAC),
    .pin10(1'b0), .pin11(1'b0), .pin12(GCLK), .pin13(BUS1), .pin14(BUS3), .pin15(BUS5), .pin16(BUS7),
    .pin18(Fout), .pin19(in_10), .pin20(1'b1));  // open: pin8, pin17
  _74161 U8 (
    .pin1(nCLRAC), .pin2(T8), .pin3(R0), .pin4(R1), .pin5(R2), .pin6(R3), .pin7(1'b1), .pin8(1'b0),
    .pin9(LD_INC), .pin10(1'b1), .pin11(A3), .pin12(A2), .pin13(A1), .pin14(A0), .pin15(RCO), .pin16(1'b1));
  _74161 U9 (
    .pin1(nCLRAC), .pin2(T8), .pin3(R4), .pin4(R5), .pin5(R6), .pin6(R7), .pin7(1'b1), .pin8(1'b0),
    .pin9(LD_INC), .pin10(RCO), .pin11(A7), .pin12(A6), .pin13(A5), .pin14(A4), .pin16(1'b1));  // open: pin15
  _74595 U4 (
    .pin1(BUS6), .pin2(BUS5), .pin3(BUS4), .pin4(BUS3), .pin5(BUS2), .pin6(BUS1), .pin7(BUS0), .pin8(1'b0),
    .pin9(U4_pin9), .pin10(nCLRAC), .pin11(GCLK), .pin12(T8), .pin13(1'b1), .pin14(Fout), .pin15(BUS7),
    .pin16(1'b1));
  // _27C1024 U7: pin names not known; wires that end beside it: A8, A8, A8, A8, A8, A8, A8, 1'b1, R3, R4, R5, R6, R7, 1'b0, IR0, IR1, IR2, IR3, R12, R13, R14, IR7, 1'b0, 1'b1
  PullDown pulldown_1 (.out(A8));
  _74595 U5 (
    .pin1(MA14), .pin2(MA13), .pin3(MA12), .pin4(MA11), .pin5(MA10), .pin6(MA9), .pin7(MA8), .pin8(1'b0),
    .pin9(U5_pin9), .pin10(nCLRAC), .pin11(GCLK), .pin12(T8), .pin13(1'b0), .pin14(U4_pin9), .pin15(MA15),
    .pin16(1'b1));
  LED led_1 (.in(U19_pin5[3]));
  D_FF IC20 (.D(IC20_nq), .C(button_1_out), .Q(U19_pin5[3]), .nQ(IC20_nq));
  LED led_2 (.in(U19_pin5[2]));
  D_FF d_ff_1 (.D(d_ff_1_nq), .C(button_2_out), .Q(U19_pin5[2]), .nQ(d_ff_1_nq));
  Button button_1 (.out(button_1_out));
  _74541 U19 (
    .pin1(SETC), .pin2(U19_pin5[3]), .pin3(U19_pin5[2]), .pin4(U19_pin5[1]), .pin5(U19_pin5[0]),
    .pin6(U19_pin9[3]), .pin7(U19_pin9[2]), .pin8(U19_pin9[1]), .pin9(U19_pin9[0]), .pin10(1'b0),
    .pin11(BUS0), .pin12(BUS1), .pin13(BUS2), .pin14(BUS3), .pin15(BUS4), .pin16(BUS5), .pin17(BUS6),
    .pin18(BUS7), .pin19(SETC), .pin20(1'b1));
  LED led_3 (.in(U19_pin5[1]));
  D_FF d_ff_2 (.D(d_ff_2_nq), .C(button_3_out), .Q(U19_pin5[1]), .nQ(d_ff_2_nq));
  Button button_2 (.out(button_2_out));
  _74541 U13 (
    .pin1(in_1), .pin2(R0), .pin3(R1), .pin4(R2), .pin5(R3), .pin6(R4), .pin7(R5), .pin8(R6), .pin9(R7),
    .pin10(1'b0), .pin11(BUS7), .pin12(BUS6), .pin13(BUS5), .pin14(BUS4), .pin15(BUS3), .pin16(BUS2),
    .pin17(BUS1), .pin18(BUS0), .pin19(in_1), .pin20(1'b1));
  LED led_4 (.in(U19_pin5[0]));
  D_FF d_ff_3 (.D(d_ff_3_nq), .C(button_4_out), .Q(U19_pin5[0]), .nQ(d_ff_3_nq));
  Button button_3 (.out(button_3_out));
  LED led_5 (.in(U19_pin9[3]));
  D_FF d_ff_4 (.D(d_ff_4_nq), .C(button_5_out), .Q(U19_pin9[3]), .nQ(d_ff_4_nq));
  Button button_4 (.out(button_4_out));
  LED led_6 (.in(U19_pin9[2]));
  D_FF d_ff_5 (.D(d_ff_5_nq), .C(button_6_out), .Q(U19_pin9[2]), .nQ(d_ff_5_nq));
  Button button_5 (.out(button_5_out));
  _74595 U6 (
    .pin1(OUT6), .pin2(OUT5), .pin3(OUT4), .pin4(OUT3), .pin5(OUT2), .pin6(OUT1), .pin7(OUT0), .pin8(1'b0),
    .pin10(nCLRAC), .pin11(GCLK), .pin12(T8), .pin13(1'b0), .pin14(Fout), .pin15(OUT7), .pin16(1'b1));  // open: pin9
  DiodeForward diodeforward_1 (.in(BUS7), .out(diodeforward_1_out));
  DiodeForward diodeforward_2 (.in(BUS6), .out(diodeforward_1_out));
  DiodeForward diodeforward_3 (.in(BUS5), .out(diodeforward_1_out));
  DiodeForward diodeforward_4 (.in(BUS4), .out(diodeforward_1_out));
  DiodeForward diodeforward_5 (.in(BUS3), .out(diodeforward_1_out));
  DiodeForward diodeforward_6 (.in(BUS2), .out(diodeforward_1_out));
  DiodeForward diodeforward_7 (.in(BUS1), .out(diodeforward_1_out));
  DiodeForward diodeforward_8 (.in(BUS0), .out(diodeforward_1_out));
  not not_1 (ZERO, diodeforward_1_out);
  PullDown pulldown_2 (.out(diodeforward_1_out));
  LED led_7 (.in(U19_pin9[1]));
  D_FF d_ff_6 (.D(d_ff_6_nq), .C(button_7_out), .Q(U19_pin9[1]), .nQ(d_ff_6_nq));
  Button button_6 (.out(button_6_out));
  LED led_8 (.in(U19_pin9[0]));
  D_FF d_ff_7 (.D(d_ff_7_nq), .C(button_8_out), .Q(U19_pin9[0]), .nQ(d_ff_7_nq));
  Button button_7 (.out(button_7_out));
  GAL1 gal1_1 (
    .CLR(CLR), .nWR(nWR), .nRD(nRD), .INC_LD(LD_INC), .Ain(Aout), .Bin(Bout), .Cin(Cin), .EnC(SETC),
    .LD(LD_t), .IR6(in_11), .IR5(in_12), .IR4(in_13), .T8(T8_t), .VCC(1'b1), .GND(1'b0));  // open: Cout, ResC, SetC, Fout
  Button button_8 (.out(button_8_out));
  _744017 U11 (
    .pin1(T5), .pin2(SETC), .pin3(LD_t), .pin4(T2), .pin5(T6), .pin6(T7), .pin7(T3), .pin8(1'b0),
    .pin9(T8_t), .pin10(T4), .pin11(RAM_INC), .pin13(1'b0), .pin14(clk), .pin15(1'b0), .pin16(1'b1));  // open: pin12
  Seven_Seg_Hex seven_seg_hex_1 (.d(U19_pin5), .dp(1'b0));
  Seven_Seg_Hex seven_seg_hex_2 (.d(U19_pin9), .dp(1'b0));
  Seven_Seg_Hex seven_seg_hex_3 (.d({4{A8}}), .dp(1'b0));
  Seven_Seg_Hex seven_seg_hex_4 (.d({MA15, MA14, MA13, MA12}), .dp(1'b0));
  Seven_Seg_Hex seven_seg_hex_5 (.d({4{A8}}), .dp(1'b0));
  Seven_Seg_Hex seven_seg_hex_6 (.d({MA11, MA10, MA9, MA8}), .dp(1'b0));
  _74165 U3 (
    .pin1(LD), .pin2(GCLK), .pin3(BUS3), .pin4(BUS2), .pin5(BUS1), .pin6(BUS0), .pin8(1'b0), .pin9(Bout),
    .pin10(1'b0), .pin11(BUS7), .pin12(BUS6), .pin13(BUS5), .pin14(BUS4), .pin15(1'b0), .pin16(1'b1));  // open: pin7
  _7474 U2 (
    .pin1(ResC), .pin2(Cout), .pin3(GCLK), .pin4(SetC_t), .pin5(Cin), .pin7(1'b0), .pin8(U2_pin8),
    .pin9(U2_pin9), .pin10(1'b1), .pin11(1'b1), .pin12(1'b1), .pin13(1'b1), .pin14(1'b1));  // open: pin6
  Seven_Seg_Hex seven_seg_hex_7 (.d({A7, A6, A5, A4}), .dp(1'b0));
  Seven_Seg_Hex seven_seg_hex_8 (.d({MA7, MA6, MA5, MA4}), .dp(1'b0));
  // _28c16 _28c16_1: pin names not known; wires that end beside it: Aout, Bout, Cin, LD_t, LD_t, in_11, in_12, in_13, Cout, ResC, SetC_t, 1'b0, 1'b1, 1'b0, 1'b0, 1'b1, 1'b0, 1'b0, 1'b0
  Seven_Seg_Hex seven_seg_hex_9 (.d({A3, A2, A1, A0}), .dp(1'b0));
  Seven_Seg_Hex seven_seg_hex_10 (.d({MA3, MA2, MA1, MA0}), .dp(1'b0));
  Seven_Seg_Hex seven_seg_hex_11 (.d({IR7, in_11, in_12, in_13}), .dp(1'b0));
  Seven_Seg_Hex seven_seg_hex_12 (.d({BUS7, BUS6, BUS5, BUS4}), .dp(1'b0));
  Seven_Seg_Hex seven_seg_hex_13 (.d({IR3, IR2, IR1, IR0}), .dp(1'b0));
  Seven_Seg_Hex seven_seg_hex_14 (.d({BUS3, BUS2, BUS1, BUS0}), .dp(1'b0));
  nor nor_1 (GCLK, GATE, clk);
  nor nor_2 (GATE, SETC, nor_3_out);
  nor nor_3 (nor_3_out, GATE, RAM_INC);
  // NOr nor_4 has open pins: In_1=LD_t, In_2=SETC, out=open
  _74164 U1 (
    .pin1(1'b1), .pin2(Fout), .pin3(U1_pin3[3]), .pin4(U1_pin3[2]), .pin5(U1_pin3[1]), .pin6(U1_pin3[0]),
    .pin7(1'b0), .pin8(GCLK), .pin9(CLR), .pin10(U1_pin12[3]), .pin11(U1_pin12[2]), .pin12(U1_pin12[1]),
    .pin13(Aout), .pin14(1'b1));
  Seven_Seg_Hex seven_seg_hex_15 (.d({BUS7, BUS6, BUS5, BUS4}), .dp(1'b0));
  Seven_Seg_Hex seven_seg_hex_16 (.d(U1_pin3), .dp(1'b0));
  Seven_Seg_Hex seven_seg_hex_17 (.d({BUS3, BUS2, BUS1, BUS0}), .dp(1'b0));
  Seven_Seg_Hex seven_seg_hex_18 (.d({U1_pin12, Aout}), .dp(1'b0));
  not not_2 (LD, LD_t);
  not not_3 (T8, T8_t);
  not not_4 (not_4_out, nWR);
  not not_5 (not_5_out, nRD);
  not not_6 (not_6_out, LD_INC);
  Reset reset_1 (.out(nCLRAC));
  LED led_9 (.in(LD_t));
  LED led_10 (.in(SETC));
  LED led_11 (.in(T2));
  LED led_12 (.in(T3));
  LED led_13 (.in(T4));
  LED led_14 (.in(T5));
  LED led_15 (.in(T6));
  LED led_16 (.in(T7));
  LED led_17 (.in(T8_t));
  LED led_18 (.in(RAM_INC));
  LED led_19 (.in(Cin));
  LED led_20 (.in(ZERO));
  LED led_21 (.in(not_4_out));
  LED led_22 (.in(not_5_out));
  LED nJMP (.in(not_6_out));
  Seven_Seg_Hex seven_seg_hex_19 (.d({OUT7, OUT6, OUT5, OUT4}), .dp(1'b0));
  Seven_Seg_Hex seven_seg_hex_20 (.d({OUT3, OUT2, OUT1, OUT0}), .dp(1'b0));

  assign T0 = LD;

  // Other names for the same wires on the sheet: A9 = A8; A10 = A8; A11 = A8; A12 = A8; A13 = A8; A14 = A8; A15 = A8;
  //   D0 = BUS0; D1 = BUS1; D2 = BUS2; D3 = BUS3; D4 = BUS4; D5 = BUS5; D6 = BUS6; D7 = BUS7; IR4 = in_13;
  //   IR5 = in_12; IR6 = in_11; nDE = in_1; nLOAD = LD; nRESET = nCLRAC; R8 = IR0; R9 = IR1; R10 = IR2; R11 = IR3;
  //   R15 = IR7; PC_INC = T8; RCLK = T8; T0_t = LD_t; EnC = SETC; KB = SETC; T1 = SETC; T9 = RAM_INC

  // Notes on the sheet:
  //   in_1: default 1
  //   clk: Hz: 20
  //   in_9: default 1
  //   in_10: default 1
  //   MITE-19
  //   MITE 8-bit  Bit Serial CPU Testbed
  //   Low RAM Counter
  //   RAM
  //   Low Address Counter
  //   Instruction ROM
  //   Carry is only set before Bit 0 of an operation
  //   Any residual carry is cleared before an operation
  //   Data Input
  //   ROM -> BUS
  //   ALU GAL
  //   Clock Sequencer
  //   ROM ADDRESS
  //   RAM ADDRESS
  //   Carry FF
  //   ALU PROM
  //   INSTRUCTION
  //   DATA BUS
  //   Shift Register A
  //   Shift Register B
  //   U14
  //   74HC02
  //   DATA
  //   ACCUMULATOR
  //   CARRY
  //   ZERO
  //   ~WR
  //   ~RD
endmodule
