// Digital circuit MITE_0_4017_clkgen.dig as structural Verilog
module MITE_0_4017_clkgen (
  input  clk,
  input  in_2,
  input  in_3,
  input  in_4,
  output T0,
  output T8,
  output LD,
  output GCLK,
  output SETC,
  output GATE
);

  wire ADD, AND, Aout, Bout, BUS0, BUS1, BUS2, BUS3, BUS4, BUS5, BUS6, BUS7, button_1_out, button_2_out,
       button_3_out, button_4_out, button_5_out, button_6_out, button_7_out, button_8_out, C, Cin, CLA, CLR,
       Cout, D0, D1, D2, D3, D4, D5, D6, D7, d_ff_1_nq, d_ff_2_nq, d_ff_3_nq, d_ff_4_nq, d_ff_5_nq,
       d_ff_6_nq, diodebackward_1_out, diodebackward_2_out, diodebackward_8_out, diodebackward_9_out,
       diodeforward_1_out, F, Fout, I0, I1, IC16_2_nq, IC16_nq, LOAD, nA, nand_2_out, nand_3_out, nand_5_out,
       nand_6_out, nand_7_out, nand_8_out, nand_9_out, nand_10_out, nand_11_out, nB, nCLRAC, nJMP, nor_3_out,
       OR, pullup_2_out, pullup_4_out, pullup_7_out, ST, SUB, T1, T2, T3, T4, T5, T6, T7, T8_t, T9, U9_pin9,
       XOR, xor_1_out, xor_2_out, xor_3_out, xor_4_out, ZERO;
  wire [3:0] U6_pin6;
  wire [3:1] U6_pin10;

  _74138 U1 (
    .pin1(in_2), .pin2(in_3), .pin3(in_4), .pin4(1'b0), .pin5(1'b0), .pin6(1'b1), .pin7(nJMP), .pin8(1'b0),
    .pin9(ST), .pin10(SUB), .pin11(ADD), .pin12(XOR), .pin13(OR), .pin14(AND), .pin15(LOAD), .pin16(1'b1));
  DiodeBackward diodebackward_1 (.in(LOAD), .out(diodebackward_1_out));
  PullUp pullup_1 (.out(diodebackward_1_out));
  DiodeBackward diodebackward_2 (.in(LOAD), .out(diodebackward_2_out));
  DiodeBackward diodebackward_3 (.in(ADD), .out(diodebackward_2_out));
  DiodeBackward diodebackward_4 (.in(SUB), .out(diodebackward_2_out));
  DiodeBackward diodebackward_5 (.in(nJMP), .out(diodebackward_2_out));
  PullUp pullup_2 (.out(pullup_2_out));
  PullUp pullup_3 (.out(diodebackward_2_out));
  DiodeBackward diodebackward_6 (.in(SUB), .out(pullup_2_out));
  _74165 U4 (
    .pin1(LD), .pin2(GCLK), .pin3(D3), .pin4(D2), .pin5(D1), .pin6(D0), .pin8(1'b0), .pin9(Bout),
    .pin10(1'b0), .pin11(D7), .pin12(D6), .pin13(D5), .pin14(D4), .pin15(1'b0), .pin16(1'b1));  // open: pin7
  PullUp pullup_4 (.out(pullup_4_out));
  DiodeBackward diodebackward_7 (.in(SUB), .out(pullup_4_out));
  DiodeBackward diodebackward_8 (.in(nJMP), .out(diodebackward_8_out));
  PullUp pullup_5 (.out(diodebackward_8_out));
  DiodeBackward diodebackward_9 (.in(AND), .out(diodebackward_9_out));
  DiodeBackward diodebackward_10 (.in(OR), .out(diodebackward_9_out));
  PullUp pullup_6 (.out(diodebackward_9_out));
  PullUp pullup_7 (.out(pullup_7_out));
  DiodeBackward diodebackward_11 (.in(LOAD), .out(pullup_7_out));
  DiodeBackward diodebackward_12 (.in(OR), .out(pullup_7_out));
  DiodeBackward diodebackward_13 (.in(XOR), .out(pullup_7_out));
  DiodeBackward diodebackward_14 (.in(ADD), .out(pullup_7_out));
  DiodeBackward diodebackward_15 (.in(SUB), .out(pullup_7_out));
  DiodeBackward diodebackward_16 (.in(ST), .out(pullup_7_out));
  DiodeBackward diodebackward_17 (.in(nJMP), .out(pullup_7_out));
  _74540 U2 (
    .pin1(1'b0), .pin2(pullup_7_out), .pin3(diodebackward_9_out), .pin4(diodebackward_8_out),
    .pin5(pullup_4_out), .pin6(pullup_2_out), .pin7(diodebackward_2_out), .pin8(diodebackward_1_out),
    .pin9(1'b0), .pin10(1'b0), .pin12(CLA), .pin13(F), .pin14(C), .pin15(nB), .pin16(nA), .pin17(I1),
    .pin18(I0), .pin19(1'b0), .pin20(1'b1));  // open: pin11
  _74595 U9 (
    .pin1(BUS6), .pin2(BUS5), .pin3(BUS4), .pin4(BUS3), .pin5(BUS2), .pin6(BUS1), .pin7(BUS0), .pin8(1'b0),
    .pin9(U9_pin9), .pin10(nCLRAC), .pin11(GCLK), .pin12(T9), .pin13(1'b0), .pin14(Fout), .pin15(BUS7),
    .pin16(1'b1));
  LED led_1 (.in(D7));
  D_FF IC16 (.D(IC16_nq), .C(button_1_out), .Q(D7), .nQ(IC16_nq));
  Button button_1 (.out(button_1_out));
  LED led_2 (.in(D6));
  D_FF d_ff_1 (.D(d_ff_1_nq), .C(button_2_out), .Q(D6), .nQ(d_ff_1_nq));
  Button button_2 (.out(button_2_out));
  LED led_3 (.in(D5));
  D_FF d_ff_2 (.D(d_ff_2_nq), .C(button_3_out), .Q(D5), .nQ(d_ff_2_nq));
  Button button_3 (.out(button_3_out));
  LED led_4 (.in(D4));
  D_FF d_ff_3 (.D(d_ff_3_nq), .C(button_4_out), .Q(D4), .nQ(d_ff_3_nq));
  Button button_4 (.out(button_4_out));
  LED led_5 (.in(D3));
  D_FF d_ff_4 (.D(d_ff_4_nq), .C(button_5_out), .Q(D3), .nQ(d_ff_4_nq));
  Button button_5 (.out(button_5_out));
  DiodeForward diodeforward_1 (.in(BUS7), .out(diodeforward_1_out));
  DiodeForward diodeforward_2 (.in(BUS6), .out(diodeforward_1_out));
  DiodeForward diodeforward_3 (.in(BUS5), .out(diodeforward_1_out));
  DiodeForward diodeforward_4 (.in(BUS4), .out(diodeforward_1_out));
  DiodeForward diodeforward_5 (.in(BUS3), .out(diodeforward_1_out));
  DiodeForward diodeforward_6 (.in(BUS2), .out(diodeforward_1_out));
  DiodeForward diodeforward_7 (.in(BUS1), .out(diodeforward_1_out));
  DiodeForward diodeforward_8 (.in(BUS0), .out(diodeforward_1_out));
  LED led_6 (.in(D2));
  D_FF d_ff_5 (.D(d_ff_5_nq), .C(button_6_out), .Q(D2), .nQ(d_ff_5_nq));
  Button button_6 (.out(button_6_out));
  LED led_7 (.in(D1));
  D_FF d_ff_6 (.D(d_ff_6_nq), .C(button_7_out), .Q(D1), .nQ(d_ff_6_nq));
  Button button_7 (.out(button_7_out));
  Seven_Seg_Hex seven_seg_hex_1 (.d({BUS7, BUS6, BUS5, BUS4}), .dp(1'b0));
  nand nand_1 (ZERO, diodeforward_1_out, diodeforward_1_out);
  PullDown pulldown_1 (.out(diodeforward_1_out));
  LED led_8 (.in(D0));
  D_FF IC16_2 (.D(IC16_2_nq), .C(button_8_out), .Q(D0), .nQ(IC16_2_nq));
  Button button_8 (.out(button_8_out));
  Seven_Seg_Hex seven_seg_hex_2 (.d({BUS3, BUS2, BUS1, BUS0}), .dp(1'b0));
  Seven_Seg_Hex seven_seg_hex_3 (.d({D7, D6, D5, D4}), .dp(1'b0));
  LED led_9 (.in(ZERO));
  Seven_Seg_Hex seven_seg_hex_4 (.d({D3, D2, D1, D0}), .dp(1'b0));
  Seven_Seg_Hex seven_seg_hex_5 (.d(U6_pin6), .dp(1'b0));
  Seven_Seg_Hex seven_seg_hex_6 (.d({U6_pin10, Aout}), .dp(1'b0));
  _74164 U6 (
    .pin1(1'b1), .pin2(Fout), .pin3(U6_pin6[3]), .pin4(U6_pin6[2]), .pin5(U6_pin6[1]), .pin6(U6_pin6[0]),
    .pin7(1'b0), .pin8(GCLK), .pin9(CLR), .pin10(U6_pin10[3]), .pin11(U6_pin10[2]), .pin12(U6_pin10[1]),
    .pin13(Aout), .pin14(1'b1));
  xor xor_1 (xor_1_out, Aout, nA);
  xor xor_2 (xor_2_out, nB, Bout);
  nand nand_2 (nand_2_out, SETC, C);
  nand nand_3 (nand_3_out, C, C);
  nand nand_4 (CLR, CLA, SETC);
  xor xor_3 (xor_3_out, xor_1_out, xor_2_out);
  nand nand_5 (nand_5_out, nand_3_out, SETC);
  _744017 U11 (
    .pin1(T5), .pin2(T1), .pin3(SETC), .pin4(T2), .pin5(T6), .pin6(T7), .pin7(T3), .pin8(1'b0), .pin9(T8_t),
    .pin10(T4), .pin11(T9), .pin13(1'b0), .pin14(clk), .pin15(1'b0), .pin16(1'b1));  // open: pin12
  xor xor_4 (xor_4_out, xor_3_out, Cin);
  nand nand_6 (nand_6_out, xor_3_out, Cin);
  nand nand_7 (nand_7_out, xor_1_out, xor_2_out);
  nand nand_8 (nand_8_out, nand_6_out, nand_7_out);
  not not_1 (LD, SETC);
  not not_2 (T8, T8_t);
  nand nand_9 (nand_9_out, xor_4_out, I0);
  nand nand_10 (nand_10_out, I1, nand_8_out);
  nand nand_11 (nand_11_out, nand_8_out, F);
  Reset reset_1 (.out(nCLRAC));
  nor nor_1 (GCLK, GATE, clk);
  nor nor_2 (GATE, T1, nor_3_out);
  nor nor_3 (nor_3_out, GATE, T9);
  // NOr nor_4 has open pins: In_1=SETC, In_2=T1, out=open
  nand nand_12 (Fout, nand_9_out, nand_10_out);
  nand nand_13 (Cout, nand_11_out, nand_11_out);
  _7474 _7474_1 (
    .pin1(nand_5_out), .pin2(Cout), .pin3(GCLK), .pin4(nand_2_out), .pin5(Cin), .pin7(1'b0), .pin10(1'b1),
    .pin11(1'b1), .pin12(1'b1), .pin13(1'b1), .pin14(1'b1));  // open: pin6, pin8, pin9
  LED led_10 (.in(SETC));
  LED led_11 (.in(T1));
  LED led_12 (.in(T2));
  LED led_13 (.in(T3));
  LED led_14 (.in(T4));
  LED led_15 (.in(T5));
  LED led_16 (.in(T6));
  LED led_17 (.in(T7));
  LED led_18 (.in(T8_t));
  LED led_19 (.in(T9));
  LED led_20 (.in(Cin));

  assign T0 = LD;

  // Other names for the same wires on the sheet: nLOAD = LD; nRESET = nCLRAC; RCLK = T8; EnC = SETC; LD_t = SETC;
  //   T0_t = SETC

  // Notes on the sheet:
  //   clk: Hz: 100
  //   MITE
  //   Instruction Input
  //   MITE 8-bit  Bit serial CPU Testbed
  //   8-bit Shift Register B
  //   Instruction Decode
  //   CLA
  //   C
  //   F
  //   ~B
  //   ~A
  //   I0
  //   I1
  //   LOAD
  //   AND
  //   OR
  //   XOR
  //   ADD
  //   SUB
  //   STORE
  //   JMP
  //   Output Display Register
  //   ENTER L
  //   Data Input
  //   OUTPUT REGISTER
  //   ZERO
  //   16 bit Shift Register A
  //   ACCUMULATOR
  //   ALU
  //   CLR ACC
  //   Clock Sequencer
  //   Any residual carry is cleared before an operation
  //   Carry is only set before Bit 0 of an operation
  //   U14
  //   74HC02
  //   Suppress Carry
  //   Carry FF
  //   CARRY
endmodule
