// Digital circuit MITE_0_ALU_PROM.dig as structural Verilog
module MITE_0_ALU_PROM (
  input  clk,
  input  in_8,
  input  in_9,
  input  in_10,
  output T0,
  output T8,
  output LD,
  output GCLK,
  output SETC,
  output GATE
);

  wire Aout, Bout, BUS0, BUS1, BUS2, BUS3, BUS4, BUS5, BUS6, BUS7, button_1_out, button_2_out, button_3_out,
       button_4_out, button_5_out, button_6_out, button_7_out, button_8_out, Cin, CLR, Cout, D0, D1, D2, D3,
       D4, D5, D6, D7, d_ff_1_nq, d_ff_2_nq, d_ff_3_nq, d_ff_4_nq, d_ff_5_nq, d_ff_6_nq, diodeforward_1_out,
       Fout, IC16_2_nq, IC16_nq, nCLRAC, nor_4_out, ResC, SetC_t, T1, T2, T3, T4, T5, T6, T7, T8_t, T9, ZERO;
  wire [3:0] U6_pin6;
  wire [3:1] U6_pin10;

  _74165 U4 (
    .pin1(LD), .pin2(GCLK), .pin3(D3), .pin4(D2), .pin5(D1), .pin6(D0), .pin8(1'b0), .pin9(Bout),
    .pin10(1'b0), .pin11(D7), .pin12(D6), .pin13(D5), .pin14(D4), .pin15(1'b0), .pin16(1'b1));  // open: pin7
  _74595 U9 (
    .pin1(BUS6), .pin2(BUS5), .pin3(BUS4), .pin4(BUS3), .pin5(BUS2), .pin6(BUS1), .pin7(BUS0), .pin8(1'b0),
    .pin10(nCLRAC), .pin11(GCLK), .pin12(T9), .pin13(1'b0), .pin14(Fout), .pin15(BUS7), .pin16(1'b1));  // open: pin9
  LED led_1 (.in(D7));
  D_FF IC16 (.D(IC16_nq), .C(button_1_out), .Q(D7), .nQ(IC16_nq));
  Button button_1 (.out(button_1_out));
  LED led_2 (.in(D6));
  D_FF d_ff_1 (.D(d_ff_1_nq), .C(button_2_out), .Q(D6), .nQ(d_ff_1_nq));
  Button button_2 (.out(button_2_out));
  LED led_3 (.in(D5));
  D_FF d_ff_2 (.D(d_ff_2_nq), .C(button_3_out), .Q(D5), .nQ(d_ff_2_nq));
  Button button_3 (.out(button_3_out));
  LED led_4 (.in(D4));
  D_FF d_ff_3 (.D(d_ff_3_nq), .C(button_4_out), .Q(D4), .nQ(d_ff_3_nq));
  Button button_4 (.out(button_4_out));
  LED led_5 (.in(D3));
  D_FF d_ff_4 (.D(d_ff_4_nq), .C(button_5_out), .Q(D3), .nQ(d_ff_4_nq));
  Button button_5 (.out(button_5_out));
  Seven_Seg_Hex seven_seg_hex_1 (.d({BUS7, BUS6, BUS5, BUS4}), .dp(1'b0));
  DiodeForward diodeforward_1 (.in(BUS7), .out(diodeforward_1_out));
  DiodeForward diodeforward_2 (.in(BUS6), .out(diodeforward_1_out));
  DiodeForward diodeforward_3 (.in(BUS5), .out(diodeforward_1_out));
  DiodeForward diodeforward_4 (.in(BUS4), .out(diodeforward_1_out));
  DiodeForward diodeforward_5 (.in(BUS3), .out(diodeforward_1_out));
  DiodeForward diodeforward_6 (.in(BUS2), .out(diodeforward_1_out));
  DiodeForward diodeforward_7 (.in(BUS1), .out(diodeforward_1_out));
  DiodeForward diodeforward_8 (.in(BUS0), .out(diodeforward_1_out));
  LED led_6 (.in(D2));
  D_FF d_ff_5 (.D(d_ff_5_nq), .C(button_6_out), .Q(D2), .nQ(d_ff_5_nq));
  Button button_6 (.out(button_6_out));
  Seven_Seg_Hex seven_seg_hex_2 (.d({BUS3, BUS2, BUS1, BUS0}), .dp(1'b0));
  LED led_7 (.in(D1));
  D_FF d_ff_6 (.D(d_ff_6_nq), .C(button_7_out), .Q(D1), .nQ(d_ff_6_nq));
  Button button_7 (.out(button_7_out));
  nor nor_1 (ZERO, diodeforward_1_out, diodeforward_1_out);
  PullDown pulldown_1 (.out(diodeforward_1_out));
  LED led_8 (.in(D0));
  D_FF IC16_2 (.D(IC16_2_nq), .C(button_8_out), .Q(D0), .nQ(IC16_2_nq));
  Button button_8 (.out(button_8_out));
  Seven_Seg_Hex seven_seg_hex_3 (.d({D7, D6, D5, D4}), .dp(1'b0));
  LED led_9 (.in(ZERO));
  Seven_Seg_Hex seven_seg_hex_4 (.d({D3, D2, D1, D0}), .dp(1'b0));
  Seven_Seg_Hex seven_seg_hex_5 (.d(U6_pin6), .dp(1'b0));
  Seven_Seg_Hex seven_seg_hex_6 (.d({U6_pin10, Aout}), .dp(1'b0));
  _74164 U6 (
    .pin1(1'b1), .pin2(Fout), .pin3(U6_pin6[3]), .pin4(U6_pin6[2]), .pin5(U6_pin6[1]), .pin6(U6_pin6[0]),
    .pin7(1'b0), .pin8(GCLK), .pin9(CLR), .pin10(U6_pin10[3]), .pin11(U6_pin10[2]), .pin12(U6_pin10[1]),
    .pin13(Aout), .pin14(1'b1));
  // _28c16 _28c16_1: pin names not known; wires that end beside it: Aout, Bout, Cin, SETC, SETC, in_8, in_9, in_10, Cout, ResC, SetC_t, 1'b0, 1'b1, 1'b0, 1'b0, 1'b1, 1'b0, 1'b0, 1'b0
  _744017 U11 (
    .pin1(T5), .pin2(T1), .pin3(SETC), .pin4(T2), .pin5(T6), .pin6(T7), .pin7(T3), .pin8(1'b0), .pin9(T8_t),
    .pin10(T4), .pin11(T9), .pin13(1'b0), .pin14(clk), .pin15(1'b0), .pin16(1'b1));  // open: pin12
  not not_1 (LD, SETC);
  not not_2 (T8, T8_t);
  Reset reset_1 (.out(nCLRAC));
  nor nor_2 (GCLK, GATE, clk);
  nor nor_3 (GATE, T1, nor_4_out);
  nor nor_4 (nor_4_out, GATE, T9);
  _7474 _7474_1 (
    .pin1(ResC), .pin2(Cout), .pin3(GCLK), .pin4(SetC_t), .pin5(Cin), .pin7(1'b0), .pin10(1'b1),
    .pin11(1'b1), .pin12(1'b1), .pin13(1'b1), .pin14(1'b1));  // open: pin6, pin8, pin9
  LED led_10 (.in(SETC));
  LED led_11 (.in(T1));
  LED led_12 (.in(T2));
  LED led_13 (.in(T3));
  LED led_14 (.in(T4));
  LED led_15 (.in(T5));
  LED led_16 (.in(T6));
  LED led_17 (.in(T7));
  LED led_18 (.in(T8_t));
  LED led_19 (.in(T9));
  LED led_20 (.in(Cin));

  assign T0 = LD;

  // Other names for the same wires on the sheet: IR4 = in_10; IR5 = in_9; IR6 = in_8; nLOAD = LD; nRESET = nCLRAC;
  //   RCLK = T8; EnC = SETC; LD_t = SETC; T0_t = SETC

  // Notes on the sheet:
  //   clk: Hz: 10
  //   MITE
  //   MITE 8-bit  Bit serial CPU Testbed
  //   8-bit Shift Register B
  //   Output Display Register
  //   ENTER L
  //   Data Input
  //   OUTPUT REGISTER
  //   ZERO
  //   16 bit Shift Register A
  //   ACCUMULATOR
  //   ALU
  //   ALU PROM
  //   Clock Sequencer
  //   U14
  //   74HC02
  //   Carry FF
  //   CARRY
endmodule
