// Digital circuit MITE_module_1.dig as structural Verilog
module MITE_module_1 (
  input  clk,
  input  in_6,
  input  in_7,
  input  in_8,
  input  in_9,
  output LD,
  output GCLK,
  output SETC,
  output GATE
);

  wire BUS0, BUS1, BUS2, BUS3, BUS4, BUS5, BUS6, BUS7, button_1_out, button_2_out, button_3_out,
       button_4_out, button_5_out, button_6_out, button_7_out, button_8_out, Cin, D0, D1, D2, D3, D4, D5, D6,
       D7, d_ff_1_nq, d_ff_2_nq, d_ff_3_nq, d_ff_4_nq, d_ff_5_nq, d_ff_6_nq, IC16_2_nq, IC16_nq, nCLRAC, T1,
       T8, T9, ZERO;

  Mod_ALU mod_alu_1 (
    .T0(SETC), .T8(T8), .GCLK(GCLK), .GATE(GATE), .I2(in_6), .I1(in_7), .I0(in_8), .D7(D7), .D6(D6), .D5(D5),
    .D4(D4), .D3(D3), .D2(D2), .D1(D1), .D0(D0), .nOE(in_9), .nRES(nCLRAC), .CLK(clk), .T1(T1), .T9(T9),
    .C(Cin), .Z(ZERO), .DB0(BUS0), .DB1(BUS1), .DB2(BUS2), .DB3(BUS3), .DB4(BUS4), .DB5(BUS5), .DB6(BUS6),
    .DB7(BUS7), .VCC(1'b1), .GND(1'b0));
  LED led_1 (.in(D7));
  D_FF IC16 (.D(IC16_nq), .C(button_1_out), .Q(D7), .nQ(IC16_nq));
  Button button_1 (.out(button_1_out));
  LED led_2 (.in(D6));
  D_FF d_ff_1 (.D(d_ff_1_nq), .C(button_2_out), .Q(D6), .nQ(d_ff_1_nq));
  Button button_2 (.out(button_2_out));
  LED led_3 (.in(D5));
  D_FF d_ff_2 (.D(d_ff_2_nq), .C(button_3_out), .Q(D5), .nQ(d_ff_2_nq));
  Button button_3 (.out(button_3_out));
  LED led_4 (.in(D4));
  D_FF d_ff_3 (.D(d_ff_3_nq), .C(button_4_out), .Q(D4), .nQ(d_ff_3_nq));
  Button button_4 (.out(button_4_out));
  LED led_5 (.in(D3));
  D_FF d_ff_4 (.D(d_ff_4_nq), .C(button_5_out), .Q(D3), .nQ(d_ff_4_nq));
  Button button_5 (.out(button_5_out));
  LED led_6 (.in(D2));
  D_FF d_ff_5 (.D(d_ff_5_nq), .C(button_6_out), .Q(D2), .nQ(d_ff_5_nq));
  Button button_6 (.out(button_6_out));
  LED led_7 (.in(D1));
  D_FF d_ff_6 (.D(d_ff_6_nq), .C(button_7_out), .Q(D1), .nQ(d_ff_6_nq));
  Button button_7 (.out(button_7_out));
  LED led_8 (.in(D0));
  D_FF IC16_2 (.D(IC16_2_nq), .C(button_8_out), .Q(D0), .nQ(IC16_2_nq));
  Button button_8 (.out(button_8_out));
  Seven_Seg_Hex seven_seg_hex_1 (.d({BUS7, BUS6, BUS5, BUS4}), .dp(1'b0));
  Seven_Seg_Hex seven_seg_hex_2 (.d({D7, D6, D5, D4}), .dp(1'b0));
  Seven_Seg_Hex seven_seg_hex_3 (.d({BUS3, BUS2, BUS1, BUS0}), .dp(1'b0));
  Seven_Seg_Hex seven_seg_hex_4 (.d({D3, D2, D1, D0}), .dp(1'b0));
  not not_1 (LD, SETC);
  Reset reset_1 (.out(nCLRAC));
  LED led_9 (.in(SETC));
  LED led_10 (.in(T1));
  LED led_11 (.in(T8));
  LED led_12 (.in(T9));
  LED led_13 (.in(ZERO));
  LED led_14 (.in(Cin));

  // Other names for the same wires on the sheet: IR4 = in_8; IR5 = in_7; IR6 = in_6; nLOAD = LD; nRESET = nCLRAC;
  //   EnC = SETC; LD_t = SETC; T0 = SETC

  // Notes on the sheet:
  //   clk: Hz: 10
  //   MITE
  //   MITE 8-bit  Bit serial CPU Testbed
  //   ENTER L
  //   Data Input
  //   OUTPUT REGISTER
  //   INPUT REGISTER
  //   CARRY
  //   ZERO
endmodule
