// Digital circuit MITE_module_2.dig as structural Verilog
module MITE_module_2 (
  input  clk,
  input  in_4,
  input  in_5,
  input  in_6,
  input  nOE,
  output nLOAD,
  output GCLK,
  output T0,
  output T1,
  output T8,
  output T9
);

  wire BUS0, BUS1, BUS2, BUS3, BUS4, BUS5, BUS6, BUS7, button_1_out, button_2_out, button_3_out,
       button_4_out, button_5_out, button_6_out, button_7_out, button_8_out, Cin, D0, D1, D2, D3, D4, D5, D6,
       D7, d_ff_1_nq, d_ff_2_nq, d_ff_3_nq, d_ff_4_nq, d_ff_5_nq, d_ff_6_nq, Fout, IC16_2_nq, IC16_nq,
       nRESET, OUT0, OUT1, OUT2, OUT3, OUT4, OUT5, OUT6, OUT7, ZERO;

  Mod_ALU mod_alu_1 (
    .T0(T0), .T8(T8), .GCLK(GCLK), .GATE(Fout), .I2(in_4), .I1(in_5), .I0(in_6), .D7(D7), .D6(D6), .D5(D5),
    .D4(D4), .D3(D3), .D2(D2), .D1(D1), .D0(D0), .nOE(nOE), .nRES(nRESET), .CLK(clk), .T1(T1), .T9(T9),
    .C(Cin), .Z(ZERO), .DB0(BUS0), .DB1(BUS1), .DB2(BUS2), .DB3(BUS3), .DB4(BUS4), .DB5(BUS5), .DB6(BUS6),
    .DB7(BUS7), .VCC(1'b1), .GND(1'b0));
  LED led_1 (.in(D7));
  D_FF IC16 (.D(IC16_nq), .C(button_1_out), .Q(D7), .nQ(IC16_nq));
  Button button_1 (.out(button_1_out));
  _74595 U6 (
    .pin1(OUT6), .pin2(OUT5), .pin3(OUT4), .pin4(OUT3), .pin5(OUT2), .pin6(OUT1), .pin7(OUT0), .pin8(1'b0),
    .pin10(nRESET), .pin11(GCLK), .pin12(T8), .pin13(1'b0), .pin14(Fout), .pin15(OUT7), .pin16(1'b1));  // open: pin9
  LED led_2 (.in(D6));
  D_FF d_ff_1 (.D(d_ff_1_nq), .C(button_2_out), .Q(D6), .nQ(d_ff_1_nq));
  Button button_2 (.out(button_2_out));
  LED led_3 (.in(D5));
  D_FF d_ff_2 (.D(d_ff_2_nq), .C(button_3_out), .Q(D5), .nQ(d_ff_2_nq));
  Button button_3 (.out(button_3_out));
  LED led_4 (.in(D4));
  D_FF d_ff_3 (.D(d_ff_3_nq), .C(button_4_out), .Q(D4), .nQ(d_ff_3_nq));
  Button button_4 (.out(button_4_out));
  LED led_5 (.in(D3));
  D_FF d_ff_4 (.D(d_ff_4_nq), .C(button_5_out), .Q(D3), .nQ(d_ff_4_nq));
  Button button_5 (.out(button_5_out));
  LED led_6 (.in(D2));
  D_FF d_ff_5 (.D(d_ff_5_nq), .C(button_6_out), .Q(D2), .nQ(d_ff_5_nq));
  Button button_6 (.out(button_6_out));
  LED led_7 (.in(D1));
  D_FF d_ff_6 (.D(d_ff_6_nq), .C(button_7_out), .Q(D1), .nQ(d_ff_6_nq));
  Button button_7 (.out(button_7_out));
  LED led_8 (.in(D0));
  D_FF IC16_2 (.D(IC16_2_nq), .C(button_8_out), .Q(D0), .nQ(IC16_2_nq));
  Button button_8 (.out(button_8_out));
  Seven_Seg_Hex seven_seg_hex_1 (.d({BUS7, BUS6, BUS5, BUS4}), .dp(1'b0));
  Seven_Seg_Hex seven_seg_hex_2 (.d({D7, D6, D5, D4}), .dp(1'b0));
  Seven_Seg_Hex seven_seg_hex_3 (.d({BUS3, BUS2, BUS1, BUS0}), .dp(1'b0));
  Seven_Seg_Hex seven_seg_hex_4 (.d({D3, D2, D1, D0}), .dp(1'b0));
  Seven_Seg_Hex seven_seg_hex_5 (.d({OUT7, OUT6, OUT5, OUT4}), .dp(1'b0));
  Seven_Seg_Hex seven_seg_hex_6 (.d({OUT3, OUT2, OUT1, OUT0}), .dp(1'b0));
  LED u_T0 (.in(T0));
  LED u_T1 (.in(T1));
  LED u_T8 (.in(T8));
  LED u_T9 (.in(T9));
  LED led_9 (.in(ZERO));
  LED led_10 (.in(Cin));
  Reset reset_1 (.out(nRESET));
  not not_1 (nLOAD, T0);

  // Other names for the same wires on the sheet: IR4 = in_6; IR5 = in_5; IR6 = in_4; RCLK = T8

  // Notes on the sheet:
  //   clk: Hz: 20
  //   MITE
  //   MITE 8-bit  Bit serial CPU Testbed
  //   Bit Serial ALU and Timing
  //   Output Register
  //   Data Input
  //   ACCUMULATOR
  //   INPUT REGISTER
  //   Instruction Input
  //   000 LOAD
  //   001 AND
  //   010  OR
  //   011  XOR
  //   100  ADD
  //   101  SUB
  //   110  STORE
  //   111  JUMP
  //   OUTPUT REGISTER
  //   CARRY
  //   ZERO
endmodule
