// Digital circuit Mod_ALU_3.dig as structural Verilog
module Mod_ALU_3 (
  input  I2,
  input  I1,
  input  I0,
  input  D7,
  input  D6,
  input  D5,
  input  D4,
  input  D3,
  input  D2,
  input  D1,
  input  D0,
  input  nOE,
  input  nRES,
  input  CLK,
  input  VCC,
  input  GND,
  output T0,
  output T8,
  output GCLK,
  output Fout,
  output T1,
  output T9,
  output C,
  output Z,
  output DB0,
  output DB1,
  output DB2,
  output DB3,
  output DB4,
  output DB5,
  output DB6,
  output DB7
);

  wire Aout, Bout, Cout, diodeforward_1_out, diodeforward_9_out, GATE, LD, nCLR, ResC, SetC, T1_t, T8_t, T9_t;

  _74595 U3 (
    .pin1(DB6), .pin2(DB5), .pin3(DB4), .pin4(DB3), .pin5(DB2), .pin6(DB1), .pin7(DB0), .pin8(1'b0),
    .pin9(Aout), .pin10(nCLR), .pin11(GCLK), .pin12(T9_t), .pin13(nOE), .pin14(Fout), .pin15(DB7),
    .pin16(1'b1));
  PowerSupply powersupply_1 (.VDD(VCC), .GND(GND));
  DiodeForward diodeforward_1 (.in(DB7), .out(diodeforward_1_out));
  DiodeForward diodeforward_2 (.in(DB6), .out(diodeforward_1_out));
  DiodeForward diodeforward_3 (.in(DB5), .out(diodeforward_1_out));
  DiodeForward diodeforward_4 (.in(DB4), .out(diodeforward_1_out));
  DiodeForward diodeforward_5 (.in(DB3), .out(diodeforward_1_out));
  DiodeForward diodeforward_6 (.in(DB2), .out(diodeforward_1_out));
  DiodeForward diodeforward_7 (.in(DB1), .out(diodeforward_1_out));
  DiodeForward diodeforward_8 (.in(DB0), .out(diodeforward_1_out));
  not not_1 (T0, LD);
  not not_2 (T1, T1_t);
  not not_3 (T8, T8_t);
  not not_4 (T9, T9_t);
  PullDown pulldown_1 (.out(diodeforward_1_out));
  not not_5 (Z, diodeforward_1_out);
  _74165 U4 (
    .pin1(T0), .pin2(GCLK), .pin3(D3), .pin4(D2), .pin5(D1), .pin6(D0), .pin8(1'b0), .pin9(Bout),
    .pin10(1'b0), .pin11(D7), .pin12(D6), .pin13(D5), .pin14(D4), .pin15(1'b0), .pin16(1'b1));  // open: pin7
  // _28c16 U1: pin names not known; wires that end beside it: Aout, Bout, C, LD, LD, I2, I1, I0, Cout, ResC, SetC, 1'b0, 1'b1, 1'b0, 1'b0, 1'b1, 1'b0, 1'b0, 1'b0
  _744017 U5 (
    .pin2(T1_t), .pin3(LD), .pin8(1'b0), .pin9(T8_t), .pin11(T9_t), .pin13(1'b0), .pin14(CLK), .pin15(1'b0),
    .pin16(1'b1));  // open: pin1, pin4, pin5, pin6, pin7, pin10, pin12
  _7474 U2 (
    .pin1(ResC), .pin2(Cout), .pin3(GCLK), .pin4(SetC), .pin5(C), .pin7(1'b0), .pin9(GATE), .pin10(T9),
    .pin11(1'b1), .pin12(1'b1), .pin13(T1), .pin14(1'b1));  // open: pin6, pin8
  DiodeForward diodeforward_9 (.in(GATE), .out(diodeforward_9_out));
  DiodeForward diodeforward_10 (.in(CLK), .out(diodeforward_9_out));
  PullDown pulldown_2 (.out(diodeforward_9_out));
  not not_6 (GCLK, diodeforward_9_out);

  // Other names for the same wires on the sheet: BUS0 = DB0; BUS1 = DB1; BUS2 = DB2; BUS3 = DB3; BUS4 = DB4;
  //   BUS5 = DB5; BUS6 = DB6; BUS7 = DB7; Cin = C; IR4 = I0; IR5 = I1; IR6 = I2; nLOAD = T0; nRESET = nRES; nT1 = T1;
  //   nT9 = T9; RCLK = T8; T0_t = LD; ZERO = Z

  // Notes on the sheet:
  //   T0: pin 25
  //   T8: pin 27
  //   GCLK: pin 15
  //   Fout: pin 29
  //   I2: pin 3
  //   I1: pin 2
  //   I0: pin 1
  //   D7: pin 4
  //   D6: pin 5
  //   D5: pin 6
  //   D4: pin 7
  //   D3: pin 8
  //   D2: pin 9
  //   D1: pin 10
  //   D0: pin 11
  //   nOE: pin 12
  //   nRES: pin 13
  //   CLK: pin 14
  //   T1: pin 26
  //   T9: pin 28
  //   C: pin 30
  //   Z: pin 31
  //   DB0: pin 17
  //   DB1: pin 18
  //   DB2: pin 19
  //   DB3: pin 20
  //   DB4: pin 21
  //   DB5: pin 22
  //   DB6: pin 23
  //   DB7: pin 24
  //   VCC: pin 32, default 1
  //   GND: pin 16
  //   Accumulator A
  //   ZERO
  //   8-bit Shift Register B
  //   ALU
  //   ALU PROM
  //   Clock Sequencer
  //   Carry FF
endmodule
